// Digital circuit 16_bit_IR.dig as structural Verilog
module _16_bit_IR (
  input  D_0,
  input  D_1,
  input  D_2,
  input  D_3,
  input  D_4,
  input  D_5,
  input  D_6,
  input  D_7,
  input  D_8,
  input  D_9,
  input  D_10,
  input  D_11,
  input  D_12,
  input  D_13,
  input  D_14,
  input  D_15,
  output Q_7,
  output Q_6,
  output Q_5,
  output Q_4,
  output Q_3,
  output Q_0,
  output Q_1,
  output Q_2,
  output Q_15,
  output Q_14,
  output Q_13,
  output Q_12,
  output Q_11,
  output Q_8,
  output Q_9,
  output Q_10
);

  // _28c64 _28c64_1: pin names not known; wires that end beside it: D_8, D_9, D_10, D_11, D_12, D_13, D_14, D_15, Q_8, Q_9, Q_15
  // _28c64 _28c64_2: pin names not known; wires that end beside it: Q_10, D_0, D_1, D_2, D_3, D_4, D_5, D_6, D_7, Q_0, Q_1, Q_2, Q_7
endmodule
