// Digital circuit 16bit_mux_2to1.dig as structural Verilog
module _16bit_mux_2to1 (
  input  I0_0,
  input  I0_1,
  input  I0_2,
  input  I0_3,
  input  I0_4,
  input  I0_5,
  input  I0_6,
  input  I0_7,
  input  I0_8,
  input  I0_9,
  input  I0_10,
  input  I0_11,
  input  I0_12,
  input  I0_13,
  input  I0_14,
  input  I0_15,
  input  I1_0,
  input  I1_1,
  input  I1_2,
  input  I1_3,
  input  I1_4,
  input  I1_5,
  input  I1_6,
  input  I1_7,
  input  I1_8,
  input  I1_9,
  input  I1_10,
  input  I1_11,
  input  I1_12,
  input  I1_13,
  input  I1_14,
  input  I1_15,
  input  Select,
  output Output_0,
  output Output_1,
  output Output_2,
  output Output_3,
  output Output_4,
  output Output_5,
  output Output_6,
  output Output_7,
  output Output_8,
  output Output_9,
  output Output_10,
  output Output_11,
  output Output_12,
  output Output_13,
  output Output_14,
  output Output_15
);

  Multiplexer multiplexer_1 (.sel(Select), .in_0(I0_0), .in_1(I1_0), .out(Output_0));
  Multiplexer multiplexer_2 (.sel(Select), .in_0(I0_1), .in_1(I1_1), .out(Output_1));
  Multiplexer multiplexer_3 (.sel(Select), .in_0(I0_2), .in_1(I1_2), .out(Output_2));
  Multiplexer multiplexer_4 (.sel(Select), .in_0(I0_3), .in_1(I1_3), .out(Output_3));
  Multiplexer multiplexer_5 (.sel(Select), .in_0(I0_4), .in_1(I1_4), .out(Output_4));
  Multiplexer multiplexer_6 (.sel(Select), .in_0(I0_5), .in_1(I1_5), .out(Output_5));
  Multiplexer multiplexer_7 (.sel(Select), .in_0(I0_6), .in_1(I1_6), .out(Output_6));
  Multiplexer multiplexer_8 (.sel(Select), .in_0(I0_7), .in_1(I1_7), .out(Output_7));
  Multiplexer multiplexer_9 (.sel(Select), .in_0(I0_8), .in_1(I1_8), .out(Output_8));
  Multiplexer multiplexer_10 (.sel(Select), .in_0(I0_9), .in_1(I1_9), .out(Output_9));
  Multiplexer multiplexer_11 (.sel(Select), .in_0(I0_10), .in_1(I1_10), .out(Output_10));
  Multiplexer multiplexer_12 (.sel(Select), .in_0(I0_11), .in_1(I1_11), .out(Output_11));
  Multiplexer multiplexer_13 (.sel(Select), .in_0(I0_12), .in_1(I1_12), .out(Output_12));
  Multiplexer multiplexer_14 (.sel(Select), .in_0(I0_13), .in_1(I1_13), .out(Output_13));
  Multiplexer multiplexer_15 (.sel(Select), .in_0(I0_14), .in_1(I1_14), .out(Output_14));
  Multiplexer multiplexer_16 (.sel(Select), .in_0(I0_15), .in_1(I1_15), .out(Output_15));
endmodule
