// Digital circuit 16bit_register.dig as structural Verilog
module _16bit_register (
  input  D_0,
  input  D_1,
  input  D_2,
  input  D_3,
  input  D_4,
  input  D_5,
  input  D_6,
  input  D_7,
  input  D_8,
  input  D_9,
  input  D_10,
  input  D_11,
  input  D_12,
  input  D_13,
  input  D_14,
  input  D_15,
  input  Reset,
  input  Clock,
  output Q_0,
  output Q_1,
  output Q_2,
  output Q_3,
  output Q_4,
  output Q_5,
  output Q_6,
  output Q_7,
  output Q_8,
  output Q_9,
  output Q_10,
  output Q_11,
  output Q_12,
  output Q_13,
  output Q_14,
  output Q_15
);

  _8bit_register _8bit_register_1 (
    .D_0(D_0), .Clock(Clock), .Reset(Reset), .D_1(D_1), .D_2(D_2), .D_3(D_3), .D_4(D_4), .D_5(D_5),
    .D_6(D_6), .D_7(D_7), .Q_0(Q_0), .Q_1(Q_1), .Q_2(Q_2), .Q_3(Q_3), .Q_4(Q_4), .Q_5(Q_5), .Q_6(Q_6),
    .Q_7(Q_7));
  _8bit_register _8bit_register_2 (
    .D_0(D_8), .Clock(Clock), .Reset(Reset), .D_1(D_9), .D_2(D_10), .D_3(D_11), .D_4(D_12), .D_5(D_13),
    .D_6(D_14), .D_7(D_15), .Q_0(Q_8), .Q_1(Q_9), .Q_2(Q_10), .Q_3(Q_11), .Q_4(Q_12), .Q_5(Q_13), .Q_6(Q_14),
    .Q_7(Q_15));
endmodule
