// Digital circuit 8Registers_encoded.dig as structural Verilog
module _8Registers_encoded (
  input  [2:0] Select_input_0,
  input  [2:0] Select_input_1,
  input  [2:0] Select_input_2,
  input  [2:0] Select_output_0,
  input  [2:0] Select_output_1,
  input  [2:0] Select_output_2,
  input  Input_0,
  input  Input_1,
  input  Input_2,
  input  Input_3,
  input  Input_4,
  input  Input_5,
  input  Input_6,
  input  Input_7,
  input  Input_8,
  input  Input_9,
  input  Input_10,
  input  Input_11,
  input  Input_12,
  input  Input_13,
  input  Input_14,
  input  Input_15,
  input  Clock,
  input  Reset,
  output Output_0,
  output Output_1,
  output Output_2,
  output Output_3,
  output Output_4,
  output Output_5,
  output Output_6,
  output Output_7,
  output Output_8,
  output Output_9,
  output Output_10,
  output Output_11,
  output Output_12,
  output Output_13,
  output Output_14,
  output Output_15
);

  wire demultiplexer_1_out_0, demultiplexer_1_out_1, demultiplexer_1_out_2, demultiplexer_1_out_3,
       demultiplexer_1_out_4, demultiplexer_1_out_5, demultiplexer_1_out_6, demultiplexer_1_out_7,
       demultiplexer_2_out_0, demultiplexer_2_out_1, demultiplexer_2_out_2, demultiplexer_2_out_3,
       demultiplexer_2_out_4, demultiplexer_2_out_5, demultiplexer_2_out_6, demultiplexer_2_out_7,
       demultiplexer_3_out_0, demultiplexer_3_out_1, demultiplexer_3_out_2, demultiplexer_3_out_3,
       demultiplexer_3_out_4, demultiplexer_3_out_5, demultiplexer_3_out_6, demultiplexer_3_out_7,
       demultiplexer_4_out_0, demultiplexer_4_out_1, demultiplexer_4_out_2, demultiplexer_4_out_3,
       demultiplexer_4_out_4, demultiplexer_4_out_5, demultiplexer_4_out_6, demultiplexer_4_out_7,
       demultiplexer_5_out_0, demultiplexer_5_out_1, demultiplexer_5_out_2, demultiplexer_5_out_3,
       demultiplexer_5_out_4, demultiplexer_5_out_5, demultiplexer_5_out_6, demultiplexer_5_out_7,
       demultiplexer_6_out_0, demultiplexer_6_out_1, demultiplexer_6_out_2, demultiplexer_6_out_3,
       demultiplexer_6_out_4, demultiplexer_6_out_5, demultiplexer_6_out_6, demultiplexer_6_out_7,
       demultiplexer_7_out_0, demultiplexer_7_out_1, demultiplexer_7_out_2, demultiplexer_7_out_3,
       demultiplexer_7_out_4, demultiplexer_7_out_5, demultiplexer_7_out_6, demultiplexer_7_out_7,
       demultiplexer_8_out_0, demultiplexer_8_out_1, demultiplexer_8_out_2, demultiplexer_8_out_3,
       demultiplexer_8_out_4, demultiplexer_8_out_5, demultiplexer_8_out_6, demultiplexer_8_out_7,
       demultiplexer_9_out_0, demultiplexer_9_out_1, demultiplexer_9_out_2, demultiplexer_9_out_3,
       demultiplexer_9_out_4, demultiplexer_9_out_5, demultiplexer_9_out_6, demultiplexer_9_out_7,
       demultiplexer_10_out_0, demultiplexer_10_out_1, demultiplexer_10_out_2, demultiplexer_10_out_3,
       demultiplexer_10_out_4, demultiplexer_10_out_5, demultiplexer_10_out_6, demultiplexer_10_out_7,
       demultiplexer_11_out_0, demultiplexer_11_out_1, demultiplexer_11_out_2, demultiplexer_11_out_3,
       demultiplexer_11_out_4, demultiplexer_11_out_5, demultiplexer_11_out_6, demultiplexer_11_out_7,
       demultiplexer_12_out_0, demultiplexer_12_out_1, demultiplexer_12_out_2, demultiplexer_12_out_3,
       demultiplexer_12_out_4, demultiplexer_12_out_5, demultiplexer_12_out_6, demultiplexer_12_out_7,
       demultiplexer_13_out_0, demultiplexer_13_out_1, demultiplexer_13_out_2, demultiplexer_13_out_3,
       demultiplexer_13_out_4, demultiplexer_13_out_5, demultiplexer_13_out_6, demultiplexer_13_out_7,
       demultiplexer_14_out_0, demultiplexer_14_out_1, demultiplexer_14_out_2, demultiplexer_14_out_3,
       demultiplexer_14_out_4, demultiplexer_14_out_5, demultiplexer_14_out_6, demultiplexer_14_out_7,
       demultiplexer_15_out_0, demultiplexer_15_out_1, demultiplexer_15_out_2, demultiplexer_15_out_3,
       demultiplexer_15_out_4, demultiplexer_15_out_5, demultiplexer_15_out_6, demultiplexer_15_out_7,
       demultiplexer_16_out_0, demultiplexer_16_out_1, demultiplexer_16_out_2, demultiplexer_16_out_3,
       demultiplexer_16_out_4, demultiplexer_16_out_5, demultiplexer_16_out_6, demultiplexer_16_out_7,
       general_purpose_registers_1_r_1_out_0, general_purpose_registers_1_r_1_out_1,
       general_purpose_registers_1_r_1_out_2, general_purpose_registers_1_r_1_out_3,
       general_purpose_registers_1_r_1_out_4, general_purpose_registers_1_r_1_out_5,
       general_purpose_registers_1_r_1_out_6, general_purpose_registers_1_r_1_out_7,
       general_purpose_registers_1_r_1_out_8, general_purpose_registers_1_r_1_out_9,
       general_purpose_registers_1_r_1_out_10, general_purpose_registers_1_r_1_out_11,
       general_purpose_registers_1_r_1_out_12, general_purpose_registers_1_r_1_out_13,
       general_purpose_registers_1_r_1_out_14, general_purpose_registers_1_r_1_out_15,
       general_purpose_registers_1_r_2_out_0, general_purpose_registers_1_r_2_out_1,
       general_purpose_registers_1_r_2_out_2, general_purpose_registers_1_r_2_out_3,
       general_purpose_registers_1_r_2_out_4, general_purpose_registers_1_r_2_out_5,
       general_purpose_registers_1_r_2_out_6, general_purpose_registers_1_r_2_out_7,
       general_purpose_registers_1_r_2_out_8, general_purpose_registers_1_r_2_out_9,
       general_purpose_registers_1_r_2_out_10, general_purpose_registers_1_r_2_out_11,
       general_purpose_registers_1_r_2_out_12, general_purpose_registers_1_r_2_out_13,
       general_purpose_registers_1_r_2_out_14, general_purpose_registers_1_r_2_out_15,
       general_purpose_registers_1_r_3_out_0, general_purpose_registers_1_r_3_out_1,
       general_purpose_registers_1_r_3_out_2, general_purpose_registers_1_r_3_out_3,
       general_purpose_registers_1_r_3_out_4, general_purpose_registers_1_r_3_out_5,
       general_purpose_registers_1_r_3_out_6, general_purpose_registers_1_r_3_out_7,
       general_purpose_registers_1_r_3_out_8, general_purpose_registers_1_r_3_out_9,
       general_purpose_registers_1_r_3_out_10, general_purpose_registers_1_r_3_out_11,
       general_purpose_registers_1_r_3_out_12, general_purpose_registers_1_r_3_out_13,
       general_purpose_registers_1_r_3_out_14, general_purpose_registers_1_r_3_out_15,
       general_purpose_registers_1_r_4_out_0, general_purpose_registers_1_r_4_out_1,
       general_purpose_registers_1_r_4_out_2, general_purpose_registers_1_r_4_out_3,
       general_purpose_registers_1_r_4_out_4, general_purpose_registers_1_r_4_out_5,
       general_purpose_registers_1_r_4_out_6, general_purpose_registers_1_r_4_out_7,
       general_purpose_registers_1_r_4_out_8, general_purpose_registers_1_r_4_out_9,
       general_purpose_registers_1_r_4_out_10, general_purpose_registers_1_r_4_out_11,
       general_purpose_registers_1_r_4_out_12, general_purpose_registers_1_r_4_out_13,
       general_purpose_registers_1_r_4_out_14, general_purpose_registers_1_r_4_out_15,
       general_purpose_registers_1_r_5_out_0, general_purpose_registers_1_r_5_out_1,
       general_purpose_registers_1_r_5_out_2, general_purpose_registers_1_r_5_out_3,
       general_purpose_registers_1_r_5_out_4, general_purpose_registers_1_r_5_out_5,
       general_purpose_registers_1_r_5_out_6, general_purpose_registers_1_r_5_out_7,
       general_purpose_registers_1_r_5_out_8, general_purpose_registers_1_r_5_out_9,
       general_purpose_registers_1_r_5_out_10, general_purpose_registers_1_r_5_out_11,
       general_purpose_registers_1_r_5_out_12, general_purpose_registers_1_r_5_out_13,
       general_purpose_registers_1_r_5_out_14, general_purpose_registers_1_r_5_out_15,
       general_purpose_registers_1_r_6_out_0, general_purpose_registers_1_r_6_out_1,
       general_purpose_registers_1_r_6_out_2, general_purpose_registers_1_r_6_out_3,
       general_purpose_registers_1_r_6_out_4, general_purpose_registers_1_r_6_out_5,
       general_purpose_registers_1_r_6_out_6, general_purpose_registers_1_r_6_out_7,
       general_purpose_registers_1_r_6_out_8, general_purpose_registers_1_r_6_out_9,
       general_purpose_registers_1_r_6_out_10, general_purpose_registers_1_r_6_out_11,
       general_purpose_registers_1_r_6_out_12, general_purpose_registers_1_r_6_out_13,
       general_purpose_registers_1_r_6_out_14, general_purpose_registers_1_r_6_out_15,
       general_purpose_registers_1_r_7_out_0, general_purpose_registers_1_r_7_out_1,
       general_purpose_registers_1_r_7_out_2, general_purpose_registers_1_r_7_out_3,
       general_purpose_registers_1_r_7_out_4, general_purpose_registers_1_r_7_out_5,
       general_purpose_registers_1_r_7_out_6, general_purpose_registers_1_r_7_out_7,
       general_purpose_registers_1_r_7_out_8, general_purpose_registers_1_r_7_out_9,
       general_purpose_registers_1_r_7_out_10, general_purpose_registers_1_r_7_out_11,
       general_purpose_registers_1_r_7_out_12, general_purpose_registers_1_r_7_out_13,
       general_purpose_registers_1_r_7_out_14, general_purpose_registers_1_r_7_out_15,
       general_purpose_registers_1_r_8_out_0, general_purpose_registers_1_r_8_out_1,
       general_purpose_registers_1_r_8_out_2, general_purpose_registers_1_r_8_out_3,
       general_purpose_registers_1_r_8_out_4, general_purpose_registers_1_r_8_out_5,
       general_purpose_registers_1_r_8_out_6, general_purpose_registers_1_r_8_out_7,
       general_purpose_registers_1_r_8_out_8, general_purpose_registers_1_r_8_out_9,
       general_purpose_registers_1_r_8_out_10, general_purpose_registers_1_r_8_out_11,
       general_purpose_registers_1_r_8_out_12, general_purpose_registers_1_r_8_out_13,
       general_purpose_registers_1_r_8_out_14, general_purpose_registers_1_r_8_out_15;

  Demultiplexer #(.Selector_Bits(3)) demultiplexer_1 (
    .sel(Select_input_0), .in(Input_0), .out_0(demultiplexer_1_out_0), .out_1(demultiplexer_1_out_1),
    .out_2(demultiplexer_1_out_2), .out_3(demultiplexer_1_out_3), .out_4(demultiplexer_1_out_4),
    .out_5(demultiplexer_1_out_5), .out_6(demultiplexer_1_out_6), .out_7(demultiplexer_1_out_7));
  Demultiplexer #(.Selector_Bits(3)) demultiplexer_2 (
    .sel(Select_input_0), .in(Input_1), .out_0(demultiplexer_2_out_0), .out_1(demultiplexer_2_out_1),
    .out_2(demultiplexer_2_out_2), .out_3(demultiplexer_2_out_3), .out_4(demultiplexer_2_out_4),
    .out_5(demultiplexer_2_out_5), .out_6(demultiplexer_2_out_6), .out_7(demultiplexer_2_out_7));
  Demultiplexer #(.Selector_Bits(3)) demultiplexer_3 (
    .sel(Select_input_0), .in(Input_2), .out_0(demultiplexer_3_out_0), .out_1(demultiplexer_3_out_1),
    .out_2(demultiplexer_3_out_2), .out_3(demultiplexer_3_out_3), .out_4(demultiplexer_3_out_4),
    .out_5(demultiplexer_3_out_5), .out_6(demultiplexer_3_out_6), .out_7(demultiplexer_3_out_7));
  Demultiplexer #(.Selector_Bits(3)) demultiplexer_4 (
    .sel(Select_input_0), .in(Input_3), .out_0(demultiplexer_4_out_0), .out_1(demultiplexer_4_out_1),
    .out_2(demultiplexer_4_out_2), .out_3(demultiplexer_4_out_3), .out_4(demultiplexer_4_out_4),
    .out_5(demultiplexer_4_out_5), .out_6(demultiplexer_4_out_6), .out_7(demultiplexer_4_out_7));
  Demultiplexer #(.Selector_Bits(3)) demultiplexer_5 (
    .sel(Select_input_0), .in(Input_4), .out_0(demultiplexer_5_out_0), .out_1(demultiplexer_5_out_1),
    .out_2(demultiplexer_5_out_2), .out_3(demultiplexer_5_out_3), .out_4(demultiplexer_5_out_4),
    .out_5(demultiplexer_5_out_5), .out_6(demultiplexer_5_out_6), .out_7(demultiplexer_5_out_7));
  Demultiplexer #(.Selector_Bits(3)) demultiplexer_6 (
    .sel(Select_input_0), .in(Input_5), .out_0(demultiplexer_6_out_0), .out_1(demultiplexer_6_out_1),
    .out_2(demultiplexer_6_out_2), .out_3(demultiplexer_6_out_3), .out_4(demultiplexer_6_out_4),
    .out_5(demultiplexer_6_out_5), .out_6(demultiplexer_6_out_6), .out_7(demultiplexer_6_out_7));
  Demultiplexer #(.Selector_Bits(3)) demultiplexer_7 (
    .sel(Select_input_0), .in(Input_6), .out_0(demultiplexer_7_out_0), .out_1(demultiplexer_7_out_1),
    .out_2(demultiplexer_7_out_2), .out_3(demultiplexer_7_out_3), .out_4(demultiplexer_7_out_4),
    .out_5(demultiplexer_7_out_5), .out_6(demultiplexer_7_out_6), .out_7(demultiplexer_7_out_7));
  Demultiplexer #(.Selector_Bits(3)) demultiplexer_8 (
    .sel(Select_input_0), .in(Input_7), .out_0(demultiplexer_8_out_0), .out_1(demultiplexer_8_out_1),
    .out_2(demultiplexer_8_out_2), .out_3(demultiplexer_8_out_3), .out_4(demultiplexer_8_out_4),
    .out_5(demultiplexer_8_out_5), .out_6(demultiplexer_8_out_6), .out_7(demultiplexer_8_out_7));
  Demultiplexer #(.Selector_Bits(3)) demultiplexer_9 (
    .sel(Select_input_0), .in(Input_8), .out_0(demultiplexer_9_out_0), .out_1(demultiplexer_9_out_1),
    .out_2(demultiplexer_9_out_2), .out_3(demultiplexer_9_out_3), .out_4(demultiplexer_9_out_4),
    .out_5(demultiplexer_9_out_5), .out_6(demultiplexer_9_out_6), .out_7(demultiplexer_9_out_7));
  Demultiplexer #(.Selector_Bits(3)) demultiplexer_10 (
    .sel(Select_input_0), .in(Input_9), .out_0(demultiplexer_10_out_0), .out_1(demultiplexer_10_out_1),
    .out_2(demultiplexer_10_out_2), .out_3(demultiplexer_10_out_3), .out_4(demultiplexer_10_out_4),
    .out_5(demultiplexer_10_out_5), .out_6(demultiplexer_10_out_6), .out_7(demultiplexer_10_out_7));
  Demultiplexer #(.Selector_Bits(3)) demultiplexer_11 (
    .sel(Select_input_0), .in(Input_10), .out_0(demultiplexer_11_out_0), .out_1(demultiplexer_11_out_1),
    .out_2(demultiplexer_11_out_2), .out_3(demultiplexer_11_out_3), .out_4(demultiplexer_11_out_4),
    .out_5(demultiplexer_11_out_5), .out_6(demultiplexer_11_out_6), .out_7(demultiplexer_11_out_7));
  Demultiplexer #(.Selector_Bits(3)) demultiplexer_12 (
    .sel(Select_input_0), .in(Input_11), .out_0(demultiplexer_12_out_0), .out_1(demultiplexer_12_out_1),
    .out_2(demultiplexer_12_out_2), .out_3(demultiplexer_12_out_3), .out_4(demultiplexer_12_out_4),
    .out_5(demultiplexer_12_out_5), .out_6(demultiplexer_12_out_6), .out_7(demultiplexer_12_out_7));
  Demultiplexer #(.Selector_Bits(3)) demultiplexer_13 (
    .sel(Select_input_0), .in(Input_12), .out_0(demultiplexer_13_out_0), .out_1(demultiplexer_13_out_1),
    .out_2(demultiplexer_13_out_2), .out_3(demultiplexer_13_out_3), .out_4(demultiplexer_13_out_4),
    .out_5(demultiplexer_13_out_5), .out_6(demultiplexer_13_out_6), .out_7(demultiplexer_13_out_7));
  Demultiplexer #(.Selector_Bits(3)) demultiplexer_14 (
    .sel(Select_input_0), .in(Input_13), .out_0(demultiplexer_14_out_0), .out_1(demultiplexer_14_out_1),
    .out_2(demultiplexer_14_out_2), .out_3(demultiplexer_14_out_3), .out_4(demultiplexer_14_out_4),
    .out_5(demultiplexer_14_out_5), .out_6(demultiplexer_14_out_6), .out_7(demultiplexer_14_out_7));
  Demultiplexer #(.Selector_Bits(3)) demultiplexer_15 (
    .sel(Select_input_0), .in(Input_14), .out_0(demultiplexer_15_out_0), .out_1(demultiplexer_15_out_1),
    .out_2(demultiplexer_15_out_2), .out_3(demultiplexer_15_out_3), .out_4(demultiplexer_15_out_4),
    .out_5(demultiplexer_15_out_5), .out_6(demultiplexer_15_out_6), .out_7(demultiplexer_15_out_7));
  Demultiplexer #(.Selector_Bits(3)) demultiplexer_16 (
    .sel(Select_input_0), .in(Input_15), .out_0(demultiplexer_16_out_0), .out_1(demultiplexer_16_out_1),
    .out_2(demultiplexer_16_out_2), .out_3(demultiplexer_16_out_3), .out_4(demultiplexer_16_out_4),
    .out_5(demultiplexer_16_out_5), .out_6(demultiplexer_16_out_6), .out_7(demultiplexer_16_out_7));
  general_purpose_registers general_purpose_registers_1 (
    .R_1_0(demultiplexer_1_out_0), .R_1_1(demultiplexer_2_out_0), .R_1_2(demultiplexer_3_out_0),
    .R_1_3(demultiplexer_4_out_0), .R_1_4(demultiplexer_5_out_0), .R_1_5(demultiplexer_6_out_0),
    .R_1_6(demultiplexer_7_out_0), .R_1_7(demultiplexer_8_out_0), .R_1_8(demultiplexer_9_out_0),
    .R_1_9(demultiplexer_10_out_0), .R_1_10(demultiplexer_11_out_0), .R_1_11(demultiplexer_12_out_0),
    .R_1_12(demultiplexer_13_out_0), .R_1_13(demultiplexer_14_out_0), .R_1_14(demultiplexer_15_out_0),
    .R_1_15(demultiplexer_16_out_0), .R_2_0(demultiplexer_1_out_1), .R_2_1(demultiplexer_2_out_1),
    .R_2_2(demultiplexer_3_out_1), .R_2_3(demultiplexer_4_out_1), .R_2_4(demultiplexer_5_out_1),
    .R_2_5(demultiplexer_6_out_1), .R_2_6(demultiplexer_7_out_1), .R_2_7(demultiplexer_8_out_1),
    .R_2_8(demultiplexer_9_out_1), .R_2_9(demultiplexer_10_out_1), .R_2_10(demultiplexer_11_out_1),
    .R_2_11(demultiplexer_12_out_1), .R_2_12(demultiplexer_13_out_1), .R_2_13(demultiplexer_14_out_1),
    .R_2_14(demultiplexer_15_out_1), .R_2_15(demultiplexer_16_out_1), .R_3_0(demultiplexer_1_out_2),
    .R_3_1(demultiplexer_2_out_2), .R_3_2(demultiplexer_3_out_2), .R_3_3(demultiplexer_4_out_2),
    .R_3_4(demultiplexer_5_out_2), .R_3_5(demultiplexer_6_out_2), .R_3_6(demultiplexer_7_out_2),
    .R_3_7(demultiplexer_8_out_2), .R_3_8(demultiplexer_9_out_2), .R_3_9(demultiplexer_10_out_2),
    .R_3_10(demultiplexer_11_out_2), .R_3_11(demultiplexer_12_out_2), .R_3_12(demultiplexer_13_out_2),
    .R_3_13(demultiplexer_14_out_2), .R_3_14(demultiplexer_15_out_2), .R_3_15(demultiplexer_16_out_2),
    .R_4_0(demultiplexer_1_out_3), .R_4_1(demultiplexer_2_out_3), .R_4_2(demultiplexer_3_out_3),
    .R_4_3(demultiplexer_4_out_3), .R_4_4(demultiplexer_5_out_3), .R_4_5(demultiplexer_6_out_3),
    .R_4_6(demultiplexer_7_out_3), .R_4_7(demultiplexer_8_out_3), .R_4_8(demultiplexer_9_out_3),
    .R_4_9(demultiplexer_10_out_3), .R_4_10(demultiplexer_11_out_3), .R_4_11(demultiplexer_12_out_3),
    .R_4_12(demultiplexer_13_out_3), .R_4_13(demultiplexer_14_out_3), .R_4_14(demultiplexer_15_out_3),
    .R_4_15(demultiplexer_16_out_3), .R_5_0(demultiplexer_1_out_4), .R_5_1(demultiplexer_2_out_4),
    .R_5_2(demultiplexer_3_out_4), .R_5_3(demultiplexer_4_out_4), .R_5_4(demultiplexer_5_out_4),
    .R_5_5(demultiplexer_6_out_4), .R_5_6(demultiplexer_7_out_4), .R_5_7(demultiplexer_8_out_4),
    .R_5_8(demultiplexer_9_out_4), .R_5_9(demultiplexer_10_out_4), .R_5_10(demultiplexer_11_out_4),
    .R_5_11(demultiplexer_12_out_4), .R_5_12(demultiplexer_13_out_4), .R_5_13(demultiplexer_14_out_4),
    .R_5_14(demultiplexer_15_out_4), .R_5_15(demultiplexer_16_out_4), .R_6_0(demultiplexer_1_out_5),
    .R_6_1(demultiplexer_2_out_5), .R_6_2(demultiplexer_3_out_5), .R_6_3(demultiplexer_4_out_5),
    .R_6_4(demultiplexer_5_out_5), .R_6_5(demultiplexer_6_out_5), .R_6_6(demultiplexer_7_out_5),
    .R_6_7(demultiplexer_8_out_5), .R_6_8(demultiplexer_9_out_5), .R_6_9(demultiplexer_10_out_5),
    .R_6_10(demultiplexer_11_out_5), .R_6_11(demultiplexer_12_out_5), .R_6_12(demultiplexer_13_out_5),
    .R_6_13(demultiplexer_14_out_5), .R_6_14(demultiplexer_15_out_5), .R_6_15(demultiplexer_16_out_5),
    .R_7_0(demultiplexer_1_out_6), .R_7_1(demultiplexer_2_out_6), .R_7_2(demultiplexer_3_out_6),
    .R_7_3(demultiplexer_4_out_6), .R_7_4(demultiplexer_5_out_6), .R_7_5(demultiplexer_6_out_6),
    .R_7_6(demultiplexer_7_out_6), .R_7_7(demultiplexer_8_out_6), .R_7_8(demultiplexer_9_out_6),
    .R_7_9(demultiplexer_10_out_6), .R_7_10(demultiplexer_11_out_6), .R_7_11(demultiplexer_12_out_6),
    .R_7_12(demultiplexer_13_out_6), .R_7_13(demultiplexer_14_out_6), .R_7_14(demultiplexer_15_out_6),
    .R_7_15(demultiplexer_16_out_6), .R_8_0(demultiplexer_1_out_7), .R_8_1(demultiplexer_2_out_7),
    .R_8_2(demultiplexer_3_out_7), .R_8_3(demultiplexer_4_out_7), .R_8_4(demultiplexer_5_out_7),
    .R_8_5(demultiplexer_6_out_7), .R_8_6(demultiplexer_7_out_7), .R_8_7(demultiplexer_8_out_7),
    .R_8_8(demultiplexer_9_out_7), .R_8_9(demultiplexer_10_out_7), .R_8_10(demultiplexer_11_out_7),
    .R_8_11(demultiplexer_12_out_7), .R_8_12(demultiplexer_13_out_7), .R_8_13(demultiplexer_14_out_7),
    .R_8_14(demultiplexer_15_out_7), .R_8_15(demultiplexer_16_out_7), .clk(Clock), .rst(Reset),
    .R_1_out_0(general_purpose_registers_1_r_1_out_0), .R_1_out_1(general_purpose_registers_1_r_1_out_1),
    .R_1_out_2(general_purpose_registers_1_r_1_out_2), .R_1_out_3(general_purpose_registers_1_r_1_out_3),
    .R_1_out_4(general_purpose_registers_1_r_1_out_4), .R_1_out_5(general_purpose_registers_1_r_1_out_5),
    .R_1_out_6(general_purpose_registers_1_r_1_out_6), .R_1_out_7(general_purpose_registers_1_r_1_out_7),
    .R_1_out_8(general_purpose_registers_1_r_1_out_8), .R_1_out_9(general_purpose_registers_1_r_1_out_9),
    .R_1_out_10(general_purpose_registers_1_r_1_out_10), .R_1_out_11(general_purpose_registers_1_r_1_out_11),
    .R_1_out_12(general_purpose_registers_1_r_1_out_12), .R_1_out_13(general_purpose_registers_1_r_1_out_13),
    .R_1_out_14(general_purpose_registers_1_r_1_out_14), .R_1_out_15(general_purpose_registers_1_r_1_out_15),
    .R_2_out_0(general_purpose_registers_1_r_2_out_0), .R_2_out_1(general_purpose_registers_1_r_2_out_1),
    .R_2_out_2(general_purpose_registers_1_r_2_out_2), .R_2_out_3(general_purpose_registers_1_r_2_out_3),
    .R_2_out_4(general_purpose_registers_1_r_2_out_4), .R_2_out_5(general_purpose_registers_1_r_2_out_5),
    .R_2_out_6(general_purpose_registers_1_r_2_out_6), .R_2_out_7(general_purpose_registers_1_r_2_out_7),
    .R_2_out_8(general_purpose_registers_1_r_2_out_8), .R_2_out_9(general_purpose_registers_1_r_2_out_9),
    .R_2_out_10(general_purpose_registers_1_r_2_out_10), .R_2_out_11(general_purpose_registers_1_r_2_out_11),
    .R_2_out_12(general_purpose_registers_1_r_2_out_12), .R_2_out_13(general_purpose_registers_1_r_2_out_13),
    .R_2_out_14(general_purpose_registers_1_r_2_out_14), .R_2_out_15(general_purpose_registers_1_r_2_out_15),
    .R_3_out_0(general_purpose_registers_1_r_3_out_0), .R_3_out_1(general_purpose_registers_1_r_3_out_1),
    .R_3_out_2(general_purpose_registers_1_r_3_out_2), .R_3_out_3(general_purpose_registers_1_r_3_out_3),
    .R_3_out_4(general_purpose_registers_1_r_3_out_4), .R_3_out_5(general_purpose_registers_1_r_3_out_5),
    .R_3_out_6(general_purpose_registers_1_r_3_out_6), .R_3_out_7(general_purpose_registers_1_r_3_out_7),
    .R_3_out_8(general_purpose_registers_1_r_3_out_8), .R_3_out_9(general_purpose_registers_1_r_3_out_9),
    .R_3_out_10(general_purpose_registers_1_r_3_out_10), .R_3_out_11(general_purpose_registers_1_r_3_out_11),
    .R_3_out_12(general_purpose_registers_1_r_3_out_12), .R_3_out_13(general_purpose_registers_1_r_3_out_13),
    .R_3_out_14(general_purpose_registers_1_r_3_out_14), .R_3_out_15(general_purpose_registers_1_r_3_out_15),
    .R_4_out_0(general_purpose_registers_1_r_4_out_0), .R_4_out_1(general_purpose_registers_1_r_4_out_1),
    .R_4_out_2(general_purpose_registers_1_r_4_out_2), .R_4_out_3(general_purpose_registers_1_r_4_out_3),
    .R_4_out_4(general_purpose_registers_1_r_4_out_4), .R_4_out_5(general_purpose_registers_1_r_4_out_5),
    .R_4_out_6(general_purpose_registers_1_r_4_out_6), .R_4_out_7(general_purpose_registers_1_r_4_out_7),
    .R_4_out_8(general_purpose_registers_1_r_4_out_8), .R_4_out_9(general_purpose_registers_1_r_4_out_9),
    .R_4_out_10(general_purpose_registers_1_r_4_out_10), .R_4_out_11(general_purpose_registers_1_r_4_out_11),
    .R_4_out_12(general_purpose_registers_1_r_4_out_12), .R_4_out_13(general_purpose_registers_1_r_4_out_13),
    .R_4_out_14(general_purpose_registers_1_r_4_out_14), .R_4_out_15(general_purpose_registers_1_r_4_out_15),
    .R_5_out_0(general_purpose_registers_1_r_5_out_0), .R_5_out_1(general_purpose_registers_1_r_5_out_1),
    .R_5_out_2(general_purpose_registers_1_r_5_out_2), .R_5_out_3(general_purpose_registers_1_r_5_out_3),
    .R_5_out_4(general_purpose_registers_1_r_5_out_4), .R_5_out_5(general_purpose_registers_1_r_5_out_5),
    .R_5_out_6(general_purpose_registers_1_r_5_out_6), .R_5_out_7(general_purpose_registers_1_r_5_out_7),
    .R_5_out_8(general_purpose_registers_1_r_5_out_8), .R_5_out_9(general_purpose_registers_1_r_5_out_9),
    .R_5_out_10(general_purpose_registers_1_r_5_out_10), .R_5_out_11(general_purpose_registers_1_r_5_out_11),
    .R_5_out_12(general_purpose_registers_1_r_5_out_12), .R_5_out_13(general_purpose_registers_1_r_5_out_13),
    .R_5_out_14(general_purpose_registers_1_r_5_out_14), .R_5_out_15(general_purpose_registers_1_r_5_out_15),
    .R_6_out_0(general_purpose_registers_1_r_6_out_0), .R_6_out_1(general_purpose_registers_1_r_6_out_1),
    .R_6_out_2(general_purpose_registers_1_r_6_out_2), .R_6_out_3(general_purpose_registers_1_r_6_out_3),
    .R_6_out_4(general_purpose_registers_1_r_6_out_4), .R_6_out_5(general_purpose_registers_1_r_6_out_5),
    .R_6_out_6(general_purpose_registers_1_r_6_out_6), .R_6_out_7(general_purpose_registers_1_r_6_out_7),
    .R_6_out_8(general_purpose_registers_1_r_6_out_8), .R_6_out_9(general_purpose_registers_1_r_6_out_9),
    .R_6_out_10(general_purpose_registers_1_r_6_out_10), .R_6_out_11(general_purpose_registers_1_r_6_out_11),
    .R_6_out_12(general_purpose_registers_1_r_6_out_12), .R_6_out_13(general_purpose_registers_1_r_6_out_13),
    .R_6_out_14(general_purpose_registers_1_r_6_out_14), .R_6_out_15(general_purpose_registers_1_r_6_out_15),
    .R_7_out_0(general_purpose_registers_1_r_7_out_0), .R_7_out_1(general_purpose_registers_1_r_7_out_1),
    .R_7_out_2(general_purpose_registers_1_r_7_out_2), .R_7_out_3(general_purpose_registers_1_r_7_out_3),
    .R_7_out_4(general_purpose_registers_1_r_7_out_4), .R_7_out_5(general_purpose_registers_1_r_7_out_5),
    .R_7_out_6(general_purpose_registers_1_r_7_out_6), .R_7_out_7(general_purpose_registers_1_r_7_out_7),
    .R_7_out_8(general_purpose_registers_1_r_7_out_8), .R_7_out_9(general_purpose_registers_1_r_7_out_9),
    .R_7_out_10(general_purpose_registers_1_r_7_out_10), .R_7_out_11(general_purpose_registers_1_r_7_out_11),
    .R_7_out_12(general_purpose_registers_1_r_7_out_12), .R_7_out_13(general_purpose_registers_1_r_7_out_13),
    .R_7_out_14(general_purpose_registers_1_r_7_out_14), .R_7_out_15(general_purpose_registers_1_r_7_out_15),
    .R_8_out_0(general_purpose_registers_1_r_8_out_0), .R_8_out_1(general_purpose_registers_1_r_8_out_1),
    .R_8_out_2(general_purpose_registers_1_r_8_out_2), .R_8_out_3(general_purpose_registers_1_r_8_out_3),
    .R_8_out_4(general_purpose_registers_1_r_8_out_4), .R_8_out_5(general_purpose_registers_1_r_8_out_5),
    .R_8_out_6(general_purpose_registers_1_r_8_out_6), .R_8_out_7(general_purpose_registers_1_r_8_out_7),
    .R_8_out_8(general_purpose_registers_1_r_8_out_8), .R_8_out_9(general_purpose_registers_1_r_8_out_9),
    .R_8_out_10(general_purpose_registers_1_r_8_out_10), .R_8_out_11(general_purpose_registers_1_r_8_out_11),
    .R_8_out_12(general_purpose_registers_1_r_8_out_12), .R_8_out_13(general_purpose_registers_1_r_8_out_13),
    .R_8_out_14(general_purpose_registers_1_r_8_out_14), .R_8_out_15(general_purpose_registers_1_r_8_out_15));
  Multiplexer #(.Selector_Bits(3)) multiplexer_1 (
    .sel(Select_output_0), .in_0(general_purpose_registers_1_r_1_out_0),
    .in_1(general_purpose_registers_1_r_2_out_0), .in_2(general_purpose_registers_1_r_3_out_0),
    .in_3(general_purpose_registers_1_r_4_out_0), .in_4(general_purpose_registers_1_r_5_out_0),
    .in_5(general_purpose_registers_1_r_6_out_0), .in_6(general_purpose_registers_1_r_7_out_0),
    .in_7(general_purpose_registers_1_r_8_out_0), .out(Output_0));
  Multiplexer #(.Selector_Bits(3)) multiplexer_2 (
    .sel(Select_output_0), .in_0(general_purpose_registers_1_r_1_out_1),
    .in_1(general_purpose_registers_1_r_2_out_1), .in_2(general_purpose_registers_1_r_3_out_1),
    .in_3(general_purpose_registers_1_r_4_out_1), .in_4(general_purpose_registers_1_r_5_out_1),
    .in_5(general_purpose_registers_1_r_6_out_1), .in_6(general_purpose_registers_1_r_7_out_1),
    .in_7(general_purpose_registers_1_r_8_out_1), .out(Output_1));
  Multiplexer #(.Selector_Bits(3)) multiplexer_3 (
    .sel(Select_output_0), .in_0(general_purpose_registers_1_r_1_out_2),
    .in_1(general_purpose_registers_1_r_2_out_2), .in_2(general_purpose_registers_1_r_3_out_2),
    .in_3(general_purpose_registers_1_r_4_out_2), .in_4(general_purpose_registers_1_r_5_out_2),
    .in_5(general_purpose_registers_1_r_6_out_2), .in_6(general_purpose_registers_1_r_7_out_2),
    .in_7(general_purpose_registers_1_r_8_out_2), .out(Output_2));
  Multiplexer #(.Selector_Bits(3)) multiplexer_4 (
    .sel(Select_output_0), .in_0(general_purpose_registers_1_r_1_out_3),
    .in_1(general_purpose_registers_1_r_2_out_3), .in_2(general_purpose_registers_1_r_3_out_3),
    .in_3(general_purpose_registers_1_r_4_out_3), .in_4(general_purpose_registers_1_r_5_out_3),
    .in_5(general_purpose_registers_1_r_6_out_3), .in_6(general_purpose_registers_1_r_7_out_3),
    .in_7(general_purpose_registers_1_r_8_out_3), .out(Output_3));
  Multiplexer #(.Selector_Bits(3)) multiplexer_5 (
    .sel(Select_output_0), .in_0(general_purpose_registers_1_r_1_out_4),
    .in_1(general_purpose_registers_1_r_2_out_4), .in_2(general_purpose_registers_1_r_3_out_4),
    .in_3(general_purpose_registers_1_r_4_out_4), .in_4(general_purpose_registers_1_r_5_out_4),
    .in_5(general_purpose_registers_1_r_6_out_4), .in_6(general_purpose_registers_1_r_7_out_4),
    .in_7(general_purpose_registers_1_r_8_out_4), .out(Output_4));
  Multiplexer #(.Selector_Bits(3)) multiplexer_6 (
    .sel(Select_output_0), .in_0(general_purpose_registers_1_r_1_out_5),
    .in_1(general_purpose_registers_1_r_2_out_5), .in_2(general_purpose_registers_1_r_3_out_5),
    .in_3(general_purpose_registers_1_r_4_out_5), .in_4(general_purpose_registers_1_r_5_out_5),
    .in_5(general_purpose_registers_1_r_6_out_5), .in_6(general_purpose_registers_1_r_7_out_5),
    .in_7(general_purpose_registers_1_r_8_out_5), .out(Output_5));
  Multiplexer #(.Selector_Bits(3)) multiplexer_7 (
    .sel(Select_output_0), .in_0(general_purpose_registers_1_r_1_out_6),
    .in_1(general_purpose_registers_1_r_2_out_6), .in_2(general_purpose_registers_1_r_3_out_6),
    .in_3(general_purpose_registers_1_r_4_out_6), .in_4(general_purpose_registers_1_r_5_out_6),
    .in_5(general_purpose_registers_1_r_6_out_6), .in_6(general_purpose_registers_1_r_7_out_6),
    .in_7(general_purpose_registers_1_r_8_out_6), .out(Output_6));
  Multiplexer #(.Selector_Bits(3)) multiplexer_8 (
    .sel(Select_output_0), .in_0(general_purpose_registers_1_r_1_out_7),
    .in_1(general_purpose_registers_1_r_2_out_7), .in_2(general_purpose_registers_1_r_3_out_7),
    .in_3(general_purpose_registers_1_r_4_out_7), .in_4(general_purpose_registers_1_r_5_out_7),
    .in_5(general_purpose_registers_1_r_6_out_7), .in_6(general_purpose_registers_1_r_7_out_7),
    .in_7(general_purpose_registers_1_r_8_out_7), .out(Output_7));
  Multiplexer #(.Selector_Bits(3)) multiplexer_9 (
    .sel(Select_output_0), .in_0(general_purpose_registers_1_r_1_out_8),
    .in_1(general_purpose_registers_1_r_2_out_8), .in_2(general_purpose_registers_1_r_3_out_8),
    .in_3(general_purpose_registers_1_r_4_out_8), .in_4(general_purpose_registers_1_r_5_out_8),
    .in_5(general_purpose_registers_1_r_6_out_8), .in_6(general_purpose_registers_1_r_7_out_8),
    .in_7(general_purpose_registers_1_r_8_out_8), .out(Output_8));
  Multiplexer #(.Selector_Bits(3)) multiplexer_10 (
    .sel(Select_output_0), .in_0(general_purpose_registers_1_r_1_out_9),
    .in_1(general_purpose_registers_1_r_2_out_9), .in_2(general_purpose_registers_1_r_3_out_9),
    .in_3(general_purpose_registers_1_r_4_out_9), .in_4(general_purpose_registers_1_r_5_out_9),
    .in_5(general_purpose_registers_1_r_6_out_9), .in_6(general_purpose_registers_1_r_7_out_9),
    .in_7(general_purpose_registers_1_r_8_out_9), .out(Output_9));
  Multiplexer #(.Selector_Bits(3)) multiplexer_11 (
    .sel(Select_output_0), .in_0(general_purpose_registers_1_r_1_out_10),
    .in_1(general_purpose_registers_1_r_2_out_10), .in_2(general_purpose_registers_1_r_3_out_10),
    .in_3(general_purpose_registers_1_r_4_out_10), .in_4(general_purpose_registers_1_r_5_out_10),
    .in_5(general_purpose_registers_1_r_6_out_10), .in_6(general_purpose_registers_1_r_7_out_10),
    .in_7(general_purpose_registers_1_r_8_out_10), .out(Output_10));
  Multiplexer #(.Selector_Bits(3)) multiplexer_12 (
    .sel(Select_output_0), .in_0(general_purpose_registers_1_r_1_out_11),
    .in_1(general_purpose_registers_1_r_2_out_11), .in_2(general_purpose_registers_1_r_3_out_11),
    .in_3(general_purpose_registers_1_r_4_out_11), .in_4(general_purpose_registers_1_r_5_out_11),
    .in_5(general_purpose_registers_1_r_6_out_11), .in_6(general_purpose_registers_1_r_7_out_11),
    .in_7(general_purpose_registers_1_r_8_out_11), .out(Output_11));
  Multiplexer #(.Selector_Bits(3)) multiplexer_13 (
    .sel(Select_output_0), .in_0(general_purpose_registers_1_r_1_out_12),
    .in_1(general_purpose_registers_1_r_2_out_12), .in_2(general_purpose_registers_1_r_3_out_12),
    .in_3(general_purpose_registers_1_r_4_out_12), .in_4(general_purpose_registers_1_r_5_out_12),
    .in_5(general_purpose_registers_1_r_6_out_12), .in_6(general_purpose_registers_1_r_7_out_12),
    .in_7(general_purpose_registers_1_r_8_out_12), .out(Output_12));
  Multiplexer #(.Selector_Bits(3)) multiplexer_14 (
    .sel(Select_output_0), .in_0(general_purpose_registers_1_r_1_out_13),
    .in_1(general_purpose_registers_1_r_2_out_13), .in_2(general_purpose_registers_1_r_3_out_13),
    .in_3(general_purpose_registers_1_r_4_out_13), .in_4(general_purpose_registers_1_r_5_out_13),
    .in_5(general_purpose_registers_1_r_6_out_13), .in_6(general_purpose_registers_1_r_7_out_13),
    .in_7(general_purpose_registers_1_r_8_out_13), .out(Output_13));
  Multiplexer #(.Selector_Bits(3)) multiplexer_15 (
    .sel(Select_output_0), .in_0(general_purpose_registers_1_r_1_out_14),
    .in_1(general_purpose_registers_1_r_2_out_14), .in_2(general_purpose_registers_1_r_3_out_14),
    .in_3(general_purpose_registers_1_r_4_out_14), .in_4(general_purpose_registers_1_r_5_out_14),
    .in_5(general_purpose_registers_1_r_6_out_14), .in_6(general_purpose_registers_1_r_7_out_14),
    .in_7(general_purpose_registers_1_r_8_out_14), .out(Output_14));
  Multiplexer #(.Selector_Bits(3)) multiplexer_16 (
    .sel(Select_output_0), .in_0(general_purpose_registers_1_r_1_out_15),
    .in_1(general_purpose_registers_1_r_2_out_15), .in_2(general_purpose_registers_1_r_3_out_15),
    .in_3(general_purpose_registers_1_r_4_out_15), .in_4(general_purpose_registers_1_r_5_out_15),
    .in_5(general_purpose_registers_1_r_6_out_15), .in_6(general_purpose_registers_1_r_7_out_15),
    .in_7(general_purpose_registers_1_r_8_out_15), .out(Output_15));
  // Pins of 1 and 3 bits meet at Select_input_0
  // Pins of 1 and 3 bits meet at Select_output_0

  assign Select_input_1 = Select_input_0;
  assign Select_input_2 = Select_input_0;
  assign Select_output_1 = Select_output_0;
  assign Select_output_2 = Select_output_0;
endmodule
