// Digital circuit 8bit_register.dig as structural Verilog
module _8bit_register (
  input  D_0,
  input  Clock,
  input  Reset,
  input  D_1,
  input  D_2,
  input  D_3,
  input  D_4,
  input  D_5,
  input  D_6,
  input  D_7,
  output Q_0,
  output Q_1,
  output Q_2,
  output Q_3,
  output Q_4,
  output Q_5,
  output Q_6,
  output Q_7
);

  wire multiplexer_1_out, multiplexer_2_out, multiplexer_3_out, multiplexer_4_out, multiplexer_5_out,
       multiplexer_6_out, multiplexer_7_out, multiplexer_8_out, xor_1_out;

  xor xor_1 (xor_1_out, Reset, Clock);
  Multiplexer multiplexer_1 (.sel(Reset), .in_0(D_0), .in_1(1'b0), .out(multiplexer_1_out));
  Multiplexer multiplexer_2 (.sel(Reset), .in_0(D_1), .in_1(1'b0), .out(multiplexer_2_out));
  Multiplexer multiplexer_3 (.sel(Reset), .in_0(D_2), .in_1(1'b0), .out(multiplexer_3_out));
  Multiplexer multiplexer_4 (.sel(Reset), .in_0(D_3), .in_1(1'b0), .out(multiplexer_4_out));
  Multiplexer multiplexer_5 (.sel(Reset), .in_0(D_4), .in_1(1'b0), .out(multiplexer_5_out));
  Multiplexer multiplexer_6 (.sel(Reset), .in_0(D_5), .in_1(1'b0), .out(multiplexer_6_out));
  Multiplexer multiplexer_7 (.sel(Reset), .in_0(D_6), .in_1(1'b0), .out(multiplexer_7_out));
  Multiplexer multiplexer_8 (.sel(Reset), .in_0(D_7), .in_1(1'b0), .out(multiplexer_8_out));
  D_FF d_ff_1 (.D(multiplexer_1_out), .C(xor_1_out), .Q(Q_0));  // open: nQ
  D_FF d_ff_2 (.D(multiplexer_2_out), .C(xor_1_out), .Q(Q_1));  // open: nQ
  D_FF d_ff_3 (.D(multiplexer_3_out), .C(xor_1_out), .Q(Q_2));  // open: nQ
  D_FF d_ff_4 (.D(multiplexer_4_out), .C(xor_1_out), .Q(Q_3));  // open: nQ
  D_FF d_ff_5 (.D(multiplexer_5_out), .C(xor_1_out), .Q(Q_4));  // open: nQ
  D_FF d_ff_6 (.D(multiplexer_6_out), .C(xor_1_out), .Q(Q_5));  // open: nQ
  D_FF d_ff_7 (.D(multiplexer_7_out), .C(xor_1_out), .Q(Q_6));  // open: nQ
  D_FF d_ff_8 (.D(multiplexer_8_out), .C(xor_1_out), .Q(Q_7));  // open: nQ
endmodule
