// Digital circuit ALU.dig as structural Verilog
module ALU (
  input  Input1_0,
  input  Input1_1,
  input  Input1_2,
  input  Input1_3,
  input  Input1_4,
  input  Input1_5,
  input  Input1_6,
  input  Input1_7,
  input  Input1_8,
  input  Input1_9,
  input  Input1_10,
  input  Input1_11,
  input  Input1_12,
  input  Input1_13,
  input  Input1_14,
  input  Input1_15,
  input  Input2_0,
  input  Input2_1,
  input  Input2_2,
  input  Input2_3,
  input  Input2_4,
  input  Input2_5,
  input  Input2_6,
  input  Input2_7,
  input  Input2_8,
  input  Input2_9,
  input  Input2_10,
  input  Input2_11,
  input  Input2_12,
  input  Input2_13,
  input  Input2_14,
  input  Input2_15,
  input  SelectOP_0,
  input  SelectOP_1,
  input  Carry_in,
  input  SelectOP_2,
  input  SelectOP_3,
  output [15:0] CarryOut,
  output Output_0,
  output Output_1,
  output Output_2,
  output Output_3,
  output Output_4,
  output Output_5,
  output Output_6,
  output Output_7,
  output Output_8,
  output Output_9,
  output Output_10,
  output Output_11,
  output Output_12,
  output Output_13,
  output Output_14,
  output Output_15,
  output [15:0] Zero,
  output [15:0] Negative,
  output [15:0] Overflow,
  output Addr_0,
  output Addr_1,
  output Addr_2,
  output Addr_3,
  output Addr_4,
  output Addr_5,
  output Addr_6,
  output Addr_7,
  output Addr_8,
  output Addr_9,
  output Addr_10,
  output Addr_11,
  output Addr_12,
  output Addr_13,
  output Addr_14,
  output Addr_15
);

  wire Compare_p33, Compare_p34, Compare_p35, Compare_p36, Compare_p37, Compare_p38, Compare_p39,
       Compare_p40, Compare_p41, Compare_p42, Compare_p43, Compare_p44, Compare_p45, Compare_p46,
       Compare_p47, Compare_p48, not_1_out;
  wire [15:0] adder_1_p25, adder_1_p41, and_16_bit_1_and_0, Compare_p32, Compare_p49, Decrement_sub_0,
       demultiplexer_1_out_1, demultiplexer_1_out_2, demultiplexer_1_out_3, demultiplexer_1_out_4,
       demultiplexer_1_out_5, demultiplexer_1_out_6, demultiplexer_1_out_7, demultiplexer_1_out_8,
       demultiplexer_1_out_9, demultiplexer_1_out_10, demultiplexer_1_out_11, demultiplexer_1_out_12,
       demultiplexer_1_out_13, demultiplexer_2_out_1, demultiplexer_2_out_2, demultiplexer_2_out_3,
       demultiplexer_2_out_4, demultiplexer_2_out_5, demultiplexer_2_out_6, demultiplexer_2_out_7,
       demultiplexer_2_out_8, demultiplexer_2_out_9, demultiplexer_2_out_10, diviser_1_div_0,
       Increment_adder_0, modulo_1_mod_0, movement_1_data_0, multiplier_1_mul_0, not_16_bit_1_not_0,
       or_1_out, or_16_bit_1_or_0, substracter_1_p41, substracter_1_p42, xor_16_bit_1_or_0;

  Demultiplexer #(.Selector_Bits(4), .Bits(16)) demultiplexer_1 (
    .sel({SelectOP_3, SelectOP_2, SelectOP_1, SelectOP_0}),
    .in({Input1_15, Input1_14, Input1_13, Input1_12, Input1_11, Input1_10, Input1_9, Input1_8, Input1_7, Input1_6, Input1_5, Input1_4, Input1_3, Input1_2, Input1_1, Input1_0}),
    .out_1(demultiplexer_1_out_1), .out_2(demultiplexer_1_out_2), .out_3(demultiplexer_1_out_3),
    .out_4(demultiplexer_1_out_4), .out_5(demultiplexer_1_out_5), .out_6(demultiplexer_1_out_6),
    .out_7(demultiplexer_1_out_7), .out_8(demultiplexer_1_out_8), .out_9(demultiplexer_1_out_9),
    .out_10(demultiplexer_1_out_10), .out_11(demultiplexer_1_out_11), .out_12(demultiplexer_1_out_12),
    .out_13(demultiplexer_1_out_13));  // open: out_0, out_14, out_15
  Demultiplexer #(.Selector_Bits(4), .Bits(16)) demultiplexer_2 (
    .sel({SelectOP_3, SelectOP_2, SelectOP_1, SelectOP_0}),
    .in({Input2_15, Input2_14, Input2_13, Input2_12, Input2_11, Input2_10, Input2_9, Input2_8, Input2_7, Input2_6, Input2_5, Input2_4, Input2_3, Input2_2, Input2_1, Input2_0}),
    .out_1(demultiplexer_2_out_1), .out_2(demultiplexer_2_out_2), .out_3(demultiplexer_2_out_3),
    .out_4(demultiplexer_2_out_4), .out_5(demultiplexer_2_out_5), .out_6(demultiplexer_2_out_6),
    .out_7(demultiplexer_2_out_7), .out_8(demultiplexer_2_out_8), .out_9(demultiplexer_2_out_9),
    .out_10(demultiplexer_2_out_10));  // open: out_0, out_11, out_12, out_13, out_14, out_15
  // Adder adder_1: pin names not known; wires that end beside it: demultiplexer_1_out_1[0], demultiplexer_1_out_1[1], demultiplexer_1_out_1[2], demultiplexer_1_out_1[3], demultiplexer_1_out_1[4], demultiplexer_1_out_1[5], demultiplexer_1_out_1[6], demultiplexer_1_out_1[7], demultiplexer_1_out_1[8], demultiplexer_1_out_1[9], demultiplexer_1_out_1[10], demultiplexer_1_out_1[11], demultiplexer_1_out_1[12], demultiplexer_1_out_1[13], demultiplexer_1_out_1[14], demultiplexer_1_out_1[15], demultiplexer_2_out_1[0], demultiplexer_2_out_1[1], demultiplexer_2_out_1[2], demultiplexer_2_out_1[3], demultiplexer_2_out_1[4], demultiplexer_2_out_1[5], demultiplexer_2_out_1[6], demultiplexer_2_out_1[7], adder_1_p25[0], adder_1_p25[1], adder_1_p25[2], adder_1_p25[3], adder_1_p25[4], adder_1_p25[5], adder_1_p25[6], adder_1_p25[7], adder_1_p25[8], adder_1_p25[9], adder_1_p25[10], adder_1_p25[11], adder_1_p25[12], adder_1_p25[13], adder_1_p25[14], adder_1_p25[15], adder_1_p41
  // Substracter substracter_1: pin names not known; wires that end beside it: demultiplexer_2_out_1[8], demultiplexer_2_out_1[9], demultiplexer_2_out_1[10], demultiplexer_2_out_1[11], demultiplexer_2_out_1[12], demultiplexer_2_out_1[13], demultiplexer_2_out_1[14], demultiplexer_2_out_1[15], Carry_in, demultiplexer_1_out_2[0], demultiplexer_1_out_2[1], demultiplexer_1_out_2[2], demultiplexer_1_out_2[3], demultiplexer_1_out_2[4], demultiplexer_1_out_2[5], demultiplexer_1_out_2[6], demultiplexer_1_out_2[7], demultiplexer_1_out_2[8], demultiplexer_1_out_2[9], demultiplexer_1_out_2[10], demultiplexer_1_out_2[11], demultiplexer_1_out_2[12], demultiplexer_1_out_2[13], demultiplexer_1_out_2[14], demultiplexer_1_out_2[15], demultiplexer_2_out_2[0], demultiplexer_2_out_2[1], demultiplexer_2_out_2[2], demultiplexer_2_out_2[3], demultiplexer_2_out_2[4], demultiplexer_2_out_2[5], demultiplexer_2_out_2[6], demultiplexer_2_out_2[7], demultiplexer_2_out_2[8], demultiplexer_2_out_2[9], demultiplexer_2_out_2[10], demultiplexer_2_out_2[11], demultiplexer_2_out_2[12], demultiplexer_2_out_2[13], demultiplexer_2_out_2[14], substracter_1_p41, substracter_1_p42[0], substracter_1_p42[1], substracter_1_p42[2], substracter_1_p42[3], substracter_1_p42[4], substracter_1_p42[5], substracter_1_p42[6], substracter_1_p42[7], substracter_1_p42[8], substracter_1_p42[9], substracter_1_p42[10], substracter_1_p42[11], substracter_1_p42[12], substracter_1_p42[13], substracter_1_p42[14], substracter_1_p42[15], adder_1_p41
  Multiplier multiplier_1 (
    .A_0(demultiplexer_1_out_3[0]), .A_1(demultiplexer_1_out_3[1]), .A_2(demultiplexer_1_out_3[2]),
    .A_3(demultiplexer_1_out_3[3]), .A_4(demultiplexer_1_out_3[4]), .A_5(demultiplexer_1_out_3[5]),
    .A_6(demultiplexer_1_out_3[6]), .A_7(demultiplexer_1_out_3[7]), .A_8(demultiplexer_1_out_3[8]),
    .A_9(demultiplexer_1_out_3[9]), .A_10(demultiplexer_1_out_3[10]), .A_11(demultiplexer_1_out_3[11]),
    .A_12(demultiplexer_1_out_3[12]), .A_13(demultiplexer_1_out_3[13]), .A_14(demultiplexer_1_out_3[14]),
    .A_15(demultiplexer_1_out_3[15]), .B_0(demultiplexer_2_out_3[0]), .B_1(demultiplexer_2_out_3[1]),
    .B_2(demultiplexer_2_out_3[2]), .B_3(demultiplexer_2_out_3[3]), .B_4(demultiplexer_2_out_3[4]),
    .B_5(demultiplexer_2_out_3[5]), .B_6(demultiplexer_2_out_3[6]), .B_7(demultiplexer_2_out_3[7]),
    .B_8(demultiplexer_2_out_3[8]), .B_9(demultiplexer_2_out_3[9]), .B_10(demultiplexer_2_out_3[10]),
    .B_11(demultiplexer_2_out_3[11]), .B_12(demultiplexer_2_out_3[12]), .B_13(demultiplexer_2_out_3[13]),
    .B_14(demultiplexer_2_out_3[14]), .B_15(demultiplexer_2_out_3[15]), .Mul_0(multiplier_1_mul_0[0]),
    .Mul_1(multiplier_1_mul_0[1]), .Mul_2(multiplier_1_mul_0[2]), .Mul_3(multiplier_1_mul_0[3]),
    .Mul_4(multiplier_1_mul_0[4]), .Mul_5(multiplier_1_mul_0[5]), .Mul_6(multiplier_1_mul_0[6]),
    .Mul_7(multiplier_1_mul_0[7]), .Mul_8(multiplier_1_mul_0[8]), .Mul_9(multiplier_1_mul_0[9]),
    .Mul_10(multiplier_1_mul_0[10]), .Mul_11(multiplier_1_mul_0[11]), .Mul_12(multiplier_1_mul_0[12]),
    .Mul_13(multiplier_1_mul_0[13]), .Mul_14(multiplier_1_mul_0[14]), .Mul_15(multiplier_1_mul_0[15]));
  Diviser diviser_1 (
    .A_0(demultiplexer_1_out_4[0]), .A_1(demultiplexer_1_out_4[1]), .A_2(demultiplexer_1_out_4[2]),
    .A_3(demultiplexer_1_out_4[3]), .A_4(demultiplexer_1_out_4[4]), .A_5(demultiplexer_1_out_4[5]),
    .A_6(demultiplexer_1_out_4[6]), .A_7(demultiplexer_1_out_4[7]), .A_8(demultiplexer_1_out_4[8]),
    .A_9(demultiplexer_1_out_4[9]), .A_10(demultiplexer_1_out_4[10]), .A_11(demultiplexer_1_out_4[11]),
    .A_12(demultiplexer_1_out_4[12]), .A_13(demultiplexer_1_out_4[13]), .A_14(demultiplexer_1_out_4[14]),
    .A_15(demultiplexer_1_out_4[15]), .B_0(demultiplexer_2_out_4[0]), .B_1(demultiplexer_2_out_4[1]),
    .B_2(demultiplexer_2_out_4[2]), .B_3(demultiplexer_2_out_4[3]), .B_4(demultiplexer_2_out_4[4]),
    .B_5(demultiplexer_2_out_4[5]), .B_6(demultiplexer_2_out_4[6]), .B_7(demultiplexer_2_out_4[7]),
    .B_8(demultiplexer_2_out_4[8]), .B_9(demultiplexer_2_out_4[9]), .B_10(demultiplexer_2_out_4[10]),
    .B_11(demultiplexer_2_out_4[11]), .B_12(demultiplexer_2_out_4[12]), .B_13(demultiplexer_2_out_4[13]),
    .B_14(demultiplexer_2_out_4[14]), .B_15(demultiplexer_2_out_4[15]), .Div_0(diviser_1_div_0[0]),
    .Div_1(diviser_1_div_0[1]), .Div_2(diviser_1_div_0[2]), .Div_3(diviser_1_div_0[3]),
    .Div_4(diviser_1_div_0[4]), .Div_5(diviser_1_div_0[5]), .Div_6(diviser_1_div_0[6]),
    .Div_7(diviser_1_div_0[7]), .Div_8(diviser_1_div_0[8]), .Div_9(diviser_1_div_0[9]),
    .Div_10(diviser_1_div_0[10]), .Div_11(diviser_1_div_0[11]), .Div_12(diviser_1_div_0[12]),
    .Div_13(diviser_1_div_0[13]), .Div_14(diviser_1_div_0[14]), .Div_15(diviser_1_div_0[15]));
  Modulo modulo_1 (
    .A_0(demultiplexer_1_out_5[0]), .A_1(demultiplexer_1_out_5[1]), .A_2(demultiplexer_1_out_5[2]),
    .A_3(demultiplexer_1_out_5[3]), .A_4(demultiplexer_1_out_5[4]), .A_5(demultiplexer_1_out_5[5]),
    .A_6(demultiplexer_1_out_5[6]), .A_7(demultiplexer_1_out_5[7]), .A_8(demultiplexer_1_out_5[8]),
    .A_9(demultiplexer_1_out_5[9]), .A_10(demultiplexer_1_out_5[10]), .A_11(demultiplexer_1_out_5[11]),
    .A_12(demultiplexer_1_out_5[12]), .A_13(demultiplexer_1_out_5[13]), .A_14(demultiplexer_1_out_5[14]),
    .A_15(demultiplexer_1_out_5[15]), .B_0(demultiplexer_2_out_5[0]), .B_1(demultiplexer_2_out_5[1]),
    .B_2(demultiplexer_2_out_5[2]), .B_3(demultiplexer_2_out_5[3]), .B_4(demultiplexer_2_out_5[4]),
    .B_5(demultiplexer_2_out_5[5]), .B_6(demultiplexer_2_out_5[6]), .B_7(demultiplexer_2_out_5[7]),
    .B_8(demultiplexer_2_out_5[8]), .B_9(demultiplexer_2_out_5[9]), .B_10(demultiplexer_2_out_5[10]),
    .B_11(demultiplexer_2_out_5[11]), .B_12(demultiplexer_2_out_5[12]), .B_13(demultiplexer_2_out_5[13]),
    .B_14(demultiplexer_2_out_5[14]), .B_15(demultiplexer_2_out_5[15]), .Mod_0(modulo_1_mod_0[0]),
    .Mod_1(modulo_1_mod_0[1]), .Mod_2(modulo_1_mod_0[2]), .Mod_3(modulo_1_mod_0[3]),
    .Mod_4(modulo_1_mod_0[4]), .Mod_5(modulo_1_mod_0[5]), .Mod_6(modulo_1_mod_0[6]),
    .Mod_7(modulo_1_mod_0[7]), .Mod_8(modulo_1_mod_0[8]), .Mod_9(modulo_1_mod_0[9]),
    .Mod_10(modulo_1_mod_0[10]), .Mod_11(modulo_1_mod_0[11]), .Mod_12(modulo_1_mod_0[12]),
    .Mod_13(modulo_1_mod_0[13]), .Mod_14(modulo_1_mod_0[14]), .Mod_15(modulo_1_mod_0[15]));
  movement movement_1 (
    .A_0(demultiplexer_1_out_6[0]), .A_1(demultiplexer_1_out_6[1]), .A_2(demultiplexer_1_out_6[2]),
    .A_3(demultiplexer_1_out_6[3]), .A_4(demultiplexer_1_out_6[4]), .A_5(demultiplexer_1_out_6[5]),
    .A_6(demultiplexer_1_out_6[6]), .A_7(demultiplexer_1_out_6[7]), .A_8(demultiplexer_1_out_6[8]),
    .A_9(demultiplexer_1_out_6[9]), .A_10(demultiplexer_1_out_6[10]), .A_11(demultiplexer_1_out_6[11]),
    .A_12(demultiplexer_1_out_6[12]), .A_13(demultiplexer_1_out_6[13]), .A_14(demultiplexer_1_out_6[14]),
    .A_15(demultiplexer_1_out_6[15]), .B_0(demultiplexer_2_out_6[0]), .B_1(demultiplexer_2_out_6[1]),
    .B_2(demultiplexer_2_out_6[2]), .B_3(demultiplexer_2_out_6[3]), .B_4(demultiplexer_2_out_6[4]),
    .B_5(demultiplexer_2_out_6[5]), .B_6(demultiplexer_2_out_6[6]), .B_7(demultiplexer_2_out_6[7]),
    .B_8(demultiplexer_2_out_6[8]), .B_9(demultiplexer_2_out_6[9]), .B_10(demultiplexer_2_out_6[10]),
    .B_11(demultiplexer_2_out_6[11]), .B_12(demultiplexer_2_out_6[12]), .B_13(demultiplexer_2_out_6[13]),
    .B_14(demultiplexer_2_out_6[14]), .B_15(demultiplexer_2_out_6[15]), .Data_0(movement_1_data_0[0]),
    .Data_1(movement_1_data_0[1]), .Data_2(movement_1_data_0[2]), .Data_3(movement_1_data_0[3]),
    .Data_4(movement_1_data_0[4]), .Data_5(movement_1_data_0[5]), .Data_6(movement_1_data_0[6]),
    .Data_7(movement_1_data_0[7]), .Data_8(movement_1_data_0[8]), .Data_9(movement_1_data_0[9]),
    .Data_10(movement_1_data_0[10]), .Data_11(movement_1_data_0[11]), .Data_12(movement_1_data_0[12]),
    .Data_13(movement_1_data_0[13]), .Data_14(movement_1_data_0[14]), .Data_15(movement_1_data_0[15]),
    .Addr_0(Addr_0), .Addr_1(Addr_1), .Addr_2(Addr_2), .Addr_3(Addr_3), .Addr_4(Addr_4), .Addr_5(Addr_5),
    .Addr_6(Addr_6), .Addr_7(Addr_7), .Addr_8(Addr_8), .Addr_9(Addr_9), .Addr_10(Addr_10), .Addr_11(Addr_11),
    .Addr_12(Addr_12), .Addr_13(Addr_13), .Addr_14(Addr_14), .Addr_15(Addr_15));
  And_16_bit and_16_bit_1 (
    .A_0(demultiplexer_1_out_7[0]), .A_1(demultiplexer_1_out_7[1]), .A_2(demultiplexer_1_out_7[2]),
    .A_3(demultiplexer_1_out_7[3]), .A_4(demultiplexer_1_out_7[4]), .A_5(demultiplexer_1_out_7[5]),
    .A_6(demultiplexer_1_out_7[6]), .A_7(demultiplexer_1_out_7[7]), .A_8(demultiplexer_1_out_7[8]),
    .A_9(demultiplexer_1_out_7[9]), .A_10(demultiplexer_1_out_7[10]), .A_11(demultiplexer_1_out_7[11]),
    .A_12(demultiplexer_1_out_7[12]), .A_13(demultiplexer_1_out_7[13]), .A_14(demultiplexer_1_out_7[14]),
    .A_15(demultiplexer_1_out_7[15]), .B_0(demultiplexer_2_out_7[0]), .B_1(demultiplexer_2_out_7[1]),
    .B_2(demultiplexer_2_out_7[2]), .B_3(demultiplexer_2_out_7[3]), .B_4(demultiplexer_2_out_7[4]),
    .B_5(demultiplexer_2_out_7[5]), .B_6(demultiplexer_2_out_7[6]), .B_7(demultiplexer_2_out_7[7]),
    .B_8(demultiplexer_2_out_7[8]), .B_9(demultiplexer_2_out_7[9]), .B_10(demultiplexer_2_out_7[10]),
    .B_11(demultiplexer_2_out_7[11]), .B_12(demultiplexer_2_out_7[12]), .B_13(demultiplexer_2_out_7[13]),
    .B_14(demultiplexer_2_out_7[14]), .B_15(demultiplexer_2_out_7[15]), .And_0(and_16_bit_1_and_0[0]),
    .And_1(and_16_bit_1_and_0[1]), .And_2(and_16_bit_1_and_0[2]), .And_3(and_16_bit_1_and_0[3]),
    .And_4(and_16_bit_1_and_0[4]), .And_5(and_16_bit_1_and_0[5]), .And_6(and_16_bit_1_and_0[6]),
    .And_7(and_16_bit_1_and_0[7]), .And_8(and_16_bit_1_and_0[8]), .And_9(and_16_bit_1_and_0[9]),
    .And_10(and_16_bit_1_and_0[10]), .And_11(and_16_bit_1_and_0[11]), .And_12(and_16_bit_1_and_0[12]),
    .And_13(and_16_bit_1_and_0[13]), .And_14(and_16_bit_1_and_0[14]), .And_15(and_16_bit_1_and_0[15]));
  Or_16_bit or_16_bit_1 (
    .A_0(demultiplexer_1_out_8[0]), .A_1(demultiplexer_1_out_8[1]), .A_2(demultiplexer_1_out_8[2]),
    .A_3(demultiplexer_1_out_8[3]), .A_4(demultiplexer_1_out_8[4]), .A_5(demultiplexer_1_out_8[5]),
    .A_6(demultiplexer_1_out_8[6]), .A_7(demultiplexer_1_out_8[7]), .A_8(demultiplexer_1_out_8[8]),
    .A_9(demultiplexer_1_out_8[9]), .A_10(demultiplexer_1_out_8[10]), .A_11(demultiplexer_1_out_8[11]),
    .A_12(demultiplexer_1_out_8[12]), .A_13(demultiplexer_1_out_8[13]), .A_14(demultiplexer_1_out_8[14]),
    .A_15(demultiplexer_1_out_8[15]), .B_0(demultiplexer_2_out_8[0]), .B_1(demultiplexer_2_out_8[1]),
    .B_2(demultiplexer_2_out_8[2]), .B_3(demultiplexer_2_out_8[3]), .B_4(demultiplexer_2_out_8[4]),
    .B_5(demultiplexer_2_out_8[5]), .B_6(demultiplexer_2_out_8[6]), .B_7(demultiplexer_2_out_8[7]),
    .B_8(demultiplexer_2_out_8[8]), .B_9(demultiplexer_2_out_8[9]), .B_10(demultiplexer_2_out_8[10]),
    .B_11(demultiplexer_2_out_8[11]), .B_12(demultiplexer_2_out_8[12]), .B_13(demultiplexer_2_out_8[13]),
    .B_14(demultiplexer_2_out_8[14]), .B_15(demultiplexer_2_out_8[15]), .Or_0(or_16_bit_1_or_0[0]),
    .Or_1(or_16_bit_1_or_0[1]), .Or_2(or_16_bit_1_or_0[2]), .Or_3(or_16_bit_1_or_0[3]),
    .Or_4(or_16_bit_1_or_0[4]), .Or_5(or_16_bit_1_or_0[5]), .Or_6(or_16_bit_1_or_0[6]),
    .Or_7(or_16_bit_1_or_0[7]), .Or_8(or_16_bit_1_or_0[8]), .Or_9(or_16_bit_1_or_0[9]),
    .Or_10(or_16_bit_1_or_0[10]), .Or_11(or_16_bit_1_or_0[11]), .Or_12(or_16_bit_1_or_0[12]),
    .Or_13(or_16_bit_1_or_0[13]), .Or_14(or_16_bit_1_or_0[14]), .Or_15(or_16_bit_1_or_0[15]));
  xor_16_bit xor_16_bit_1 (
    .A_0(demultiplexer_1_out_9[0]), .A_1(demultiplexer_1_out_9[1]), .A_2(demultiplexer_1_out_9[2]),
    .A_3(demultiplexer_1_out_9[3]), .A_4(demultiplexer_1_out_9[4]), .A_5(demultiplexer_1_out_9[5]),
    .A_6(demultiplexer_1_out_9[6]), .A_7(demultiplexer_1_out_9[7]), .A_8(demultiplexer_1_out_9[8]),
    .A_9(demultiplexer_1_out_9[9]), .A_10(demultiplexer_1_out_9[10]), .A_11(demultiplexer_1_out_9[11]),
    .A_12(demultiplexer_1_out_9[12]), .A_13(demultiplexer_1_out_9[13]), .A_14(demultiplexer_1_out_9[14]),
    .A_15(demultiplexer_1_out_9[15]), .B_0(demultiplexer_2_out_9[0]), .B_1(demultiplexer_2_out_9[1]),
    .B_2(demultiplexer_2_out_9[2]), .B_3(demultiplexer_2_out_9[3]), .B_4(demultiplexer_2_out_9[4]),
    .B_5(demultiplexer_2_out_9[5]), .B_6(demultiplexer_2_out_9[6]), .B_7(demultiplexer_2_out_9[7]),
    .B_8(demultiplexer_2_out_9[8]), .B_9(demultiplexer_2_out_9[9]), .B_10(demultiplexer_2_out_9[10]),
    .B_11(demultiplexer_2_out_9[11]), .B_12(demultiplexer_2_out_9[12]), .B_13(demultiplexer_2_out_9[13]),
    .B_14(demultiplexer_2_out_9[14]), .B_15(demultiplexer_2_out_9[15]), .Or_0(xor_16_bit_1_or_0[0]),
    .Or_1(xor_16_bit_1_or_0[1]), .Or_2(xor_16_bit_1_or_0[2]), .Or_3(xor_16_bit_1_or_0[3]),
    .Or_4(xor_16_bit_1_or_0[4]), .Or_5(xor_16_bit_1_or_0[5]), .Or_6(xor_16_bit_1_or_0[6]),
    .Or_7(xor_16_bit_1_or_0[7]), .Or_8(xor_16_bit_1_or_0[8]), .Or_9(xor_16_bit_1_or_0[9]),
    .Or_10(xor_16_bit_1_or_0[10]), .Or_11(xor_16_bit_1_or_0[11]), .Or_12(xor_16_bit_1_or_0[12]),
    .Or_13(xor_16_bit_1_or_0[13]), .Or_14(xor_16_bit_1_or_0[14]), .Or_15(xor_16_bit_1_or_0[15]));
  not_16_bit not_16_bit_1 (
    .A_0(demultiplexer_1_out_10[0]), .A_1(demultiplexer_1_out_10[1]), .A_2(demultiplexer_1_out_10[2]),
    .A_3(demultiplexer_1_out_10[3]), .A_4(demultiplexer_1_out_10[4]), .A_5(demultiplexer_1_out_10[5]),
    .A_6(demultiplexer_1_out_10[6]), .A_7(demultiplexer_1_out_10[7]), .A_8(demultiplexer_1_out_10[8]),
    .A_9(demultiplexer_1_out_10[9]), .A_10(demultiplexer_1_out_10[10]), .A_11(demultiplexer_1_out_10[11]),
    .A_12(demultiplexer_1_out_10[12]), .A_13(demultiplexer_1_out_10[13]), .A_14(demultiplexer_1_out_10[14]),
    .A_15(demultiplexer_1_out_10[15]), .Not_0(not_16_bit_1_not_0[0]), .Not_1(not_16_bit_1_not_0[1]),
    .Not_2(not_16_bit_1_not_0[2]), .Not_3(not_16_bit_1_not_0[3]), .Not_4(not_16_bit_1_not_0[4]),
    .Not_5(not_16_bit_1_not_0[5]), .Not_6(not_16_bit_1_not_0[6]), .Not_7(not_16_bit_1_not_0[7]),
    .Not_8(not_16_bit_1_not_0[8]), .Not_9(not_16_bit_1_not_0[9]), .Not_10(not_16_bit_1_not_0[10]),
    .Not_11(not_16_bit_1_not_0[11]), .Not_12(not_16_bit_1_not_0[12]), .Not_13(not_16_bit_1_not_0[13]),
    .Not_14(not_16_bit_1_not_0[14]), .Not_15(not_16_bit_1_not_0[15]));
  // Substracter Compare: pin names not known; wires that end beside it: demultiplexer_1_out_11[0], demultiplexer_1_out_11[1], demultiplexer_1_out_11[2], demultiplexer_1_out_11[3], demultiplexer_1_out_11[4], demultiplexer_1_out_11[5], demultiplexer_1_out_11[6], demultiplexer_1_out_11[7], demultiplexer_1_out_11[8], demultiplexer_1_out_11[9], demultiplexer_1_out_11[10], demultiplexer_1_out_11[11], demultiplexer_1_out_11[12], demultiplexer_1_out_11[13], demultiplexer_1_out_11[14], demultiplexer_1_out_11[15], demultiplexer_2_out_10[0], demultiplexer_2_out_10[1], demultiplexer_2_out_10[2], demultiplexer_2_out_10[3], demultiplexer_2_out_10[4], demultiplexer_2_out_10[5], demultiplexer_2_out_10[6], demultiplexer_2_out_10[7], demultiplexer_2_out_10[8], demultiplexer_2_out_10[9], demultiplexer_2_out_10[10], demultiplexer_2_out_10[11], demultiplexer_2_out_10[12], demultiplexer_2_out_10[13], demultiplexer_2_out_10[14], Compare_p32, Compare_p33, Compare_p34, Compare_p35, Compare_p36, Compare_p37, Compare_p38, Compare_p39, Compare_p40, Compare_p41, Compare_p42, Compare_p43, Compare_p44, Compare_p45, Compare_p46, Compare_p47, Compare_p48, Compare_p49
  Adder Increment (
    .A_0(demultiplexer_1_out_12[0]), .A_1(demultiplexer_1_out_12[1]), .A_2(demultiplexer_1_out_12[2]),
    .A_3(demultiplexer_1_out_12[3]), .A_4(demultiplexer_1_out_12[4]), .A_5(demultiplexer_1_out_12[5]),
    .A_6(demultiplexer_1_out_12[6]), .A_7(demultiplexer_1_out_12[7]), .A_8(demultiplexer_1_out_12[8]),
    .A_9(demultiplexer_1_out_12[9]), .A_10(demultiplexer_1_out_12[10]), .A_11(demultiplexer_1_out_12[11]),
    .A_12(demultiplexer_1_out_12[12]), .A_13(demultiplexer_1_out_12[13]), .A_14(demultiplexer_1_out_12[14]),
    .A_15(demultiplexer_1_out_12[15]), .B_0(1'b1), .B_1(1'b0), .B_2(1'b0), .B_3(1'b0), .B_4(1'b0),
    .B_5(1'b0), .B_6(1'b0), .B_7(1'b0), .B_8(1'b0), .B_9(1'b0), .B_10(1'b0), .B_11(1'b0), .B_12(1'b0),
    .B_13(1'b0), .B_14(1'b0), .B_15(1'b0), .Carry_in(Carry_in), .Adder_0(Increment_adder_0[0]),
    .Adder_1(Increment_adder_0[1]), .Adder_2(Increment_adder_0[2]), .Adder_3(Increment_adder_0[3]),
    .Adder_4(Increment_adder_0[4]), .Adder_5(Increment_adder_0[5]), .Adder_6(Increment_adder_0[6]),
    .Adder_7(Increment_adder_0[7]), .Adder_8(Increment_adder_0[8]), .Adder_9(Increment_adder_0[9]),
    .Adder_10(Increment_adder_0[10]), .Adder_11(Increment_adder_0[11]), .Adder_12(Increment_adder_0[12]),
    .Adder_13(Increment_adder_0[13]), .Adder_14(Increment_adder_0[14]), .Adder_15(Increment_adder_0[15]));  // open: Carry_out
  Substracter Decrement (
    .A_0(demultiplexer_1_out_13[0]), .A_1(demultiplexer_1_out_13[1]), .A_2(demultiplexer_1_out_13[2]),
    .A_3(demultiplexer_1_out_13[3]), .A_4(demultiplexer_1_out_13[4]), .A_5(demultiplexer_1_out_13[5]),
    .A_6(demultiplexer_1_out_13[6]), .A_7(demultiplexer_1_out_13[7]), .A_8(demultiplexer_1_out_13[8]),
    .A_9(demultiplexer_1_out_13[9]), .A_10(demultiplexer_1_out_13[10]), .A_11(demultiplexer_1_out_13[11]),
    .A_12(demultiplexer_1_out_13[12]), .A_13(demultiplexer_1_out_13[13]), .A_14(demultiplexer_1_out_13[14]),
    .A_15(demultiplexer_1_out_13[15]), .B_0(1'b1), .B_1(1'b0), .B_2(1'b0), .B_3(1'b0), .B_4(1'b0),
    .B_5(1'b0), .B_6(1'b0), .B_7(1'b0), .B_8(1'b0), .B_9(1'b0), .B_10(1'b0), .B_11(1'b0), .B_12(1'b0),
    .B_13(1'b0), .B_14(1'b0), .B_15(1'b0), .Carry_in(Carry_in), .Sub_0(Decrement_sub_0[0]),
    .Sub_1(Decrement_sub_0[1]), .Sub_2(Decrement_sub_0[2]), .Sub_3(Decrement_sub_0[3]),
    .Sub_4(Decrement_sub_0[4]), .Sub_5(Decrement_sub_0[5]), .Sub_6(Decrement_sub_0[6]),
    .Sub_7(Decrement_sub_0[7]), .Sub_8(Decrement_sub_0[8]), .Sub_9(Decrement_sub_0[9]),
    .Sub_10(Decrement_sub_0[10]), .Sub_11(Decrement_sub_0[11]), .Sub_12(Decrement_sub_0[12]),
    .Sub_13(Decrement_sub_0[13]), .Sub_14(Decrement_sub_0[14]), .Sub_15(Decrement_sub_0[15]));  // open: Carry_out
  not not_1 (not_1_out, Compare_p32[0]);
  Multiplexer #(.Selector_Bits(4), .Bits(16)) multiplexer_1 (
    .sel({SelectOP_3, SelectOP_2, SelectOP_1, SelectOP_0}), .in_1(adder_1_p25), .in_2(substracter_1_p42),
    .in_3(multiplier_1_mul_0), .in_4(diviser_1_div_0), .in_5(modulo_1_mod_0), .in_6(movement_1_data_0),
    .in_7(and_16_bit_1_and_0), .in_8(or_16_bit_1_or_0), .in_9(xor_16_bit_1_or_0), .in_10(not_16_bit_1_not_0),
    .in_11(Increment_adder_0), .in_12(Decrement_sub_0),
    .out({Output_15, Output_14, Output_13, Output_12, Output_11, Output_10, Output_9, Output_8, Output_7, Output_6, Output_5, Output_4, Output_3, Output_2, Output_1, Output_0}));  // open: in_0, in_13, in_14, in_15
  Multiplexer #(.Selector_Bits(4), .Bits(16)) multiplexer_2 (
    .sel({SelectOP_3, SelectOP_2, SelectOP_1, SelectOP_0}), .in_1(adder_1_p41), .in_11(Compare_p32),
    .out(CarryOut));  // open: in_0, in_2, in_3, in_4, in_5, in_6, in_7, in_8, in_9, in_10, in_12, in_13, in_14, in_15
  Multiplexer #(.Selector_Bits(4), .Bits(16)) multiplexer_3 (
    .sel({SelectOP_3, SelectOP_2, SelectOP_1, SelectOP_0}), .in_2(adder_1_p41), .in_11(Compare_p49),
    .out(Zero));  // open: in_0, in_1, in_3, in_4, in_5, in_6, in_7, in_8, in_9, in_10, in_12, in_13, in_14, in_15
  Multiplexer #(.Selector_Bits(4), .Bits(16)) multiplexer_4 (
    .sel({SelectOP_3, SelectOP_2, SelectOP_1, SelectOP_0}), .in_2(substracter_1_p41), .in_11(Compare_p32),
    .out(Negative));  // open: in_0, in_1, in_3, in_4, in_5, in_6, in_7, in_8, in_9, in_10, in_12, in_13, in_14, in_15
  Multiplexer #(.Selector_Bits(4), .Bits(16)) multiplexer_5 (
    .sel({SelectOP_3, SelectOP_2, SelectOP_1, SelectOP_0}), .in_1(adder_1_p41), .in_11(or_1_out),
    .out(Overflow));  // open: in_0, in_2, in_3, in_4, in_5, in_6, in_7, in_8, in_9, in_10, in_12, in_13, in_14, in_15
  or or_1 (or_1_out[0], not_1_out, Compare_p33, Compare_p34, Compare_p35, Compare_p36, Compare_p37, Compare_p38, Compare_p39, Compare_p40, Compare_p41, Compare_p42, Compare_p43, Compare_p44, Compare_p45, Compare_p46, Compare_p47, Compare_p48);
  // Pins of 1 and 16 bits meet at CarryOut
  // Pins of 1 and 16 bits meet at Zero
  // Pins of 1 and 16 bits meet at Negative
  // Pins of 1 and 16 bits meet at Overflow
  // Pins of 1 and 16 bits meet at Compare_p32
  // Pins of 1 and 16 bits meet at or_1_out
endmodule
