// Digital circuit Adder.dig as structural Verilog
module Adder (
  input  A_0,
  input  A_1,
  input  A_2,
  input  A_3,
  input  A_4,
  input  A_5,
  input  A_6,
  input  A_7,
  input  A_8,
  input  A_9,
  input  A_10,
  input  A_11,
  input  A_12,
  input  A_13,
  input  A_14,
  input  A_15,
  input  B_0,
  input  B_1,
  input  B_2,
  input  B_3,
  input  B_4,
  input  B_5,
  input  B_6,
  input  B_7,
  input  B_8,
  input  B_9,
  input  B_10,
  input  B_11,
  input  B_12,
  input  B_13,
  input  B_14,
  input  B_15,
  input  Carry_in,
  output Adder_0,
  output Adder_1,
  output Adder_2,
  output Adder_3,
  output Adder_4,
  output Adder_5,
  output Adder_6,
  output Adder_7,
  output Adder_8,
  output Adder_9,
  output Adder_10,
  output Adder_11,
  output Adder_12,
  output Adder_13,
  output Adder_14,
  output Adder_15,
  output Carry_out
);

  wire add_1_c_o, add_2_c_o, add_3_c_o, add_4_c_o, add_5_c_o, add_6_c_o, add_7_c_o, add_8_c_o, add_9_c_o,
       add_10_c_o, add_11_c_o, add_12_c_o, add_13_c_o, add_14_c_o, add_15_c_o;

  Add add_1 (.a(A_0), .b(B_0), .c_i(Carry_in), .s(Adder_0), .c_o(add_1_c_o));
  Add add_2 (.a(A_1), .b(B_1), .c_i(add_1_c_o), .s(Adder_1), .c_o(add_2_c_o));
  Add add_3 (.a(A_2), .b(B_2), .c_i(add_2_c_o), .s(Adder_2), .c_o(add_3_c_o));
  Add add_4 (.a(A_3), .b(B_3), .c_i(add_3_c_o), .s(Adder_3), .c_o(add_4_c_o));
  Add add_5 (.a(A_4), .b(B_4), .c_i(add_4_c_o), .s(Adder_4), .c_o(add_5_c_o));
  Add add_6 (.a(A_5), .b(B_5), .c_i(add_5_c_o), .s(Adder_5), .c_o(add_6_c_o));
  Add add_7 (.a(A_6), .b(B_6), .c_i(add_6_c_o), .s(Adder_6), .c_o(add_7_c_o));
  Add add_8 (.a(A_7), .b(B_7), .c_i(add_7_c_o), .s(Adder_7), .c_o(add_8_c_o));
  Add add_9 (.a(A_8), .b(B_8), .c_i(add_8_c_o), .s(Adder_8), .c_o(add_9_c_o));
  Add add_10 (.a(A_9), .b(B_9), .c_i(add_9_c_o), .s(Adder_9), .c_o(add_10_c_o));
  Add add_11 (.a(A_10), .b(B_10), .c_i(add_10_c_o), .s(Adder_10), .c_o(add_11_c_o));
  Add add_12 (.a(A_11), .b(B_11), .c_i(add_11_c_o), .s(Adder_11), .c_o(add_12_c_o));
  Add add_13 (.a(A_12), .b(B_12), .c_i(add_12_c_o), .s(Adder_12), .c_o(add_13_c_o));
  Add add_14 (.a(A_13), .b(B_13), .c_i(add_13_c_o), .s(Adder_13), .c_o(add_14_c_o));
  Add add_15 (.a(A_14), .b(B_14), .c_i(add_14_c_o), .s(Adder_14), .c_o(add_15_c_o));
  Add add_16 (.a(A_15), .b(B_15), .c_i(add_15_c_o), .s(Adder_15), .c_o(Carry_out));
endmodule
