// Digital circuit And_16_bit.dig as structural Verilog
module And_16_bit (
  input  A_0,
  input  A_1,
  input  A_2,
  input  A_3,
  input  A_4,
  input  A_5,
  input  A_6,
  input  A_7,
  input  A_8,
  input  A_9,
  input  A_10,
  input  A_11,
  input  A_12,
  input  A_13,
  input  A_14,
  input  A_15,
  input  B_0,
  input  B_1,
  input  B_2,
  input  B_3,
  input  B_4,
  input  B_5,
  input  B_6,
  input  B_7,
  input  B_8,
  input  B_9,
  input  B_10,
  input  B_11,
  input  B_12,
  input  B_13,
  input  B_14,
  input  B_15,
  output And_0,
  output And_1,
  output And_2,
  output And_3,
  output And_4,
  output And_5,
  output And_6,
  output And_7,
  output And_8,
  output And_9,
  output And_10,
  output And_11,
  output And_12,
  output And_13,
  output And_14,
  output And_15
);

  and u_and_1 (And_0, A_0, B_0);
  and u_and_2 (And_1, A_1, B_1);
  and u_and_3 (And_2, A_2, B_2);
  and u_and_4 (And_3, A_3, B_3);
  and u_and_5 (And_4, A_4, B_4);
  and u_and_6 (And_5, A_5, B_5);
  and u_and_7 (And_6, A_6, B_6);
  and u_and_8 (And_7, A_7, B_7);
  and u_and_9 (And_8, A_8, B_8);
  and u_and_10 (And_9, A_9, B_9);
  and u_and_11 (And_10, A_10, B_10);
  and u_and_12 (And_11, A_11, B_11);
  and u_and_13 (And_12, A_12, B_12);
  and u_and_14 (And_13, A_13, B_13);
  and u_and_15 (And_14, A_14, B_14);
  and and_16 (And_15, A_15, B_15);
endmodule
