// Digital circuit Computing_Sistem.dig as structural Verilog
module Computing_Sistem (
  input  Emergency_3,
  input  Flags3_0,
  input  Flags3_1,
  input  Flags3_2,
  input  Emergency_2,
  input  Flags2_0,
  input  Flags2_1,
  input  Flags2_2,
  input  Emergency_1,
  input  Flags1_0,
  input  Flags1_1,
  input  Flags1_2,
  input  Emergency_0,
  input  Flags0_0,
  input  Flags0_1,
  input  Flags0_2,
  input  SenzorMasina1_0,
  input  SenzorMasina1_1,
  input  SenzorMasina1_2,
  input  SenzorMasina2_0,
  input  SenzorMasina2_1,
  input  SenzorMasina2_2,
  input  SenzorMasina3_0,
  input  SenzorMasina3_1,
  input  SenzorMasina3_2,
  input  SenzorMasina0_0,
  input  SenzorMasina0_1,
  input  SenzorMasina0_2,
  input  Frequency
);

  wire _8registers_encoded_1_output_0, _8registers_encoded_1_output_1, _8registers_encoded_1_output_2,
       _8registers_encoded_1_output_3, _8registers_encoded_1_output_4, _8registers_encoded_1_output_5,
       _8registers_encoded_1_output_6, _8registers_encoded_1_output_7, _8registers_encoded_1_output_8,
       _8registers_encoded_1_output_9, _8registers_encoded_1_output_10, _8registers_encoded_1_output_11,
       _8registers_encoded_1_output_12, _8registers_encoded_1_output_13, _8registers_encoded_1_output_14,
       _8registers_encoded_1_output_15, _16bit_mux_2to1_1_output_0, _16bit_mux_2to1_1_output_1,
       _16bit_mux_2to1_1_output_2, _16bit_mux_2to1_1_output_3, _16bit_mux_2to1_1_output_4,
       _16bit_mux_2to1_1_output_5, _16bit_mux_2to1_1_output_6, _16bit_mux_2to1_1_output_7,
       _16bit_mux_2to1_1_output_8, _16bit_mux_2to1_1_output_9, _16bit_mux_2to1_1_output_10,
       _16bit_mux_2to1_1_output_11, _16bit_mux_2to1_1_output_12, _16bit_mux_2to1_1_output_13,
       _16bit_mux_2to1_1_output_14, _16bit_mux_2to1_1_output_15, _16bit_mux_2to1_2_output_0,
       _16bit_mux_2to1_2_output_1, _16bit_mux_2to1_2_output_2, _16bit_mux_2to1_2_output_3,
       _16bit_mux_2to1_2_output_4, _16bit_mux_2to1_2_output_5, _16bit_mux_2to1_2_output_6,
       _16bit_mux_2to1_2_output_7, _16bit_mux_2to1_2_output_8, _16bit_mux_2to1_2_output_9,
       _16bit_mux_2to1_2_output_10, _16bit_mux_2to1_2_output_11, _16bit_mux_2to1_2_output_12,
       _16bit_mux_2to1_2_output_13, _16bit_mux_2to1_2_output_14, _16bit_mux_2to1_2_output_15,
       _16bit_mux_2to1_3_output_0, _16bit_mux_2to1_3_output_1, _16bit_mux_2to1_3_output_2,
       _16bit_mux_2to1_3_output_3, _16bit_mux_2to1_3_output_4, _16bit_mux_2to1_3_output_5,
       _16bit_mux_2to1_3_output_6, _16bit_mux_2to1_3_output_7, _16bit_mux_2to1_3_output_8,
       _16bit_mux_2to1_3_output_9, _16bit_mux_2to1_3_output_10, _16bit_mux_2to1_3_output_11,
       _16bit_mux_2to1_3_output_12, _16bit_mux_2to1_3_output_13, _16bit_mux_2to1_3_output_14,
       _16bit_mux_2to1_3_output_15, _16bit_mux_2to1_4_output_0, _16bit_mux_2to1_4_output_1,
       _16bit_mux_2to1_4_output_2, _16bit_mux_2to1_4_output_3, _16bit_mux_2to1_4_output_4,
       _16bit_mux_2to1_4_output_5, _16bit_mux_2to1_4_output_6, _16bit_mux_2to1_4_output_7,
       _16bit_mux_2to1_4_output_8, _16bit_mux_2to1_4_output_9, _16bit_mux_2to1_4_output_10,
       _16bit_mux_2to1_4_output_11, _16bit_mux_2to1_4_output_12, _16bit_mux_2to1_4_output_13,
       _16bit_mux_2to1_4_output_14, _16bit_mux_2to1_4_output_15, _16bit_mux_2to1_5_output_0,
       _16bit_mux_2to1_5_output_1, _16bit_mux_2to1_5_output_2, _16bit_mux_2to1_5_output_3,
       _16bit_mux_2to1_5_output_4, _16bit_mux_2to1_5_output_5, _16bit_mux_2to1_5_output_6,
       _16bit_mux_2to1_5_output_7, _16bit_mux_2to1_5_output_8, _16bit_mux_2to1_5_output_9,
       _16bit_mux_2to1_5_output_10, _16bit_mux_2to1_5_output_11, _16bit_mux_2to1_5_output_12,
       _16bit_mux_2to1_5_output_13, _16bit_mux_2to1_5_output_14, _16bit_mux_2to1_5_output_15, add_1_c_o,
       add_6_c_o, add_6_s, add_7_c_o, add_7_s, add_8_s, add_9_c_o, add_11_c_o, add_13_c_o, add_16_c_o,
       adder_1_adder_0, adder_1_adder_1, adder_1_adder_2, adder_1_adder_3, adder_1_adder_4, adder_1_adder_5,
       adder_1_adder_6, adder_1_adder_7, adder_1_adder_8, adder_1_adder_9, adder_1_adder_10,
       adder_1_adder_11, adder_1_adder_12, adder_1_adder_13, adder_1_adder_14, adder_1_adder_15, ALU_addr_0,
       ALU_addr_1, ALU_addr_2, ALU_addr_3, ALU_addr_4, ALU_addr_5, ALU_addr_6, ALU_addr_7, ALU_addr_8,
       ALU_addr_9, ALU_addr_10, ALU_addr_11, ALU_addr_12, ALU_addr_13, ALU_addr_14, ALU_addr_15,
       ALU_carryout, ALU_negative, ALU_output_0, ALU_output_1, ALU_output_2, ALU_output_3, ALU_output_4,
       ALU_output_5, ALU_output_6, ALU_output_7, ALU_output_8, ALU_output_9, ALU_output_10, ALU_output_11,
       ALU_output_12, ALU_output_13, ALU_output_14, ALU_output_15, ALU_overflow, and_1_out, and_2_out,
       and_3_out, and_4_out, and_5_out, and_6_out, and_7_out, and_8_out, and_9_out, and_10_out, and_11_out,
       and_12_out, and_13_out, and_14_out, and_15_out, and_16_out, and_17_out, and_18_out, and_19_out,
       and_20_out, Cold_q, decoder_1_out_0, decoder_1_out_1, decoder_1_out_2, decoder_1_out_3,
       decoder_2_out_0, decoder_2_out_1, decoder_2_out_2, decoder_2_out_3, decoder_3_out_0, decoder_3_out_1,
       decoder_3_out_2, decoder_3_out_3, decoder_4_out_0, decoder_4_out_1, decoder_4_out_2, decoder_4_out_3,
       decoder_5_out_0, decoder_5_out_1, decoder_5_out_2, decoder_5_out_3, enable_counter_0_q,
       enable_counter_1_q, enable_counter_2_q, enable_counter_3_q, ID_branchingcond, ID_c_0, ID_c_1, ID_c_2,
       ID_c_3, ID_c_4, ID_c_5, ID_c_6, ID_c_7, ID_c_8, ID_c_9, ID_c_10, ID_c_11, ID_c_13, ID_c_14, ID_c_15,
       ID_c_16, ID_c_17, ID_c_18, ID_c_19, ID_c_20, ID_c_21, ID_c_22, ID_c_23, ID_c_24, ID_nextaddr_0,
       ID_nextaddr_1, ID_nextaddr_2, ID_nextaddr_3, ID_nextaddr_4, ID_nextaddr_5, IR_q_0, IR_q_1, IR_q_2,
       IR_q_3, IR_q_4, IR_q_5, IR_q_6, IR_q_7, IR_q_8, IR_q_9, IR_q_10, IR_q_11, IR_q_12, IR_q_13, IR_q_14,
       IR_q_15, IR_q_16, IR_q_17, IR_q_18, IR_q_19, IR_q_20, IR_q_21, Memory_outdata_0, Memory_outdata_1,
       Memory_outdata_2, Memory_outdata_3, Memory_outdata_4, Memory_outdata_5, Memory_outdata_6,
       Memory_outdata_7, Memory_outdata_8, Memory_outdata_9, Memory_outdata_10, Memory_outdata_11,
       Memory_outdata_12, Memory_outdata_13, Memory_outdata_14, Memory_outdata_15, multiplexer_8_out,
       multiplexer_9_out, multiplexer_10_out, multiplexer_11_out, multiplexer_12_out, multiplexer_13_out,
       multiplexer_14_out, multiplexer_15_out, multiplexer_16_out, multiplexer_17_out, multiplexer_18_out,
       multiplexer_19_out, multiplexer_20_out, multiplexer_21_out, multiplexer_22_out, multiplexer_23_out,
       nand_1_out, not_1_out, not_2_out, operationselect_1_selop_0, operationselect_1_selop_1,
       operationselect_1_selop_2, operationselect_1_selop_3, or_1_out, or_2_out, or_3_out, or_4_out,
       or_5_out, or_6_out, or_7_out, or_8_out, or_9_out, or_10_out, or_11_out, or_12_out, or_13_out,
       or_14_out, or_15_out, PC_pc_0, PC_pc_1, PC_pc_2, PC_pc_3, PC_pc_4, PC_pc_5, PC_pc_6, PC_pc_7, PC_pc_8,
       PC_pc_9, PC_pc_10, PC_pc_11, PC_pc_12, PC_pc_13, PC_pc_14, PC_pc_15, Register_q_0, Register_q_1,
       Register_q_2, Register_q_3, Register_q_4, Register_q_5, Register_q_6, Register_q_7, Register_q_8,
       Register_q_9, Register_q_10, Register_q_11, Register_q_12, Register_q_13, Register_q_14,
       Register_q_15, Semafor_0_emergency, Semafor_1_emergency, Semafor_2_emergency, Semafor_3_emergency,
       undriven, undriven_2, undriven_3, undriven_4, undriven_5, undriven_6, undriven_7, undriven_8,
       undriven_9, undriven_10, undriven_11, undriven_12, undriven_13, undriven_14, undriven_15, undriven_16,
       WB_output_0, WB_output_1, WB_output_2, WB_output_3, WB_output_4, WB_output_5, WB_output_6,
       WB_output_7, WB_output_8, WB_output_9, WB_output_10, WB_output_11, WB_output_12, WB_output_13,
       WB_output_14, WB_output_15;
  wire [1:0] add_3_s, add_4_s, add_5_s, add_15_s, index_controller_1_index_0, index_incrementer_1_increment_0;
  wire [2:0] add_9_s, add_10_s, multiplexer_1_out, multiplexer_2_out, multiplexer_3_out, multiplexer_4_out,
       Semafor_0_flag_3, Semafor_1_flag_3, Semafor_2_flag_3, Semafor_3_flag_3, sub_1_s, sub_2_s, sub_3_s;
  wire [3:3] add_10_c_o;
  wire [7:0] add_1_s, add_11_s, add_13_s, add_16_s, Semafor_0_q_0_0, Semafor_0_q_1_0, Semafor_0_q_2_0,
       Semafor_1_q_0_0, Semafor_1_q_1_0, Semafor_1_q_2_0, Semafor_2_q_0_0, Semafor_2_q_1_0, Semafor_2_q_2_0,
       Semafor_3_q_0_0, Semafor_3_q_1_0, Semafor_3_q_2_0;
  wire [15:0] add_2_s, add_12_s, add_14_s, add_17_s, multiplexer_5_out, multiplexer_6_out, multiplexer_7_out;

  _16bit_mux_2to1 _16bit_mux_2to1_1 (
    .I0_0(adder_1_adder_0), .I0_1(adder_1_adder_1), .I0_2(adder_1_adder_2), .I0_3(adder_1_adder_3),
    .I0_4(adder_1_adder_4), .I0_5(adder_1_adder_5), .I0_6(adder_1_adder_6), .I0_7(adder_1_adder_7),
    .I0_8(adder_1_adder_8), .I0_9(adder_1_adder_9), .I0_10(adder_1_adder_10), .I0_11(adder_1_adder_11),
    .I0_12(adder_1_adder_12), .I0_13(adder_1_adder_13), .I0_14(adder_1_adder_14), .I0_15(adder_1_adder_15),
    .I1_0(ID_nextaddr_0), .I1_1(ID_nextaddr_1), .I1_2(ID_nextaddr_2), .I1_3(ID_nextaddr_3),
    .I1_4(ID_nextaddr_4), .I1_5(ID_nextaddr_5), .I1_6(1'b0), .I1_7(1'b0), .I1_8(1'b0), .I1_9(1'b0),
    .I1_10(1'b0), .I1_11(1'b0), .I1_12(1'b0), .I1_13(1'b0), .I1_14(1'b0), .I1_15(1'b0),
    .Select(ID_branchingcond), .Output_0(_16bit_mux_2to1_1_output_0), .Output_1(_16bit_mux_2to1_1_output_1),
    .Output_2(_16bit_mux_2to1_1_output_2), .Output_3(_16bit_mux_2to1_1_output_3),
    .Output_4(_16bit_mux_2to1_1_output_4), .Output_5(_16bit_mux_2to1_1_output_5),
    .Output_6(_16bit_mux_2to1_1_output_6), .Output_7(_16bit_mux_2to1_1_output_7),
    .Output_8(_16bit_mux_2to1_1_output_8), .Output_9(_16bit_mux_2to1_1_output_9),
    .Output_10(_16bit_mux_2to1_1_output_10), .Output_11(_16bit_mux_2to1_1_output_11),
    .Output_12(_16bit_mux_2to1_1_output_12), .Output_13(_16bit_mux_2to1_1_output_13),
    .Output_14(_16bit_mux_2to1_1_output_14), .Output_15(_16bit_mux_2to1_1_output_15));
  Program_Counter PC (
    .JumpAddr_0(_16bit_mux_2to1_1_output_0), .Clock(Frequency), .Reset(ID_c_0),
    .JumpAddr_1(_16bit_mux_2to1_1_output_1), .JumpAddr_2(_16bit_mux_2to1_1_output_2),
    .JumpAddr_3(_16bit_mux_2to1_1_output_3), .JumpAddr_4(_16bit_mux_2to1_1_output_4),
    .JumpAddr_5(_16bit_mux_2to1_1_output_5), .JumpAddr_6(_16bit_mux_2to1_1_output_6),
    .JumpAddr_7(_16bit_mux_2to1_1_output_7), .JumpAddr_8(_16bit_mux_2to1_1_output_8),
    .JumpAddr_9(_16bit_mux_2to1_1_output_9), .JumpAddr_10(_16bit_mux_2to1_1_output_10),
    .JumpAddr_11(_16bit_mux_2to1_1_output_11), .JumpAddr_12(_16bit_mux_2to1_1_output_12),
    .JumpAddr_13(_16bit_mux_2to1_1_output_13), .JumpAddr_14(_16bit_mux_2to1_1_output_14),
    .JumpAddr_15(_16bit_mux_2to1_1_output_15), .PC_0(PC_pc_0), .PC_1(PC_pc_1), .PC_2(PC_pc_2),
    .PC_3(PC_pc_3), .PC_4(PC_pc_4), .PC_5(PC_pc_5), .PC_6(PC_pc_6), .PC_7(PC_pc_7), .PC_8(PC_pc_8),
    .PC_9(PC_pc_9), .PC_10(PC_pc_10), .PC_11(PC_pc_11), .PC_12(PC_pc_12), .PC_13(PC_pc_13), .PC_14(PC_pc_14),
    .PC_15(PC_pc_15));
  Adder adder_1 (
    .A_0(1'b1), .A_1(1'b0), .A_2(1'b0), .A_3(1'b0), .A_4(1'b0), .A_5(1'b0), .A_6(1'b0), .A_7(1'b0),
    .A_8(1'b0), .A_9(1'b0), .A_10(1'b0), .A_11(1'b0), .A_12(1'b0), .A_13(1'b0), .A_14(1'b0), .A_15(1'b0),
    .B_0(PC_pc_0), .B_1(PC_pc_1), .B_2(PC_pc_2), .B_3(PC_pc_3), .B_4(PC_pc_4), .B_5(PC_pc_5), .B_6(PC_pc_6),
    .B_7(PC_pc_7), .B_8(PC_pc_8), .B_9(PC_pc_9), .B_10(PC_pc_10), .B_11(PC_pc_11), .B_12(PC_pc_12),
    .B_13(PC_pc_13), .B_14(PC_pc_14), .B_15(PC_pc_15), .Adder_0(adder_1_adder_0), .Adder_1(adder_1_adder_1),
    .Adder_2(adder_1_adder_2), .Adder_3(adder_1_adder_3), .Adder_4(adder_1_adder_4),
    .Adder_5(adder_1_adder_5), .Adder_6(adder_1_adder_6), .Adder_7(adder_1_adder_7),
    .Adder_8(adder_1_adder_8), .Adder_9(adder_1_adder_9), .Adder_10(adder_1_adder_10),
    .Adder_11(adder_1_adder_11), .Adder_12(adder_1_adder_12), .Adder_13(adder_1_adder_13),
    .Adder_14(adder_1_adder_14), .Adder_15(adder_1_adder_15));  // open: Carry_in, Carry_out
  Add #(.Bits(8)) add_1 (.a(Semafor_0_q_1_0), .b(Semafor_0_q_2_0), .s(add_1_s), .c_o(add_1_c_o));  // open: c_i
  Add add_2 (.a(Semafor_0_q_0_0[0]), .b(add_1_s[0]), .c_i(add_1_c_o), .s(add_2_s[0]));  // open: c_o
  Multiplexer #(.Selector_Bits(2)) multiplexer_1 (
    .sel(index_controller_1_index_0), .in_0(Semafor_0_flag_3[0]), .in_1(Semafor_1_flag_3[0]),
    .in_2(Semafor_2_flag_3[0]), .in_3(Semafor_3_flag_3[0]), .out(multiplexer_1_out[0]));
  Multiplexer #(.Selector_Bits(2)) multiplexer_2 (
    .sel(add_3_s), .in_0(Semafor_0_flag_3[0]), .in_1(Semafor_1_flag_3[0]), .in_2(Semafor_2_flag_3[0]),
    .in_3(Semafor_3_flag_3[0]), .out(multiplexer_2_out[0]));
  Multiplexer #(.Selector_Bits(2)) multiplexer_3 (
    .sel(add_4_s), .in_0(Semafor_0_flag_3[0]), .in_1(Semafor_1_flag_3[0]), .in_2(Semafor_2_flag_3[0]),
    .in_3(Semafor_3_flag_3[0]), .out(multiplexer_3_out[0]));
  Multiplexer #(.Selector_Bits(2)) multiplexer_4 (
    .sel(add_5_s), .in_0(Semafor_0_flag_3[0]), .in_1(Semafor_1_flag_3[0]), .in_2(Semafor_2_flag_3[0]),
    .in_3(Semafor_3_flag_3[0]), .out(multiplexer_4_out[0]));
  or or_1 (or_1_out, Semafor_0_emergency, Semafor_1_emergency);
  or or_2 (or_2_out, Semafor_2_emergency, Semafor_3_emergency);
  Memory IR (
    .A_0(PC_pc_0), .A_1(PC_pc_1), .A_2(PC_pc_2), .A_3(PC_pc_3), .A_4(PC_pc_4), .A_5(PC_pc_5), .A_6(PC_pc_6),
    .A_7(PC_pc_7), .A_8(PC_pc_8), .A_9(PC_pc_9), .A_10(PC_pc_10), .A_11(PC_pc_11), .A_12(PC_pc_12),
    .A_13(PC_pc_13), .A_14(PC_pc_14), .A_15(PC_pc_15), .Q_7(IR_q_7), .Q_6(IR_q_6), .Q_5(IR_q_5),
    .Q_4(IR_q_4), .Q_3(IR_q_3), .Q_0(IR_q_0), .Q_1(IR_q_1), .Q_2(IR_q_2), .Q_15(IR_q_15), .Q_14(IR_q_14),
    .Q_13(IR_q_13), .Q_12(IR_q_12), .Q_11(IR_q_11), .Q_8(IR_q_8), .Q_9(IR_q_9), .Q_10(IR_q_10),
    .Q_21(IR_q_21), .Q_20(IR_q_20), .Q_19(IR_q_19), .Q_18(IR_q_18), .Q_16(IR_q_16), .Q_17(IR_q_17));
  or or_3 (or_3_out, or_1_out, or_2_out);
  Semafor Semafor_0 (
    .Enable_counters(enable_counter_0_q), .Reset_counters(and_17_out), .Async_counter1(SenzorMasina0_2),
    .Async_counter2(SenzorMasina0_1), .Async_counter3(SenzorMasina0_0), .Flag_sensor1(Flags0_2),
    .Flag_sensor2(Flags0_1), .Flag_sensor3(Flags0_0), .Emergency_sensor(Emergency_0), .Set_verde(and_9_out),
    .Set_galben(and_5_out), .Set_rosu(and_1_out), .Begin(ID_c_0), .Q_0_0(Semafor_0_q_0_0[0]),
    .Q_0_1(Semafor_0_q_0_0[1]), .Q_0_2(Semafor_0_q_0_0[2]), .Q_0_3(Semafor_0_q_0_0[3]),
    .Q_0_4(Semafor_0_q_0_0[4]), .Q_0_5(Semafor_0_q_0_0[5]), .Q_0_6(Semafor_0_q_0_0[6]),
    .Q_0_7(Semafor_0_q_0_0[7]), .Q_1_0(Semafor_0_q_1_0[0]), .Q_1_1(Semafor_0_q_1_0[1]),
    .Q_1_2(Semafor_0_q_1_0[2]), .Q_1_3(Semafor_0_q_1_0[3]), .Q_1_4(Semafor_0_q_1_0[4]),
    .Q_1_5(Semafor_0_q_1_0[5]), .Q_1_6(Semafor_0_q_1_0[6]), .Q_1_7(Semafor_0_q_1_0[7]),
    .Q_2_0(Semafor_0_q_2_0[0]), .Q_2_1(Semafor_0_q_2_0[1]), .Q_2_2(Semafor_0_q_2_0[2]),
    .Q_2_3(Semafor_0_q_2_0[3]), .Q_2_4(Semafor_0_q_2_0[4]), .Q_2_5(Semafor_0_q_2_0[5]),
    .Q_2_6(Semafor_0_q_2_0[6]), .Q_2_7(Semafor_0_q_2_0[7]), .Flag_1(Semafor_0_flag_3[0]),
    .Flag_2(Semafor_0_flag_3[1]), .Flag_3(Semafor_0_flag_3[2]), .Emergency(Semafor_0_emergency));  // open: Color_green, Color_yellow, Color_red
  Add add_3 (.a(index_controller_1_index_0[0]), .b(1'b1), .s(add_3_s[0]));  // open: c_i, c_o
  Add add_4 (.a(index_controller_1_index_0[0]), .b(1'b0), .s(add_4_s[0]));  // open: c_i, c_o
  Add add_5 (.a(index_controller_1_index_0[0]), .b(1'b1), .s(add_5_s[0]));  // open: c_i, c_o
  Sub #(.Bits(3)) sub_1 (.a(multiplexer_2_out), .b(multiplexer_1_out), .s(sub_1_s));  // open: c_i, c_o
  Sub #(.Bits(3)) sub_2 (.a(multiplexer_2_out), .b(multiplexer_3_out), .s(sub_2_s));  // open: c_i, c_o
  Sub #(.Bits(3)) sub_3 (.a(multiplexer_2_out), .b(multiplexer_4_out), .s(sub_3_s));  // open: c_i, c_o
  Add add_6 (.a(add_12_s[0]), .b(add_2_s[0]), .s(add_6_s), .c_o(add_6_c_o));  // open: c_i
  Add add_7 (.a(add_14_s[0]), .b(add_6_s), .c_i(add_6_c_o), .s(add_7_s), .c_o(add_7_c_o));
  Add add_8 (.a(add_17_s[0]), .b(add_7_s), .c_i(add_7_c_o), .s(add_8_s));  // open: c_o
  Add #(.Bits(3)) add_9 (.a(sub_1_s), .b(sub_2_s), .s(add_9_s), .c_o(add_9_c_o));  // open: c_i
  Add #(.Bits(3)) add_10 (.a(add_9_s), .b(sub_3_s), .c_i(add_9_c_o), .s(add_10_s), .c_o(add_10_c_o[3]));
  Add #(.Bits(8)) add_11 (.a(Semafor_1_q_1_0), .b(Semafor_1_q_2_0), .s(add_11_s), .c_o(add_11_c_o));  // open: c_i
  Add add_12 (.a(Semafor_1_q_0_0[0]), .b(add_11_s[0]), .c_i(add_11_c_o), .s(add_12_s[0]));  // open: c_o
  and and_1 (and_1_out, decoder_1_out_0, ID_c_5);
  and and_2 (and_2_out, decoder_1_out_1, ID_c_5);
  Decoder #(.Selector_Bits(2)) decoder_1 (
    .sel(index_controller_1_index_0), .out_0(decoder_1_out_0), .out_1(decoder_1_out_1),
    .out_2(decoder_1_out_2), .out_3(decoder_1_out_3));
  and and_3 (and_3_out, decoder_1_out_2, ID_c_5);
  Semafor Semafor_1 (
    .Enable_counters(enable_counter_1_q), .Reset_counters(and_18_out), .Async_counter2(SenzorMasina1_2),
    .Async_counter3(SenzorMasina1_1), .Async_counter1(SenzorMasina1_0), .Flag_sensor1(Flags1_2),
    .Flag_sensor2(Flags1_1), .Flag_sensor3(Flags1_0), .Emergency_sensor(Emergency_1), .Set_verde(and_10_out),
    .Set_galben(and_6_out), .Set_rosu(and_2_out), .Begin(ID_c_0), .Q_0_0(Semafor_1_q_0_0[0]),
    .Q_0_1(Semafor_1_q_0_0[1]), .Q_0_2(Semafor_1_q_0_0[2]), .Q_0_3(Semafor_1_q_0_0[3]),
    .Q_0_4(Semafor_1_q_0_0[4]), .Q_0_5(Semafor_1_q_0_0[5]), .Q_0_6(Semafor_1_q_0_0[6]),
    .Q_0_7(Semafor_1_q_0_0[7]), .Q_1_0(Semafor_1_q_1_0[0]), .Q_1_1(Semafor_1_q_1_0[1]),
    .Q_1_2(Semafor_1_q_1_0[2]), .Q_1_3(Semafor_1_q_1_0[3]), .Q_1_4(Semafor_1_q_1_0[4]),
    .Q_1_5(Semafor_1_q_1_0[5]), .Q_1_6(Semafor_1_q_1_0[6]), .Q_1_7(Semafor_1_q_1_0[7]),
    .Q_2_0(Semafor_1_q_2_0[0]), .Q_2_1(Semafor_1_q_2_0[1]), .Q_2_2(Semafor_1_q_2_0[2]),
    .Q_2_3(Semafor_1_q_2_0[3]), .Q_2_4(Semafor_1_q_2_0[4]), .Q_2_5(Semafor_1_q_2_0[5]),
    .Q_2_6(Semafor_1_q_2_0[6]), .Q_2_7(Semafor_1_q_2_0[7]), .Flag_1(Semafor_1_flag_3[0]),
    .Flag_2(Semafor_1_flag_3[1]), .Flag_3(Semafor_1_flag_3[2]), .Emergency(Semafor_1_emergency));  // open: Color_green, Color_yellow, Color_red
  and and_4 (and_4_out, decoder_1_out_3, ID_c_5);
  and and_5 (and_5_out, decoder_2_out_0, ID_c_9);
  and and_6 (and_6_out, decoder_2_out_1, ID_c_9);
  Decoder #(.Selector_Bits(2)) decoder_2 (
    .sel(index_controller_1_index_0), .out_0(decoder_2_out_0), .out_1(decoder_2_out_1),
    .out_2(decoder_2_out_2), .out_3(decoder_2_out_3));
  and and_7 (and_7_out, decoder_2_out_2, ID_c_9);
  and and_8 (and_8_out, decoder_2_out_3, ID_c_9);
  Multiplexer multiplexer_5 (.sel(ID_branchingcond), .in_0(add_8_s), .in_1(add_10_s[0]), .out(multiplexer_5_out[0]));
  Add #(.Bits(8)) add_13 (.a(Semafor_2_q_1_0), .b(Semafor_2_q_2_0), .s(add_13_s), .c_o(add_13_c_o));  // open: c_i
  Add add_14 (.a(Semafor_2_q_0_0[0]), .b(add_13_s[0]), .c_i(add_13_c_o), .s(add_14_s[0]));  // open: c_o
  nand nand_1 (nand_1_out, index_controller_1_index_0[0], index_controller_1_index_0[1]);
  InstructionDecoder ID (
    .CS_0(IR_q_0), .CS_1(IR_q_1), .CS_2(IR_q_2), .CS_3(IR_q_3), .T_verde(nand_1_out), .Emergency(or_3_out),
    .emergency_0(Semafor_0_emergency), .emergency_1(Semafor_1_emergency), .emergency_2(Semafor_2_emergency),
    .emergency_3(Semafor_3_emergency), .cold(Cold_q), .T_verde_lt_T_min(ALU_negative),
    .T_verde_gt_T_max(or_4_out), .index__eq_3(nand_1_out), .Debit(nand_1_out), .Emergency_4(or_3_out),
    .T_galben(nand_1_out), .BA_0(IR_q_4), .BA_1(IR_q_5), .BA_2(IR_q_6), .BA_3(IR_q_7), .BA_4(IR_q_8),
    .BA_5(IR_q_9), .CF_0(IR_q_10), .CF_1(IR_q_11), .CF_2(IR_q_12), .CF_3(IR_q_13), .CF_4(IR_q_14),
    .CF_5(IR_q_15), .CF_6(IR_q_16), .CF_7(IR_q_17), .CF_8(IR_q_18), .CF_9(IR_q_19), .CF_10(IR_q_20),
    .CF_11(IR_q_21), .BranchingCond(ID_branchingcond), .NextAddr_0(ID_nextaddr_0),
    .NextAddr_1(ID_nextaddr_1), .NextAddr_2(ID_nextaddr_2), .NextAddr_3(ID_nextaddr_3),
    .NextAddr_4(ID_nextaddr_4), .NextAddr_5(ID_nextaddr_5), .C_0(ID_c_0), .C_1(ID_c_1), .C_2(ID_c_2),
    .C_3(ID_c_3), .C_4(ID_c_4), .C_5(ID_c_5), .C_6(ID_c_6), .C_7(ID_c_7), .C_8(ID_c_8), .C_9(ID_c_9),
    .C_10(ID_c_10), .C_11(ID_c_11), .C_12(ID_branchingcond), .C_13(ID_c_13), .C_14(ID_c_14), .C_15(ID_c_15),
    .C_16(ID_c_16), .C_17(ID_c_17), .C_18(ID_c_18), .C_19(ID_c_19), .C_20(ID_c_20), .C_21(ID_c_21),
    .C_22(ID_c_22), .C_23(ID_c_23), .C_24(ID_c_24));
  and and_9 (and_9_out, decoder_3_out_0, ID_c_2);
  RS_FF_AS Cold (.S(ID_c_0), .R(ID_c_19), .Q(Cold_q));  // open: nQ
  or or_4 (or_4_out, ALU_carryout, ALU_overflow);
  Semafor Semafor_2 (
    .Enable_counters(enable_counter_2_q), .Reset_counters(and_19_out), .Async_counter2(SenzorMasina2_2),
    .Async_counter3(SenzorMasina2_1), .Async_counter1(SenzorMasina2_0), .Flag_sensor1(Flags2_2),
    .Flag_sensor2(Flags2_1), .Flag_sensor3(Flags2_0), .Emergency_sensor(Emergency_2), .Set_verde(and_11_out),
    .Set_galben(and_7_out), .Set_rosu(and_3_out), .Begin(ID_c_0), .Q_0_0(Semafor_2_q_0_0[0]),
    .Q_0_1(Semafor_2_q_0_0[1]), .Q_0_2(Semafor_2_q_0_0[2]), .Q_0_3(Semafor_2_q_0_0[3]),
    .Q_0_4(Semafor_2_q_0_0[4]), .Q_0_5(Semafor_2_q_0_0[5]), .Q_0_6(Semafor_2_q_0_0[6]),
    .Q_0_7(Semafor_2_q_0_0[7]), .Q_1_0(Semafor_2_q_1_0[0]), .Q_1_1(Semafor_2_q_1_0[1]),
    .Q_1_2(Semafor_2_q_1_0[2]), .Q_1_3(Semafor_2_q_1_0[3]), .Q_1_4(Semafor_2_q_1_0[4]),
    .Q_1_5(Semafor_2_q_1_0[5]), .Q_1_6(Semafor_2_q_1_0[6]), .Q_1_7(Semafor_2_q_1_0[7]),
    .Q_2_0(Semafor_2_q_2_0[0]), .Q_2_1(Semafor_2_q_2_0[1]), .Q_2_2(Semafor_2_q_2_0[2]),
    .Q_2_3(Semafor_2_q_2_0[3]), .Q_2_4(Semafor_2_q_2_0[4]), .Q_2_5(Semafor_2_q_2_0[5]),
    .Q_2_6(Semafor_2_q_2_0[6]), .Q_2_7(Semafor_2_q_2_0[7]), .Flag_1(Semafor_2_flag_3[0]),
    .Flag_2(Semafor_2_flag_3[1]), .Flag_3(Semafor_2_flag_3[2]), .Emergency(Semafor_2_emergency));  // open: Color_green, Color_yellow, Color_red
  and and_10 (and_10_out, decoder_3_out_1, ID_c_2);
  Decoder #(.Selector_Bits(2)) decoder_3 (
    .sel(index_controller_1_index_0), .out_0(decoder_3_out_0), .out_1(decoder_3_out_1),
    .out_2(decoder_3_out_2), .out_3(decoder_3_out_3));
  and and_11 (and_11_out, decoder_3_out_2, ID_c_2);
  and and_12 (and_12_out, decoder_3_out_3, ID_c_2);
  or or_5 (or_5_out, ID_c_6, or_7_out);
  or or_6 (or_6_out, ID_c_4, ID_c_22);
  or or_7 (or_7_out, ID_c_7, ID_c_8);
  Add #(.Bits(2)) add_15 (
    .a(index_controller_1_index_0), .b(index_incrementer_1_increment_0), .s(add_15_s));  // open: c_i, c_o
  or or_8 (or_8_out, or_5_out, ID_c_18);
  or or_9 (or_9_out, decoder_4_out_0, ID_c_21);
  or or_10 (or_10_out, ID_c_14, ID_c_15);
  Index_controller index_controller_1 (
    .D_0(add_15_s[0]), .D_1(add_15_s[1]), .Reset(ID_c_0), .Increment(or_8_out), .Override(or_5_out),
    .index_0(index_controller_1_index_0[0]), .index_1(index_controller_1_index_0[1]));
  RS_FF_AS enable_counter_0 (.S(and_13_out), .R(ID_c_9), .Q(enable_counter_0_q));  // open: nQ
  and and_13 (and_13_out, or_9_out, ID_c_1);
  or or_11 (or_11_out, decoder_4_out_1, ID_c_21);
  Add #(.Bits(8)) add_16 (.a(Semafor_3_q_1_0), .b(Semafor_3_q_2_0), .s(add_16_s), .c_o(add_16_c_o));  // open: c_i
  Add add_17 (.a(Semafor_3_q_0_0[0]), .b(add_16_s[0]), .c_i(add_16_c_o), .s(add_17_s[0]));  // open: c_o
  index_incrementer index_incrementer_1 (
    .C_6(ID_c_6), .C_7(ID_c_7), .C_8(ID_c_8), .increment_0(index_incrementer_1_increment_0[0]),
    .increment_1(index_incrementer_1_increment_0[1]));
  RS_FF_AS enable_counter_1 (.S(and_14_out), .R(ID_c_9), .Q(enable_counter_1_q));  // open: nQ
  and and_14 (and_14_out, or_11_out, ID_c_1);
  or or_12 (or_12_out, decoder_4_out_2, ID_c_21);
  Decoder #(.Selector_Bits(2)) decoder_4 (
    .sel(index_controller_1_index_0), .out_0(decoder_4_out_0), .out_1(decoder_4_out_1),
    .out_2(decoder_4_out_2), .out_3(decoder_4_out_3));
  Multiplexer #(.Selector_Bits(2), .Bits(16)) multiplexer_6 (
    .in_0(add_2_s), .in_1(add_12_s), .in_2(add_14_s), .in_3(add_17_s), .out(multiplexer_6_out));  // open: sel
  RS_FF_AS enable_counter_2 (.S(and_15_out), .R(ID_c_9), .Q(enable_counter_2_q));  // open: nQ
  and and_15 (and_15_out, or_12_out, ID_c_1);
  or or_13 (or_13_out, decoder_4_out_3, ID_c_21);
  _16bit_mux_2to1 _16bit_mux_2to1_2 (
    .I0_0(ALU_output_0), .I0_1(ALU_output_1), .I0_2(ALU_output_2), .I0_3(ALU_output_3), .I0_4(ALU_output_4),
    .I0_5(ALU_output_5), .I0_6(ALU_output_6), .I0_7(ALU_output_7), .I0_8(ALU_output_8), .I0_9(ALU_output_9),
    .I0_10(ALU_output_10), .I0_11(ALU_output_11), .I0_12(ALU_output_12), .I0_13(ALU_output_13),
    .I0_14(ALU_output_14), .I0_15(ALU_output_15), .I1_0(WB_output_0), .I1_1(WB_output_1), .I1_2(WB_output_2),
    .I1_3(WB_output_3), .I1_4(WB_output_4), .I1_5(WB_output_5), .I1_6(WB_output_6), .I1_7(WB_output_7),
    .I1_8(WB_output_8), .I1_9(WB_output_9), .I1_10(WB_output_10), .I1_11(WB_output_11), .I1_12(WB_output_12),
    .I1_13(WB_output_13), .I1_14(WB_output_14), .I1_15(WB_output_15), .Output_0(_16bit_mux_2to1_2_output_0),
    .Output_1(_16bit_mux_2to1_2_output_1), .Output_2(_16bit_mux_2to1_2_output_2),
    .Output_3(_16bit_mux_2to1_2_output_3), .Output_4(_16bit_mux_2to1_2_output_4),
    .Output_5(_16bit_mux_2to1_2_output_5), .Output_6(_16bit_mux_2to1_2_output_6),
    .Output_7(_16bit_mux_2to1_2_output_7), .Output_8(_16bit_mux_2to1_2_output_8),
    .Output_9(_16bit_mux_2to1_2_output_9), .Output_10(_16bit_mux_2to1_2_output_10),
    .Output_11(_16bit_mux_2to1_2_output_11), .Output_12(_16bit_mux_2to1_2_output_12),
    .Output_13(_16bit_mux_2to1_2_output_13), .Output_14(_16bit_mux_2to1_2_output_14),
    .Output_15(_16bit_mux_2to1_2_output_15));  // open: Select
  RS_FF_AS enable_counter_3 (.S(and_16_out), .R(ID_c_9), .Q(enable_counter_3_q));  // open: nQ
  and and_16 (and_16_out, or_13_out, ID_c_1);
  or or_14 (or_14_out, ID_c_23, ID_c_24, ID_c_20, ID_c_16);
  Semafor Semafor_3 (
    .Enable_counters(enable_counter_3_q), .Reset_counters(and_20_out), .Async_counter2(SenzorMasina3_2),
    .Async_counter3(SenzorMasina3_1), .Async_counter1(SenzorMasina3_0), .Flag_sensor1(Flags3_2),
    .Flag_sensor2(Flags3_1), .Flag_sensor3(Flags3_0), .Emergency_sensor(Emergency_3), .Set_verde(and_12_out),
    .Set_galben(and_8_out), .Set_rosu(and_4_out), .Begin(ID_c_0), .Q_0_0(Semafor_3_q_0_0[0]),
    .Q_0_1(Semafor_3_q_0_0[1]), .Q_0_2(Semafor_3_q_0_0[2]), .Q_0_3(Semafor_3_q_0_0[3]),
    .Q_0_4(Semafor_3_q_0_0[4]), .Q_0_5(Semafor_3_q_0_0[5]), .Q_0_6(Semafor_3_q_0_0[6]),
    .Q_0_7(Semafor_3_q_0_0[7]), .Q_1_0(Semafor_3_q_1_0[0]), .Q_1_1(Semafor_3_q_1_0[1]),
    .Q_1_2(Semafor_3_q_1_0[2]), .Q_1_3(Semafor_3_q_1_0[3]), .Q_1_4(Semafor_3_q_1_0[4]),
    .Q_1_5(Semafor_3_q_1_0[5]), .Q_1_6(Semafor_3_q_1_0[6]), .Q_1_7(Semafor_3_q_1_0[7]),
    .Q_2_0(Semafor_3_q_2_0[0]), .Q_2_1(Semafor_3_q_2_0[1]), .Q_2_2(Semafor_3_q_2_0[2]),
    .Q_2_3(Semafor_3_q_2_0[3]), .Q_2_4(Semafor_3_q_2_0[4]), .Q_2_5(Semafor_3_q_2_0[5]),
    .Q_2_6(Semafor_3_q_2_0[6]), .Q_2_7(Semafor_3_q_2_0[7]), .Flag_1(Semafor_3_flag_3[0]),
    .Flag_2(Semafor_3_flag_3[1]), .Flag_3(Semafor_3_flag_3[2]), .Emergency(Semafor_3_emergency));  // open: Color_green, Color_yellow, Color_red
  _8Registers_encoded _8registers_encoded_1 (
    .Input_0(_16bit_mux_2to1_2_output_0), .Input_1(_16bit_mux_2to1_2_output_1),
    .Input_2(_16bit_mux_2to1_2_output_2), .Input_3(_16bit_mux_2to1_2_output_3),
    .Input_4(_16bit_mux_2to1_2_output_4), .Input_5(_16bit_mux_2to1_2_output_5),
    .Input_6(_16bit_mux_2to1_2_output_6), .Input_7(_16bit_mux_2to1_2_output_7),
    .Input_8(_16bit_mux_2to1_2_output_8), .Input_9(_16bit_mux_2to1_2_output_9),
    .Input_10(_16bit_mux_2to1_2_output_10), .Input_11(_16bit_mux_2to1_2_output_11),
    .Input_12(_16bit_mux_2to1_2_output_12), .Input_13(_16bit_mux_2to1_2_output_13),
    .Input_14(_16bit_mux_2to1_2_output_14), .Input_15(_16bit_mux_2to1_2_output_15), .Clock(Frequency),
    .Reset(ID_c_0), .Output_0(_8registers_encoded_1_output_0), .Output_1(_8registers_encoded_1_output_1),
    .Output_2(_8registers_encoded_1_output_2), .Output_3(_8registers_encoded_1_output_3),
    .Output_4(_8registers_encoded_1_output_4), .Output_5(_8registers_encoded_1_output_5),
    .Output_6(_8registers_encoded_1_output_6), .Output_7(_8registers_encoded_1_output_7),
    .Output_8(_8registers_encoded_1_output_8), .Output_9(_8registers_encoded_1_output_9),
    .Output_10(_8registers_encoded_1_output_10), .Output_11(_8registers_encoded_1_output_11),
    .Output_12(_8registers_encoded_1_output_12), .Output_13(_8registers_encoded_1_output_13),
    .Output_14(_8registers_encoded_1_output_14), .Output_15(_8registers_encoded_1_output_15));  // open: Select_input_0, Select_input_1, Select_input_2, Select_output_0, Select_output_1, Select_output_2
  OperationSelect operationselect_1 (
    .Add(ID_c_17), .Mul(or_10_out), .Div(ID_c_13), .Mov(or_14_out), .Dec(or_6_out),
    .SelOP_0(operationselect_1_selop_0), .SelOP_1(operationselect_1_selop_1),
    .SelOP_2(operationselect_1_selop_2), .SelOP_3(operationselect_1_selop_3));  // open: Sub, And, Or, Xor, Not, Cmp, Inc, Mod
  Multiplexer #(.Bits(16)) multiplexer_7 (
    .sel(ID_c_11), .in_0(multiplexer_6_out), .in_1(multiplexer_5_out), .out(multiplexer_7_out));
  _16bit_mux_2to1 _16bit_mux_2to1_3 (
    .I0_0(_8registers_encoded_1_output_0), .I0_1(_8registers_encoded_1_output_1),
    .I0_2(_8registers_encoded_1_output_2), .I0_3(_8registers_encoded_1_output_3),
    .I0_4(_8registers_encoded_1_output_4), .I0_5(_8registers_encoded_1_output_5),
    .I0_6(_8registers_encoded_1_output_6), .I0_7(_8registers_encoded_1_output_7),
    .I0_8(_8registers_encoded_1_output_8), .I0_9(_8registers_encoded_1_output_9),
    .I0_10(_8registers_encoded_1_output_10), .I0_11(_8registers_encoded_1_output_11),
    .I0_12(_8registers_encoded_1_output_12), .I0_13(_8registers_encoded_1_output_13),
    .I0_14(_8registers_encoded_1_output_14), .I0_15(_8registers_encoded_1_output_15),
    .I1_0(_16bit_mux_2to1_5_output_0), .I1_1(_16bit_mux_2to1_5_output_1), .I1_2(_16bit_mux_2to1_5_output_2),
    .I1_3(_16bit_mux_2to1_5_output_3), .I1_4(_16bit_mux_2to1_5_output_4), .I1_5(_16bit_mux_2to1_5_output_5),
    .I1_6(_16bit_mux_2to1_5_output_6), .I1_7(_16bit_mux_2to1_5_output_7), .I1_8(_16bit_mux_2to1_5_output_8),
    .I1_9(_16bit_mux_2to1_5_output_9), .I1_10(_16bit_mux_2to1_5_output_10),
    .I1_11(_16bit_mux_2to1_5_output_11), .I1_12(_16bit_mux_2to1_5_output_12),
    .I1_13(_16bit_mux_2to1_5_output_13), .I1_14(_16bit_mux_2to1_5_output_14),
    .I1_15(_16bit_mux_2to1_5_output_15), .Select(or_15_out), .Output_0(_16bit_mux_2to1_3_output_0),
    .Output_1(_16bit_mux_2to1_3_output_1), .Output_2(_16bit_mux_2to1_3_output_2),
    .Output_3(_16bit_mux_2to1_3_output_3), .Output_4(_16bit_mux_2to1_3_output_4),
    .Output_5(_16bit_mux_2to1_3_output_5), .Output_6(_16bit_mux_2to1_3_output_6),
    .Output_7(_16bit_mux_2to1_3_output_7), .Output_8(_16bit_mux_2to1_3_output_8),
    .Output_9(_16bit_mux_2to1_3_output_9), .Output_10(_16bit_mux_2to1_3_output_10),
    .Output_11(_16bit_mux_2to1_3_output_11), .Output_12(_16bit_mux_2to1_3_output_12),
    .Output_13(_16bit_mux_2to1_3_output_13), .Output_14(_16bit_mux_2to1_3_output_14),
    .Output_15(_16bit_mux_2to1_3_output_15));
  _16bit_mux_2to1 _16bit_mux_2to1_4 (
    .I0_0(Register_q_0), .I0_1(Register_q_1), .I0_2(Register_q_2), .I0_3(Register_q_3), .I0_4(Register_q_4),
    .I0_5(Register_q_5), .I0_6(Register_q_6), .I0_7(Register_q_7), .I0_8(Register_q_8), .I0_9(Register_q_9),
    .I0_10(Register_q_10), .I0_11(Register_q_11), .I0_12(Register_q_12), .I0_13(Register_q_13),
    .I0_14(Register_q_14), .I0_15(Register_q_15), .I1_0(multiplexer_7_out[0]), .I1_1(multiplexer_7_out[1]),
    .I1_2(multiplexer_7_out[2]), .I1_3(multiplexer_7_out[3]), .I1_4(multiplexer_7_out[4]),
    .I1_5(multiplexer_7_out[5]), .I1_6(multiplexer_7_out[6]), .I1_7(multiplexer_7_out[7]),
    .I1_8(multiplexer_7_out[8]), .I1_9(multiplexer_7_out[9]), .I1_10(multiplexer_7_out[10]),
    .I1_11(multiplexer_7_out[11]), .I1_12(multiplexer_7_out[12]), .I1_13(multiplexer_7_out[13]),
    .I1_14(multiplexer_7_out[14]), .I1_15(multiplexer_7_out[15]), .Select(ID_c_10),
    .Output_0(_16bit_mux_2to1_4_output_0), .Output_1(_16bit_mux_2to1_4_output_1),
    .Output_2(_16bit_mux_2to1_4_output_2), .Output_3(_16bit_mux_2to1_4_output_3),
    .Output_4(_16bit_mux_2to1_4_output_4), .Output_5(_16bit_mux_2to1_4_output_5),
    .Output_6(_16bit_mux_2to1_4_output_6), .Output_7(_16bit_mux_2to1_4_output_7),
    .Output_8(_16bit_mux_2to1_4_output_8), .Output_9(_16bit_mux_2to1_4_output_9),
    .Output_10(_16bit_mux_2to1_4_output_10), .Output_11(_16bit_mux_2to1_4_output_11),
    .Output_12(_16bit_mux_2to1_4_output_12), .Output_13(_16bit_mux_2to1_4_output_13),
    .Output_14(_16bit_mux_2to1_4_output_14), .Output_15(_16bit_mux_2to1_4_output_15));
  ALU ALU (
    .Input1_0(_16bit_mux_2to1_4_output_0), .Input1_1(_16bit_mux_2to1_4_output_1),
    .Input1_2(_16bit_mux_2to1_4_output_2), .Input1_3(_16bit_mux_2to1_4_output_3),
    .Input1_4(_16bit_mux_2to1_4_output_4), .Input1_5(_16bit_mux_2to1_4_output_5),
    .Input1_6(_16bit_mux_2to1_4_output_6), .Input1_7(_16bit_mux_2to1_4_output_7),
    .Input1_8(_16bit_mux_2to1_4_output_8), .Input1_9(_16bit_mux_2to1_4_output_9),
    .Input1_10(_16bit_mux_2to1_4_output_10), .Input1_11(_16bit_mux_2to1_4_output_11),
    .Input1_12(_16bit_mux_2to1_4_output_12), .Input1_13(_16bit_mux_2to1_4_output_13),
    .Input1_14(_16bit_mux_2to1_4_output_14), .Input1_15(_16bit_mux_2to1_4_output_15),
    .Input2_0(_16bit_mux_2to1_3_output_0), .Input2_1(_16bit_mux_2to1_3_output_1),
    .Input2_2(_16bit_mux_2to1_3_output_2), .Input2_3(_16bit_mux_2to1_3_output_3),
    .Input2_4(_16bit_mux_2to1_3_output_4), .Input2_5(_16bit_mux_2to1_3_output_5),
    .Input2_6(_16bit_mux_2to1_3_output_6), .Input2_7(_16bit_mux_2to1_3_output_7),
    .Input2_8(_16bit_mux_2to1_3_output_8), .Input2_9(_16bit_mux_2to1_3_output_9),
    .Input2_10(_16bit_mux_2to1_3_output_10), .Input2_11(_16bit_mux_2to1_3_output_11),
    .Input2_12(_16bit_mux_2to1_3_output_12), .Input2_13(_16bit_mux_2to1_3_output_13),
    .Input2_14(_16bit_mux_2to1_3_output_14), .Input2_15(_16bit_mux_2to1_3_output_15),
    .SelectOP_0(operationselect_1_selop_0), .SelectOP_1(operationselect_1_selop_1),
    .SelectOP_2(operationselect_1_selop_2), .SelectOP_3(operationselect_1_selop_3), .CarryOut(ALU_carryout),
    .Output_0(ALU_output_0), .Output_1(ALU_output_1), .Output_2(ALU_output_2), .Output_3(ALU_output_3),
    .Output_4(ALU_output_4), .Output_5(ALU_output_5), .Output_6(ALU_output_6), .Output_7(ALU_output_7),
    .Output_8(ALU_output_8), .Output_9(ALU_output_9), .Output_10(ALU_output_10), .Output_11(ALU_output_11),
    .Output_12(ALU_output_12), .Output_13(ALU_output_13), .Output_14(ALU_output_14),
    .Output_15(ALU_output_15), .Zero(nand_1_out), .Negative(ALU_negative), .Overflow(ALU_overflow),
    .Addr_0(ALU_addr_0), .Addr_1(ALU_addr_1), .Addr_2(ALU_addr_2), .Addr_3(ALU_addr_3), .Addr_4(ALU_addr_4),
    .Addr_5(ALU_addr_5), .Addr_6(ALU_addr_6), .Addr_7(ALU_addr_7), .Addr_8(ALU_addr_8), .Addr_9(ALU_addr_9),
    .Addr_10(ALU_addr_10), .Addr_11(ALU_addr_11), .Addr_12(ALU_addr_12), .Addr_13(ALU_addr_13),
    .Addr_14(ALU_addr_14), .Addr_15(ALU_addr_15));  // open: Carry_in
  and and_17 (and_17_out, decoder_5_out_0, ID_c_3);
  and and_18 (and_18_out, decoder_5_out_1, ID_c_3);
  Decoder #(.Selector_Bits(2)) decoder_5 (
    .sel(index_controller_1_index_0), .out_0(decoder_5_out_0), .out_1(decoder_5_out_1),
    .out_2(decoder_5_out_2), .out_3(decoder_5_out_3));
  not not_1 (not_1_out, operationselect_1_selop_0);
  not not_2 (not_2_out, operationselect_1_selop_3);
  and and_19 (and_19_out, decoder_5_out_2, ID_c_3);
  _16bit_register Register (
    .D_0(ALU_output_0), .D_1(ALU_output_1), .D_2(ALU_output_2), .D_3(ALU_output_3), .D_4(ALU_output_4),
    .D_5(ALU_output_5), .D_6(ALU_output_6), .D_7(ALU_output_7), .D_8(ALU_output_8), .D_9(ALU_output_9),
    .D_10(ALU_output_10), .D_11(ALU_output_11), .D_12(ALU_output_12), .D_13(ALU_output_13),
    .D_14(ALU_output_14), .D_15(ALU_output_15), .Reset(ID_c_0), .Clock(Frequency), .Q_0(Register_q_0),
    .Q_1(Register_q_1), .Q_2(Register_q_2), .Q_3(Register_q_3), .Q_4(Register_q_4), .Q_5(Register_q_5),
    .Q_6(Register_q_6), .Q_7(Register_q_7), .Q_8(Register_q_8), .Q_9(Register_q_9), .Q_10(Register_q_10),
    .Q_11(Register_q_11), .Q_12(Register_q_12), .Q_13(Register_q_13), .Q_14(Register_q_14),
    .Q_15(Register_q_15));
  or or_15 (or_15_out, not_1_out, operationselect_1_selop_1, operationselect_1_selop_2, not_2_out);
  and and_20 (and_20_out, decoder_5_out_3, ID_c_3);
  _16bit_mux_2to1 _16bit_mux_2to1_5 (
    .I0_0(undriven_16), .I0_1(undriven_15), .I0_2(undriven_14), .I0_3(undriven_13), .I0_4(undriven_12),
    .I0_5(undriven_11), .I0_6(undriven_10), .I0_7(undriven_9), .I0_8(undriven_8), .I0_9(undriven_7),
    .I0_10(undriven_6), .I0_11(undriven_5), .I0_12(undriven_4), .I0_13(undriven_3), .I0_14(undriven_2),
    .I0_15(undriven), .I1_0(ALU_output_0), .I1_1(ALU_output_1), .I1_2(ALU_output_2), .I1_3(ALU_output_3),
    .I1_4(ALU_output_4), .I1_5(ALU_output_5), .I1_6(ALU_output_6), .I1_7(ALU_output_7), .I1_8(ALU_output_8),
    .I1_9(ALU_output_9), .I1_10(ALU_output_10), .I1_11(ALU_output_11), .I1_12(ALU_output_12),
    .I1_13(ALU_output_13), .I1_14(ALU_output_14), .I1_15(ALU_output_15),
    .Output_0(_16bit_mux_2to1_5_output_0), .Output_1(_16bit_mux_2to1_5_output_1),
    .Output_2(_16bit_mux_2to1_5_output_2), .Output_3(_16bit_mux_2to1_5_output_3),
    .Output_4(_16bit_mux_2to1_5_output_4), .Output_5(_16bit_mux_2to1_5_output_5),
    .Output_6(_16bit_mux_2to1_5_output_6), .Output_7(_16bit_mux_2to1_5_output_7),
    .Output_8(_16bit_mux_2to1_5_output_8), .Output_9(_16bit_mux_2to1_5_output_9),
    .Output_10(_16bit_mux_2to1_5_output_10), .Output_11(_16bit_mux_2to1_5_output_11),
    .Output_12(_16bit_mux_2to1_5_output_12), .Output_13(_16bit_mux_2to1_5_output_13),
    .Output_14(_16bit_mux_2to1_5_output_14), .Output_15(_16bit_mux_2to1_5_output_15));  // open: Select
  Multiplexer multiplexer_8 (
    .sel(or_15_out), .in_0(ALU_output_0), .in_1(_8registers_encoded_1_output_0), .out(multiplexer_8_out));
  Multiplexer multiplexer_9 (
    .sel(or_15_out), .in_0(ALU_output_1), .in_1(_8registers_encoded_1_output_1), .out(multiplexer_9_out));
  Multiplexer multiplexer_10 (
    .sel(or_15_out), .in_0(ALU_output_2), .in_1(_8registers_encoded_1_output_2), .out(multiplexer_10_out));
  Multiplexer multiplexer_11 (
    .sel(or_15_out), .in_0(ALU_output_3), .in_1(_8registers_encoded_1_output_3), .out(multiplexer_11_out));
  Multiplexer multiplexer_12 (
    .sel(or_15_out), .in_0(ALU_output_4), .in_1(_8registers_encoded_1_output_4), .out(multiplexer_12_out));
  Multiplexer multiplexer_13 (
    .sel(or_15_out), .in_0(ALU_output_5), .in_1(_8registers_encoded_1_output_5), .out(multiplexer_13_out));
  Multiplexer multiplexer_14 (
    .sel(or_15_out), .in_0(ALU_output_6), .in_1(_8registers_encoded_1_output_6), .out(multiplexer_14_out));
  Multiplexer multiplexer_15 (
    .sel(or_15_out), .in_0(ALU_output_7), .in_1(_8registers_encoded_1_output_7), .out(multiplexer_15_out));
  Multiplexer multiplexer_16 (
    .sel(or_15_out), .in_0(ALU_output_8), .in_1(_8registers_encoded_1_output_8), .out(multiplexer_16_out));
  Multiplexer multiplexer_17 (
    .sel(or_15_out), .in_0(ALU_output_9), .in_1(_8registers_encoded_1_output_9), .out(multiplexer_17_out));
  Multiplexer multiplexer_18 (
    .sel(or_15_out), .in_0(ALU_output_10), .in_1(_8registers_encoded_1_output_10), .out(multiplexer_18_out));
  Multiplexer multiplexer_19 (
    .sel(or_15_out), .in_0(ALU_output_11), .in_1(_8registers_encoded_1_output_11), .out(multiplexer_19_out));
  Multiplexer multiplexer_20 (
    .sel(or_15_out), .in_0(ALU_output_12), .in_1(_8registers_encoded_1_output_12), .out(multiplexer_20_out));
  Multiplexer multiplexer_21 (
    .sel(or_15_out), .in_0(ALU_output_13), .in_1(_8registers_encoded_1_output_13), .out(multiplexer_21_out));
  Multiplexer multiplexer_22 (
    .sel(or_15_out), .in_0(ALU_output_14), .in_1(_8registers_encoded_1_output_14), .out(multiplexer_22_out));
  Multiplexer multiplexer_23 (
    .sel(or_15_out), .in_0(ALU_output_15), .in_1(_8registers_encoded_1_output_15), .out(multiplexer_23_out));
  DataMemory Memory (
    .A_0(ALU_addr_0), .A_1(ALU_addr_1), .A_2(ALU_addr_2), .A_3(ALU_addr_3), .A_4(ALU_addr_4),
    .A_5(ALU_addr_5), .A_6(ALU_addr_6), .A_7(ALU_addr_7), .A_8(ALU_addr_8), .A_9(ALU_addr_9),
    .A_10(ALU_addr_10), .A_11(ALU_addr_11), .A_12(ALU_addr_12), .A_13(ALU_addr_13), .A_14(ALU_addr_14),
    .A_15(ALU_addr_15), .WE(ID_c_0), .D_0(multiplexer_8_out), .D_1(multiplexer_9_out),
    .D_2(multiplexer_10_out), .D_3(multiplexer_11_out), .D_4(multiplexer_12_out), .D_5(multiplexer_13_out),
    .D_6(multiplexer_14_out), .D_7(multiplexer_15_out), .D_8(multiplexer_16_out), .D_9(multiplexer_17_out),
    .D_10(multiplexer_18_out), .D_11(multiplexer_19_out), .D_12(multiplexer_20_out),
    .D_13(multiplexer_21_out), .D_14(multiplexer_22_out), .D_15(multiplexer_23_out),
    .OutData_0(Memory_outdata_0), .OutData_1(Memory_outdata_1), .OutData_2(Memory_outdata_2),
    .OutData_3(Memory_outdata_3), .OutData_4(Memory_outdata_4), .OutData_5(Memory_outdata_5),
    .OutData_6(Memory_outdata_6), .OutData_7(Memory_outdata_7), .OutData_8(Memory_outdata_8),
    .OutData_9(Memory_outdata_9), .OutData_10(Memory_outdata_10), .OutData_11(Memory_outdata_11),
    .OutData_12(Memory_outdata_12), .OutData_13(Memory_outdata_13), .OutData_14(Memory_outdata_14),
    .OutData_15(Memory_outdata_15));
  _16bit_register Stack_Pointer (
    .D_0(undriven_16), .D_1(undriven_15), .D_2(undriven_14), .D_3(undriven_13), .D_4(undriven_12),
    .D_5(undriven_11), .D_6(undriven_10), .D_7(undriven_9), .D_8(undriven_8), .D_9(undriven_7),
    .D_10(undriven_6), .D_11(undriven_5), .D_12(undriven_4), .D_13(undriven_3), .D_14(undriven_2),
    .D_15(undriven), .Reset(ID_c_0), .Clock(Frequency), .Q_0(ALU_addr_0), .Q_1(ALU_addr_1), .Q_2(ALU_addr_2),
    .Q_3(ALU_addr_3), .Q_4(ALU_addr_4), .Q_5(ALU_addr_5), .Q_6(ALU_addr_6), .Q_7(ALU_addr_7),
    .Q_8(ALU_addr_8), .Q_9(ALU_addr_9), .Q_10(ALU_addr_10), .Q_11(ALU_addr_11), .Q_12(ALU_addr_12),
    .Q_13(ALU_addr_13), .Q_14(ALU_addr_14), .Q_15(ALU_addr_15));
  _16bit_mux_2to1 WB (
    .I0_0(ALU_output_0), .I0_1(ALU_output_1), .I0_2(ALU_output_2), .I0_3(ALU_output_3), .I0_4(ALU_output_4),
    .I0_5(ALU_output_5), .I0_6(ALU_output_6), .I0_7(ALU_output_7), .I0_8(ALU_output_8), .I0_9(ALU_output_9),
    .I0_10(ALU_output_10), .I0_11(ALU_output_11), .I0_12(ALU_output_12), .I0_13(ALU_output_13),
    .I0_14(ALU_output_14), .I0_15(ALU_output_15), .I1_0(Memory_outdata_0), .I1_1(Memory_outdata_1),
    .I1_2(Memory_outdata_2), .I1_3(Memory_outdata_3), .I1_4(Memory_outdata_4), .I1_5(Memory_outdata_5),
    .I1_6(Memory_outdata_6), .I1_7(Memory_outdata_7), .I1_8(Memory_outdata_8), .I1_9(Memory_outdata_9),
    .I1_10(Memory_outdata_10), .I1_11(Memory_outdata_11), .I1_12(Memory_outdata_12),
    .I1_13(Memory_outdata_13), .I1_14(Memory_outdata_14), .I1_15(Memory_outdata_15), .Output_0(WB_output_0),
    .Output_1(WB_output_1), .Output_2(WB_output_2), .Output_3(WB_output_3), .Output_4(WB_output_4),
    .Output_5(WB_output_5), .Output_6(WB_output_6), .Output_7(WB_output_7), .Output_8(WB_output_8),
    .Output_9(WB_output_9), .Output_10(WB_output_10), .Output_11(WB_output_11), .Output_12(WB_output_12),
    .Output_13(WB_output_13), .Output_14(WB_output_14), .Output_15(WB_output_15));  // open: Select
  // Pins of 1 and 2 bits meet at index_controller_1_index_0
  // Pins of 1 and 8 bits meet at Semafor_3_q_0_0
  // Pins of 1 and 8 bits meet at Semafor_2_q_0_0
  // Pins of 1 and 8 bits meet at Semafor_1_q_0_0
  // Pins of 1 and 8 bits meet at Semafor_0_q_0_0
  // Pins of 1 and 8 bits meet at add_16_s
  // Pins of 1 and 16 bits meet at add_17_s
  // Pins of 1 and 8 bits meet at add_13_s
  // Pins of 1 and 16 bits meet at add_14_s
  // Pins of 1 and 8 bits meet at add_11_s
  // Pins of 1 and 16 bits meet at add_12_s
  // Pins of 1 and 8 bits meet at add_1_s

  // Notes on the sheet:
  //   DebitTotal_0
  //   Emergency signal
  //   DebitTotal_1
  //   Rosu
  //   CS bits
  //   BA bits
  //   CF bits
  //   Galben
  //   DebitTotal_2
  //   Verde
  //   DebitTotal_3
endmodule
