// Digital circuit Counter_Async.dig as structural Verilog
module Counter_Async (
  input  Enable,
  input  Reset,
  input  Clock,
  output Q_0,
  output Q_1,
  output Q_2,
  output Q_3,
  output Q_4,
  output Q_5,
  output Q_6,
  output Q_7
);

  wire and_1_out, and_2_out, and_3_out, and_4_out, and_5_out, and_6_out, and_7_out, multiplexer_1_out,
       multiplexer_2_out, multiplexer_3_out, multiplexer_4_out, multiplexer_5_out, multiplexer_6_out,
       multiplexer_7_out, multiplexer_8_out, xor_1_out, xor_2_out, xor_3_out, xor_4_out, xor_5_out,
       xor_6_out, xor_7_out, xor_8_out, xor_9_out;

  and and_1 (and_1_out, Q_0, Enable);
  and and_2 (and_2_out, Q_1, and_1_out);
  and and_3 (and_3_out, Q_2, and_2_out);
  xor xor_1 (xor_1_out, Reset, Clock);
  and and_4 (and_4_out, Q_3, and_3_out);
  and and_5 (and_5_out, Q_4, and_4_out);
  and and_6 (and_6_out, Q_5, and_5_out);
  and and_7 (and_7_out, Q_6, and_6_out);
  xor xor_2 (xor_2_out, Q_0, Enable);
  xor xor_3 (xor_3_out, Q_1, and_1_out);
  xor xor_4 (xor_4_out, Q_2, and_2_out);
  xor xor_5 (xor_5_out, Q_3, and_3_out);
  xor xor_6 (xor_6_out, Q_4, and_4_out);
  xor xor_7 (xor_7_out, Q_5, and_5_out);
  xor xor_8 (xor_8_out, Q_6, and_6_out);
  xor xor_9 (xor_9_out, Q_7, and_7_out);
  Multiplexer multiplexer_1 (.sel(Reset), .in_0(xor_2_out), .in_1(1'b0), .out(multiplexer_1_out));
  Multiplexer multiplexer_2 (.sel(Reset), .in_0(xor_3_out), .in_1(1'b0), .out(multiplexer_2_out));
  Multiplexer multiplexer_3 (.sel(Reset), .in_0(xor_4_out), .in_1(1'b0), .out(multiplexer_3_out));
  Multiplexer multiplexer_4 (.sel(Reset), .in_0(xor_5_out), .in_1(1'b0), .out(multiplexer_4_out));
  Multiplexer multiplexer_5 (.sel(Reset), .in_0(xor_6_out), .in_1(1'b0), .out(multiplexer_5_out));
  Multiplexer multiplexer_6 (.sel(Reset), .in_0(xor_7_out), .in_1(1'b0), .out(multiplexer_6_out));
  Multiplexer multiplexer_7 (.sel(Reset), .in_0(xor_8_out), .in_1(1'b0), .out(multiplexer_7_out));
  Multiplexer multiplexer_8 (.sel(Reset), .in_0(xor_9_out), .in_1(1'b0), .out(multiplexer_8_out));
  D_FF d_ff_1 (.D(multiplexer_1_out), .C(xor_1_out), .Q(Q_0));  // open: nQ
  D_FF d_ff_2 (.D(multiplexer_2_out), .C(xor_1_out), .Q(Q_1));  // open: nQ
  D_FF d_ff_3 (.D(multiplexer_3_out), .C(xor_1_out), .Q(Q_2));  // open: nQ
  D_FF d_ff_4 (.D(multiplexer_4_out), .C(xor_1_out), .Q(Q_3));  // open: nQ
  D_FF d_ff_5 (.D(multiplexer_5_out), .C(xor_1_out), .Q(Q_4));  // open: nQ
  D_FF d_ff_6 (.D(multiplexer_6_out), .C(xor_1_out), .Q(Q_5));  // open: nQ
  D_FF d_ff_7 (.D(multiplexer_7_out), .C(xor_1_out), .Q(Q_6));  // open: nQ
  D_FF d_ff_8 (.D(multiplexer_8_out), .C(xor_1_out), .Q(Q_7));  // open: nQ
endmodule
