// Digital circuit DataMemory.dig as structural Verilog
module DataMemory (
  input  A_0,
  input  A_1,
  input  A_2,
  input  A_3,
  input  A_4,
  input  A_5,
  input  A_6,
  input  A_7,
  input  A_8,
  input  A_9,
  input  A_10,
  input  A_11,
  input  A_12,
  input  A_13,
  input  A_14,
  input  A_15,
  input  WE,
  input  D_0,
  input  D_1,
  input  D_2,
  input  D_3,
  input  D_4,
  input  D_5,
  input  D_6,
  input  D_7,
  input  D_8,
  input  D_9,
  input  D_10,
  input  D_11,
  input  D_12,
  input  D_13,
  input  D_14,
  input  D_15,
  output OutData_0,
  output OutData_1,
  output OutData_2,
  output OutData_3,
  output OutData_4,
  output OutData_5,
  output OutData_6,
  output OutData_7,
  output OutData_8,
  output OutData_9,
  output OutData_10,
  output OutData_11,
  output OutData_12,
  output OutData_13,
  output OutData_14,
  output OutData_15
);

  // _28c010 _28c010_1: pin names not known; wires that end beside it: 1'b0, A_15, A_12, A_7, A_6, A_5, A_4, A_3, A_2, A_1, A_0, D_0, D_1, WE, A_14, A_13, A_8, A_9, A_11, A_10
  // _28c010 _28c010_2: pin names not known; wires that end beside it: D_2, 1'b0, A_15, A_12, A_7, A_6, A_5, A_4, A_3, A_2, A_1, A_0, D_8, D_9, D_10, WE, A_14, A_13, A_8, A_9, A_11, A_10
  Multiplexer multiplexer_1 (.sel(WE), .in_0(1'b0), .in_1(D_0), .out(OutData_0));
  Multiplexer multiplexer_2 (.sel(WE), .in_0(1'b0), .in_1(D_1), .out(OutData_1));
  Multiplexer multiplexer_3 (.sel(WE), .in_0(1'b0), .in_1(D_2), .out(OutData_2));
  Multiplexer multiplexer_4 (.sel(WE), .in_0(1'b0), .in_1(D_3), .out(OutData_3));
  Multiplexer multiplexer_5 (.sel(WE), .in_0(1'b0), .in_1(D_4), .out(OutData_4));
  Multiplexer multiplexer_6 (.sel(WE), .in_0(1'b0), .in_1(D_5), .out(OutData_5));
  Multiplexer multiplexer_7 (.sel(WE), .in_0(1'b0), .in_1(D_6), .out(OutData_6));
  Multiplexer multiplexer_8 (.sel(WE), .in_0(1'b0), .in_1(D_7), .out(OutData_7));
  Multiplexer multiplexer_9 (.sel(WE), .in_0(1'b0), .in_1(D_8), .out(OutData_8));
  Multiplexer multiplexer_10 (.sel(WE), .in_0(1'b0), .in_1(D_9), .out(OutData_9));
  Multiplexer multiplexer_11 (.sel(WE), .in_0(1'b0), .in_1(D_10), .out(OutData_10));
  Multiplexer multiplexer_12 (.sel(WE), .in_0(1'b0), .in_1(D_11), .out(OutData_11));
  Multiplexer multiplexer_13 (.sel(WE), .in_0(1'b0), .in_1(D_12), .out(OutData_12));
  Multiplexer multiplexer_14 (.sel(WE), .in_0(1'b0), .in_1(D_13), .out(OutData_13));
  Multiplexer multiplexer_15 (.sel(WE), .in_0(1'b0), .in_1(D_14), .out(OutData_14));
  Multiplexer multiplexer_16 (.sel(WE), .in_0(1'b0), .in_1(D_15), .out(OutData_15));
endmodule
