// Digital circuit Diviser.dig as structural Verilog
module Diviser (
  input  A_0,
  input  A_1,
  input  A_2,
  input  A_3,
  input  A_4,
  input  A_5,
  input  A_6,
  input  A_7,
  input  A_8,
  input  A_9,
  input  A_10,
  input  A_11,
  input  A_12,
  input  A_13,
  input  A_14,
  input  A_15,
  input  B_0,
  input  B_1,
  input  B_2,
  input  B_3,
  input  B_4,
  input  B_5,
  input  B_6,
  input  B_7,
  input  B_8,
  input  B_9,
  input  B_10,
  input  B_11,
  input  B_12,
  input  B_13,
  input  B_14,
  input  B_15,
  output Div_0,
  output Div_1,
  output Div_2,
  output Div_3,
  output Div_4,
  output Div_5,
  output Div_6,
  output Div_7,
  output Div_8,
  output Div_9,
  output Div_10,
  output Div_11,
  output Div_12,
  output Div_13,
  output Div_14,
  output Div_15
);

  Div #(.Bits(16)) u_div_1 (
    .a({A_15, A_14, A_13, A_12, A_11, A_10, A_9, A_8, A_7, A_6, A_5, A_4, A_3, A_2, A_1, A_0}),
    .b({B_15, B_14, B_13, B_12, B_11, B_10, B_9, B_8, B_7, B_6, B_5, B_4, B_3, B_2, B_1, B_0}),
    .q({Div_15, Div_14, Div_13, Div_12, Div_11, Div_10, Div_9, Div_8, Div_7, Div_6, Div_5, Div_4, Div_3, Div_2, Div_1, Div_0}));  // open: r
endmodule
