// Digital circuit Index_controller.dig as structural Verilog
module Index_controller (
  input  D_0,
  input  D_1,
  input  Reset,
  input  Increment,
  input  Override,
  output index_0,
  output index_1
);

  wire multiplexer_1_out, multiplexer_2_out, multiplexer_3_out, multiplexer_4_out, xor_1_out, xor_2_out,
       xor_3_out;

  xor xor_1 (xor_1_out, Reset, Increment);
  xor xor_2 (xor_2_out, index_0, 1'b1);
  xor xor_3 (xor_3_out, index_1, index_0);
  Multiplexer multiplexer_1 (.sel(Reset), .in_0(xor_2_out), .in_1(1'b0), .out(multiplexer_1_out));
  Multiplexer multiplexer_2 (.sel(Reset), .in_0(xor_3_out), .in_1(1'b0), .out(multiplexer_2_out));
  Multiplexer multiplexer_3 (.sel(Override), .in_0(multiplexer_1_out), .in_1(D_0), .out(multiplexer_3_out));
  Multiplexer multiplexer_4 (.sel(Override), .in_0(multiplexer_2_out), .in_1(D_1), .out(multiplexer_4_out));
  D_FF d_ff_1 (.D(multiplexer_3_out), .C(xor_1_out), .Q(index_0));  // open: nQ
  D_FF d_ff_2 (.D(multiplexer_4_out), .C(xor_1_out), .Q(index_1));  // open: nQ
endmodule
