// Digital circuit InstructionDecoder.dig as structural Verilog
module InstructionDecoder (
  input  CS_0,
  input  CS_1,
  input  CS_2,
  input  CS_3,
  input  T_verde,
  input  Emergency,
  input  emergency_0,
  input  emergency_1,
  input  emergency_2,
  input  emergency_3,
  input  cold,
  input  T_verde_lt_T_min,
  input  T_verde_gt_T_max,
  input  index__eq_3,
  input  Debit,
  input  Emergency_4,
  input  T_galben,
  input  BA_0,
  input  BA_1,
  input  BA_2,
  input  BA_3,
  input  BA_4,
  input  BA_5,
  input  CF_0,
  input  CF_1,
  input  CF_2,
  input  CF_3,
  input  CF_4,
  input  CF_5,
  input  CF_6,
  input  CF_7,
  input  CF_8,
  input  CF_9,
  input  CF_10,
  input  CF_11,
  output BranchingCond,
  output NextAddr_0,
  output NextAddr_1,
  output NextAddr_2,
  output NextAddr_3,
  output NextAddr_4,
  output NextAddr_5,
  output C_0,
  output C_1,
  output C_2,
  output C_3,
  output C_4,
  output C_5,
  output C_6,
  output C_7,
  output C_8,
  output C_9,
  output C_10,
  output C_11,
  output C_12,
  output C_13,
  output C_14,
  output C_15,
  output C_16,
  output C_17,
  output C_18,
  output C_19,
  output C_20,
  output C_21,
  output C_22,
  output C_23,
  output C_24
);

  wire not_1_out, not_2_out, not_3_out, not_4_out;

  not not_1 (not_1_out, Emergency);
  not not_2 (not_2_out, T_verde);
  not not_3 (not_3_out, Debit);
  not not_4 (not_4_out, T_galben);
  Multiplexer #(.Selector_Bits(4)) multiplexer_1 (
    .sel({CS_3, CS_2, CS_1, CS_0}), .in_0(1'b0), .in_1(not_2_out), .in_2(not_1_out), .in_3(emergency_0),
    .in_4(emergency_1), .in_5(emergency_2), .in_6(emergency_3), .in_7(cold), .in_8(T_verde_lt_T_min),
    .in_9(T_verde_gt_T_max), .in_10(index__eq_3), .in_11(not_3_out), .in_12(Emergency_4), .in_13(not_4_out),
    .in_14(1'b0), .in_15(1'b1), .out(BranchingCond));
  Decoder #(.Selector_Bits(4)) decoder_1 (
    .sel({CF_3, CF_2, CF_1, CF_0}), .out_1(C_0), .out_2(C_1), .out_3(C_4), .out_4(C_5), .out_5(C_6),
    .out_6(C_7), .out_7(C_8), .out_8(C_9), .out_9(C_16), .out_10(C_17), .out_11(C_18), .out_12(C_19),
    .out_13(C_20), .out_14(C_22), .out_15(C_23));  // open: out_0
  Decoder #(.Selector_Bits(2)) decoder_2 (.sel({CF_5, CF_4}), .out_1(C_2), .out_2(C_10), .out_3(C_21));  // open: out_0
  Decoder #(.Selector_Bits(2)) decoder_3 (.sel({CF_7, CF_6}), .out_1(C_11), .out_2(C_3), .out_3(C_24));  // open: out_0

  assign C_12 = CF_8;
  assign C_13 = CF_9;
  assign C_14 = CF_10;
  assign C_15 = CF_11;
  assign NextAddr_0 = BA_0;
  assign NextAddr_1 = BA_1;
  assign NextAddr_2 = BA_2;
  assign NextAddr_3 = BA_3;
  assign NextAddr_4 = BA_4;
  assign NextAddr_5 = BA_5;
endmodule
