// Digital circuit Memory.dig as structural Verilog
module Memory (
  input  A_0,
  input  A_1,
  input  A_2,
  input  A_3,
  input  A_4,
  input  A_5,
  input  A_6,
  input  A_7,
  input  A_8,
  input  A_9,
  input  A_10,
  input  A_11,
  input  A_12,
  input  A_13,
  input  A_14,
  input  A_15,
  output Q_7,
  output Q_6,
  output Q_5,
  output Q_4,
  output Q_3,
  output Q_0,
  output Q_1,
  output Q_2,
  output Q_15,
  output Q_14,
  output Q_13,
  output Q_12,
  output Q_11,
  output Q_8,
  output Q_9,
  output Q_10,
  output Q_21,
  output Q_20,
  output Q_19,
  output Q_18,
  output Q_16,
  output Q_17
);

  // _28c010 _28c010_1: pin names not known; wires that end beside it: A_15, A_12, A_7, A_6, A_5, A_4, A_3, A_2, A_1, A_0, Q_16, Q_17, Q_18, A_14, A_13, A_8, A_9, A_11, A_10
  // _28c010 _28c010_2: pin names not known; wires that end beside it: A_15, A_12, A_7, A_6, A_5, A_4, A_3, A_2, A_1, A_0, Q_8, Q_9, A_14, A_13, A_8, A_9, A_11, A_10
  // _28c010 _28c010_3: pin names not known; wires that end beside it: Q_10, A_15, A_12, A_7, A_6, A_5, A_4, A_3, A_2, A_1, A_0, Q_0, Q_1, Q_2, A_14, A_13, A_8, A_9, A_11, A_10
endmodule
