// Digital circuit Modulo.dig as structural Verilog
module Modulo (
  input  A_0,
  input  A_1,
  input  A_2,
  input  A_3,
  input  A_4,
  input  A_5,
  input  A_6,
  input  A_7,
  input  A_8,
  input  A_9,
  input  A_10,
  input  A_11,
  input  A_12,
  input  A_13,
  input  A_14,
  input  A_15,
  input  B_0,
  input  B_1,
  input  B_2,
  input  B_3,
  input  B_4,
  input  B_5,
  input  B_6,
  input  B_7,
  input  B_8,
  input  B_9,
  input  B_10,
  input  B_11,
  input  B_12,
  input  B_13,
  input  B_14,
  input  B_15,
  output Mod_0,
  output Mod_1,
  output Mod_2,
  output Mod_3,
  output Mod_4,
  output Mod_5,
  output Mod_6,
  output Mod_7,
  output Mod_8,
  output Mod_9,
  output Mod_10,
  output Mod_11,
  output Mod_12,
  output Mod_13,
  output Mod_14,
  output Mod_15
);

  Div #(.Bits(16)) div_1 (
    .a({A_15, A_14, A_13, A_12, A_11, A_10, A_9, A_8, A_7, A_6, A_5, A_4, A_3, A_2, A_1, A_0}),
    .b({B_15, B_14, B_13, B_12, B_11, B_10, B_9, B_8, B_7, B_6, B_5, B_4, B_3, B_2, B_1, B_0}),
    .r({Mod_15, Mod_14, Mod_13, Mod_12, Mod_11, Mod_10, Mod_9, Mod_8, Mod_7, Mod_6, Mod_5, Mod_4, Mod_3, Mod_2, Mod_1, Mod_0}));  // open: q
endmodule
