// Digital circuit Multiplier.dig as structural Verilog
module Multiplier (
  input  A_0,
  input  A_1,
  input  A_2,
  input  A_3,
  input  A_4,
  input  A_5,
  input  A_6,
  input  A_7,
  input  A_8,
  input  A_9,
  input  A_10,
  input  A_11,
  input  A_12,
  input  A_13,
  input  A_14,
  input  A_15,
  input  B_0,
  input  B_1,
  input  B_2,
  input  B_3,
  input  B_4,
  input  B_5,
  input  B_6,
  input  B_7,
  input  B_8,
  input  B_9,
  input  B_10,
  input  B_11,
  input  B_12,
  input  B_13,
  input  B_14,
  input  B_15,
  output Mul_0,
  output Mul_1,
  output Mul_2,
  output Mul_3,
  output Mul_4,
  output Mul_5,
  output Mul_6,
  output Mul_7,
  output Mul_8,
  output Mul_9,
  output Mul_10,
  output Mul_11,
  output Mul_12,
  output Mul_13,
  output Mul_14,
  output Mul_15
);

  wire [31:16] mul_1_mul;

  Mul #(.Bits(16)) u_mul_1 (
    .a({A_15, A_14, A_13, A_12, A_11, A_10, A_9, A_8, A_7, A_6, A_5, A_4, A_3, A_2, A_1, A_0}),
    .b({B_15, B_14, B_13, B_12, B_11, B_10, B_9, B_8, B_7, B_6, B_5, B_4, B_3, B_2, B_1, B_0}),
    .mul({mul_1_mul, Mul_15, Mul_14, Mul_13, Mul_12, Mul_11, Mul_10, Mul_9, Mul_8, Mul_7, Mul_6, Mul_5, Mul_4, Mul_3, Mul_2, Mul_1, Mul_0}));
endmodule
