// Digital circuit OperationSelect.dig as structural Verilog
module OperationSelect (
  input  Add,
  input  Sub,
  input  Mul,
  input  Div,
  input  Mov,
  input  And,
  input  Or,
  input  Xor,
  input  Not,
  input  Cmp,
  input  Inc,
  input  Dec,
  input  Mod,
  output SelOP_0,
  output SelOP_1,
  output SelOP_2,
  output SelOP_3
);

  wire add_11_c_o, multiplexer_1_out, multiplexer_2_out, multiplexer_3_out, multiplexer_4_out,
       multiplexer_5_out, multiplexer_6_out, multiplexer_7_out, multiplexer_8_out, multiplexer_9_out,
       multiplexer_10_out, multiplexer_11_out, multiplexer_12_out, multiplexer_13_out, nand_1_out, not_1_out,
       not_2_out, not_3_out, not_4_out;
  wire [1:0] add_1_s, add_2_s, add_3_s, add_4_s, add_5_s, add_6_s, add_7_s, add_8_s, add_9_s;
  wire [2:0] add_10_s;
  wire [2:2] add_7_c_o, add_8_c_o, add_9_c_o;
  wire [3:0] add_11_s;
  wire [3:3] add_10_c_o;

  Multiplexer multiplexer_1 (.sel(nand_1_out), .in_0(Add), .in_1(1'b0), .out(multiplexer_1_out));
  Multiplexer multiplexer_2 (.sel(nand_1_out), .in_0(Sub), .in_1(1'b0), .out(multiplexer_2_out));
  Multiplexer multiplexer_3 (.sel(nand_1_out), .in_0(Mul), .in_1(1'b0), .out(multiplexer_3_out));
  Multiplexer multiplexer_4 (.sel(nand_1_out), .in_0(Div), .in_1(1'b0), .out(multiplexer_4_out));
  Multiplexer multiplexer_5 (.sel(nand_1_out), .in_0(Mod), .in_1(1'b0), .out(multiplexer_5_out));
  Multiplexer multiplexer_6 (.sel(nand_1_out), .in_0(Mov), .in_1(1'b0), .out(multiplexer_6_out));
  Multiplexer multiplexer_7 (.sel(nand_1_out), .in_0(And), .in_1(1'b0), .out(multiplexer_7_out));
  Multiplexer multiplexer_8 (.sel(nand_1_out), .in_0(Or), .in_1(1'b0), .out(multiplexer_8_out));
  Multiplexer multiplexer_9 (.sel(nand_1_out), .in_0(Xor), .in_1(1'b0), .out(multiplexer_9_out));
  Multiplexer multiplexer_10 (.sel(nand_1_out), .in_0(Not), .in_1(1'b0), .out(multiplexer_10_out));
  Multiplexer multiplexer_11 (.sel(nand_1_out), .in_0(Cmp), .in_1(1'b0), .out(multiplexer_11_out));
  Multiplexer multiplexer_12 (.sel(nand_1_out), .in_0(Inc), .in_1(1'b0), .out(multiplexer_12_out));
  Multiplexer multiplexer_13 (.sel(nand_1_out), .in_0(Dec), .in_1(1'b0), .out(multiplexer_13_out));
  Add add_1 (.a(Div), .b(Mod), .c_i(Mov), .s(add_1_s[0]), .c_o(add_1_s[1]));
  Add add_2 (.a(And), .b(Or), .c_i(1'b0), .s(add_2_s[0]), .c_o(add_2_s[1]));
  Add add_3 (.a(Xor), .b(Not), .c_i(1'b0), .s(add_3_s[0]), .c_o(add_3_s[1]));
  Add add_4 (.a(Cmp), .b(Inc), .c_i(1'b0), .s(add_4_s[0]), .c_o(add_4_s[1]));
  Add add_5 (.a(Dec), .b(Mul), .c_i(1'b0), .s(add_5_s[0]), .c_o(add_5_s[1]));
  Add add_6 (.a(Sub), .b(Add), .c_i(1'b0), .s(add_6_s[0]), .c_o(add_6_s[1]));
  Add #(.Bits(2)) add_7 (.a(add_1_s), .b(add_2_s), .c_i(1'b0), .s(add_7_s), .c_o(add_7_c_o[2]));
  Add #(.Bits(2)) add_8 (.a(add_3_s), .b(add_4_s), .c_i(1'b0), .s(add_8_s), .c_o(add_8_c_o[2]));
  Add #(.Bits(2)) add_9 (.a(add_5_s), .b(add_6_s), .c_i(1'b0), .s(add_9_s), .c_o(add_9_c_o[2]));
  Add #(.Bits(3)) add_10 (
    .a({add_7_c_o[2], add_7_s}), .b({add_8_c_o[2], add_8_s}), .c_i(1'b0), .s(add_10_s), .c_o(add_10_c_o[3]));
  nand nand_1 (nand_1_out, add_11_s[0], not_4_out, not_3_out, not_2_out, not_1_out);
  Add #(.Bits(4)) add_11 (
    .a({add_10_c_o[3], add_10_s}), .b({1'b0, add_9_c_o[2], add_9_s}), .c_i(1'b0), .s(add_11_s),
    .c_o(add_11_c_o));
  not not_1 (not_1_out, add_11_c_o);
  not not_2 (not_2_out, add_11_s[3]);
  not not_3 (not_3_out, add_11_s[2]);
  not not_4 (not_4_out, add_11_s[1]);
  or or_1 (SelOP_0, multiplexer_1_out, multiplexer_3_out, multiplexer_5_out, multiplexer_7_out, multiplexer_9_out, multiplexer_11_out, multiplexer_13_out);
  or or_2 (SelOP_1, multiplexer_2_out, multiplexer_3_out, multiplexer_6_out, multiplexer_7_out, multiplexer_10_out, multiplexer_11_out);
  or or_3 (SelOP_2, multiplexer_4_out, multiplexer_5_out, multiplexer_6_out, multiplexer_7_out, multiplexer_12_out, multiplexer_13_out);
  or or_4 (SelOP_3, multiplexer_8_out, multiplexer_9_out, multiplexer_10_out, multiplexer_11_out, multiplexer_12_out, multiplexer_13_out);

  // Notes on the sheet:
  //   ● NOOP 0000 ok
  //   ● ADD  0001 ok
  //   ● SUB  0010 ok
  //   ● MUL  0011 ok
  //   ● DIV  0100 ok
  //   ● MOD  0101 ok
  //   ● MOV  0110 ok
  //   ● AND  0111 ok
  //   ● OR   1000 ok
  //   ● XOR  1001 ok
  //   ● NOT  1010 ok
  //   ● CMP  1011 ok
  //   ● INC  1100 ok
  //   ● DEC  1101 ok
endmodule
