// Digital circuit Program_Counter.dig as structural Verilog
module Program_Counter (
  input  JumpAddr_0,
  input  Clock,
  input  Reset,
  input  JumpAddr_1,
  input  JumpAddr_2,
  input  JumpAddr_3,
  input  JumpAddr_4,
  input  JumpAddr_5,
  input  JumpAddr_6,
  input  JumpAddr_7,
  input  JumpAddr_8,
  input  JumpAddr_9,
  input  JumpAddr_10,
  input  JumpAddr_11,
  input  JumpAddr_12,
  input  JumpAddr_13,
  input  JumpAddr_14,
  input  JumpAddr_15,
  output PC_0,
  output PC_1,
  output PC_2,
  output PC_3,
  output PC_4,
  output PC_5,
  output PC_6,
  output PC_7,
  output PC_8,
  output PC_9,
  output PC_10,
  output PC_11,
  output PC_12,
  output PC_13,
  output PC_14,
  output PC_15
);

  wire multiplexer_1_out, multiplexer_2_out, multiplexer_3_out, multiplexer_4_out, multiplexer_5_out,
       multiplexer_6_out, multiplexer_7_out, multiplexer_8_out, multiplexer_9_out, multiplexer_10_out,
       multiplexer_11_out, multiplexer_12_out, multiplexer_13_out, multiplexer_14_out, multiplexer_15_out,
       multiplexer_16_out, xor_1_out;

  xor xor_1 (xor_1_out, Reset, Clock);
  Multiplexer multiplexer_1 (.sel(Reset), .in_0(JumpAddr_0), .in_1(1'b0), .out(multiplexer_1_out));
  Multiplexer multiplexer_2 (.sel(Reset), .in_0(JumpAddr_1), .in_1(1'b0), .out(multiplexer_2_out));
  Multiplexer multiplexer_3 (.sel(Reset), .in_0(JumpAddr_2), .in_1(1'b0), .out(multiplexer_3_out));
  Multiplexer multiplexer_4 (.sel(Reset), .in_0(JumpAddr_3), .in_1(1'b0), .out(multiplexer_4_out));
  Multiplexer multiplexer_5 (.sel(Reset), .in_0(JumpAddr_4), .in_1(1'b0), .out(multiplexer_5_out));
  Multiplexer multiplexer_6 (.sel(Reset), .in_0(JumpAddr_5), .in_1(1'b0), .out(multiplexer_6_out));
  Multiplexer multiplexer_7 (.sel(Reset), .in_0(JumpAddr_6), .in_1(1'b0), .out(multiplexer_7_out));
  Multiplexer multiplexer_8 (.sel(Reset), .in_0(JumpAddr_7), .in_1(1'b0), .out(multiplexer_8_out));
  Multiplexer multiplexer_9 (.sel(Reset), .in_0(JumpAddr_8), .in_1(1'b0), .out(multiplexer_9_out));
  Multiplexer multiplexer_10 (.sel(Reset), .in_0(JumpAddr_9), .in_1(1'b0), .out(multiplexer_10_out));
  Multiplexer multiplexer_11 (.sel(Reset), .in_0(JumpAddr_10), .in_1(1'b0), .out(multiplexer_11_out));
  Multiplexer multiplexer_12 (.sel(Reset), .in_0(JumpAddr_11), .in_1(1'b0), .out(multiplexer_12_out));
  Multiplexer multiplexer_13 (.sel(Reset), .in_0(JumpAddr_12), .in_1(1'b0), .out(multiplexer_13_out));
  Multiplexer multiplexer_14 (.sel(Reset), .in_0(JumpAddr_13), .in_1(1'b0), .out(multiplexer_14_out));
  Multiplexer multiplexer_15 (.sel(Reset), .in_0(JumpAddr_14), .in_1(1'b0), .out(multiplexer_15_out));
  Multiplexer multiplexer_16 (.sel(Reset), .in_0(JumpAddr_15), .in_1(1'b0), .out(multiplexer_16_out));
  D_FF d_ff_1 (.D(multiplexer_1_out), .C(xor_1_out), .Q(PC_0));  // open: nQ
  D_FF d_ff_2 (.D(multiplexer_2_out), .C(xor_1_out), .Q(PC_1));  // open: nQ
  D_FF d_ff_3 (.D(multiplexer_3_out), .C(xor_1_out), .Q(PC_2));  // open: nQ
  D_FF d_ff_4 (.D(multiplexer_4_out), .C(xor_1_out), .Q(PC_3));  // open: nQ
  D_FF d_ff_5 (.D(multiplexer_5_out), .C(xor_1_out), .Q(PC_4));  // open: nQ
  D_FF d_ff_6 (.D(multiplexer_6_out), .C(xor_1_out), .Q(PC_5));  // open: nQ
  D_FF d_ff_7 (.D(multiplexer_7_out), .C(xor_1_out), .Q(PC_6));  // open: nQ
  D_FF d_ff_8 (.D(multiplexer_8_out), .C(xor_1_out), .Q(PC_7));  // open: nQ
  D_FF d_ff_9 (.D(multiplexer_9_out), .C(xor_1_out), .Q(PC_8));  // open: nQ
  D_FF d_ff_10 (.D(multiplexer_10_out), .C(xor_1_out), .Q(PC_9));  // open: nQ
  D_FF d_ff_11 (.D(multiplexer_11_out), .C(xor_1_out), .Q(PC_10));  // open: nQ
  D_FF d_ff_12 (.D(multiplexer_12_out), .C(xor_1_out), .Q(PC_11));  // open: nQ
  D_FF d_ff_13 (.D(multiplexer_13_out), .C(xor_1_out), .Q(PC_12));  // open: nQ
  D_FF d_ff_14 (.D(multiplexer_14_out), .C(xor_1_out), .Q(PC_13));  // open: nQ
  D_FF d_ff_15 (.D(multiplexer_15_out), .C(xor_1_out), .Q(PC_14));  // open: nQ
  D_FF d_ff_16 (.D(multiplexer_16_out), .C(xor_1_out), .Q(PC_15));  // open: nQ
endmodule
