// Digital circuit Semafor.dig as structural Verilog
module Semafor (
  input  Enable_counters,
  input  Reset_counters,
  input  Async_counter2,
  input  Async_counter3,
  input  Async_counter1,
  input  Flag_sensor1,
  input  Flag_sensor2,
  input  Flag_sensor3,
  input  Emergency_sensor,
  input  Set_verde,
  input  Set_galben,
  input  Set_rosu,
  input  Begin,
  output Q_0_0,
  output Q_0_1,
  output Q_0_2,
  output Q_0_3,
  output Q_0_4,
  output Q_0_5,
  output Q_0_6,
  output Q_0_7,
  output Q_1_0,
  output Q_1_1,
  output Q_1_2,
  output Q_1_3,
  output Q_1_4,
  output Q_1_5,
  output Q_1_6,
  output Q_1_7,
  output Q_2_0,
  output Q_2_1,
  output Q_2_2,
  output Q_2_3,
  output Q_2_4,
  output Q_2_5,
  output Q_2_6,
  output Q_2_7,
  output Flag_1,
  output Flag_2,
  output Flag_3,
  output Emergency,
  output Color_green,
  output Color_yellow,
  output Color_red
);

  wire or_1_out, or_2_out, or_3_out, xor_1_out;

  or or_1 (or_1_out, Set_galben, Set_rosu);
  or or_2 (or_2_out, Set_verde, Set_rosu);
  or or_3 (or_3_out, Set_verde, Set_galben);
  Counter_Async counter_async_1 (
    .Enable(Enable_counters), .Reset(Async_counter1), .Clock(Reset_counters), .Q_0(Q_0_0), .Q_1(Q_0_1),
    .Q_2(Q_0_2), .Q_3(Q_0_3), .Q_4(Q_0_4), .Q_5(Q_0_5), .Q_6(Q_0_6), .Q_7(Q_0_7));
  Counter_Async counter_async_2 (
    .Enable(Enable_counters), .Reset(Async_counter2), .Clock(Reset_counters), .Q_0(Q_1_0), .Q_1(Q_1_1),
    .Q_2(Q_1_2), .Q_3(Q_1_3), .Q_4(Q_1_4), .Q_5(Q_1_5), .Q_6(Q_1_6), .Q_7(Q_1_7));
  Counter_Async counter_async_3 (
    .Enable(Enable_counters), .Reset(Async_counter3), .Clock(Reset_counters), .Q_0(Q_2_0), .Q_1(Q_2_1),
    .Q_2(Q_2_2), .Q_3(Q_2_3), .Q_4(Q_2_4), .Q_5(Q_2_5), .Q_6(Q_2_6), .Q_7(Q_2_7));
  RS_FF_AS rs_ff_as_1 (.S(Set_verde), .R(or_1_out), .Q(Color_green));  // open: nQ
  RS_FF_AS rs_ff_as_2 (.S(Set_galben), .R(or_2_out), .Q(Color_yellow));  // open: nQ
  xor xor_1 (xor_1_out, Begin, Set_rosu);
  RS_FF_AS rs_ff_as_3 (.S(xor_1_out), .R(or_3_out), .Q(Color_red));  // open: nQ

  assign Emergency = Emergency_sensor;
  assign Flag_1 = Flag_sensor1;
  assign Flag_2 = Flag_sensor2;
  assign Flag_3 = Flag_sensor3;
endmodule
