// Digital circuit Substracter.dig as structural Verilog
module Substracter (
  input  A_0,
  input  A_1,
  input  A_2,
  input  A_3,
  input  A_4,
  input  A_5,
  input  A_6,
  input  A_7,
  input  A_8,
  input  A_9,
  input  A_10,
  input  A_11,
  input  A_12,
  input  A_13,
  input  A_14,
  input  A_15,
  input  B_0,
  input  B_1,
  input  B_2,
  input  B_3,
  input  B_4,
  input  B_5,
  input  B_6,
  input  B_7,
  input  B_8,
  input  B_9,
  input  B_10,
  input  B_11,
  input  B_12,
  input  B_13,
  input  B_14,
  input  B_15,
  input  Carry_in,
  output Carry_out,
  output Sub_0,
  output Sub_1,
  output Sub_2,
  output Sub_3,
  output Sub_4,
  output Sub_5,
  output Sub_6,
  output Sub_7,
  output Sub_8,
  output Sub_9,
  output Sub_10,
  output Sub_11,
  output Sub_12,
  output Sub_13,
  output Sub_14,
  output Sub_15,
  output Zero
);

  wire or_1_out, sub_1_c_o, sub_2_c_o, sub_3_c_o, sub_4_c_o, sub_5_c_o, sub_6_c_o, sub_7_c_o, sub_8_c_o,
       sub_9_c_o, sub_10_c_o, sub_11_c_o, sub_12_c_o, sub_13_c_o, sub_14_c_o, sub_15_c_o;

  Sub u_sub_1 (.a(A_0), .b(B_0), .c_i(Carry_in), .s(Sub_0), .c_o(sub_1_c_o));
  Sub u_sub_2 (.a(A_1), .b(B_1), .c_i(sub_1_c_o), .s(Sub_1), .c_o(sub_2_c_o));
  Sub u_sub_3 (.a(A_2), .b(B_2), .c_i(sub_2_c_o), .s(Sub_2), .c_o(sub_3_c_o));
  Sub u_sub_4 (.a(A_3), .b(B_3), .c_i(sub_3_c_o), .s(Sub_3), .c_o(sub_4_c_o));
  Sub u_sub_5 (.a(A_4), .b(B_4), .c_i(sub_4_c_o), .s(Sub_4), .c_o(sub_5_c_o));
  Sub u_sub_6 (.a(A_5), .b(B_5), .c_i(sub_5_c_o), .s(Sub_5), .c_o(sub_6_c_o));
  Sub u_sub_7 (.a(A_6), .b(B_6), .c_i(sub_6_c_o), .s(Sub_6), .c_o(sub_7_c_o));
  Sub u_sub_8 (.a(A_7), .b(B_7), .c_i(sub_7_c_o), .s(Sub_7), .c_o(sub_8_c_o));
  Sub u_sub_9 (.a(A_8), .b(B_8), .c_i(sub_8_c_o), .s(Sub_8), .c_o(sub_9_c_o));
  Sub u_sub_10 (.a(A_9), .b(B_9), .c_i(sub_9_c_o), .s(Sub_9), .c_o(sub_10_c_o));
  Sub u_sub_11 (.a(A_10), .b(B_10), .c_i(sub_10_c_o), .s(Sub_10), .c_o(sub_11_c_o));
  Sub u_sub_12 (.a(A_11), .b(B_11), .c_i(sub_11_c_o), .s(Sub_10), .c_o(sub_12_c_o));
  Sub u_sub_13 (.a(A_12), .b(B_12), .c_i(sub_12_c_o), .s(Sub_12), .c_o(sub_13_c_o));
  Sub u_sub_14 (.a(A_13), .b(B_13), .c_i(sub_13_c_o), .s(Sub_13), .c_o(sub_14_c_o));
  Sub u_sub_15 (.a(A_14), .b(B_14), .c_i(sub_14_c_o), .s(Sub_14), .c_o(sub_15_c_o));
  Sub sub_16 (.a(A_15), .b(B_15), .c_i(sub_15_c_o), .s(Sub_15), .c_o(Carry_out));
  or or_1 (or_1_out, Sub_10, Sub_15, Sub_14, Sub_13, Sub_12, Sub_10, Sub_9, Sub_8, Sub_7, Sub_6, Sub_5, Sub_4, Sub_3, Sub_2, Sub_1, Sub_0);
  not not_1 (Zero, or_1_out);

  assign Sub_11 = Sub_10;
endmodule
