// Digital circuit decounter.dig as structural Verilog
module decounter (
  input  D_0,
  input  NewInput,
  input  Decrement,
  input  D_1,
  input  D_2,
  input  D_3,
  output Q_0,
  output Q_1,
  output Q_2,
  output Q_3
);

  wire d_ff_1_nq, d_ff_2_nq, d_ff_3_nq, d_ff_4_nq, multiplexer_1_out, multiplexer_2_out, multiplexer_3_out,
       multiplexer_4_out;

  Multiplexer multiplexer_1 (.sel(NewInput), .in_0(d_ff_1_nq), .in_1(D_0), .out(multiplexer_1_out));
  Multiplexer multiplexer_2 (.sel(NewInput), .in_0(d_ff_2_nq), .in_1(D_1), .out(multiplexer_2_out));
  Multiplexer multiplexer_3 (.sel(NewInput), .in_0(d_ff_3_nq), .in_1(D_2), .out(multiplexer_3_out));
  Multiplexer multiplexer_4 (.sel(NewInput), .in_0(d_ff_4_nq), .in_1(D_3), .out(multiplexer_4_out));
  D_FF d_ff_1 (.D(multiplexer_1_out), .C(Decrement), .Q(Q_0), .nQ(d_ff_1_nq));
  D_FF d_ff_2 (.D(multiplexer_2_out), .C(Q_0), .Q(Q_1), .nQ(d_ff_2_nq));
  D_FF d_ff_3 (.D(multiplexer_3_out), .C(Q_1), .Q(Q_2), .nQ(d_ff_3_nq));
  D_FF d_ff_4 (.D(multiplexer_4_out), .C(Q_2), .Q(Q_3), .nQ(d_ff_4_nq));
endmodule
