// Digital circuit general_purpose_registers.dig as structural Verilog
module general_purpose_registers (
  input  R_1_0,
  input  R_1_1,
  input  R_1_2,
  input  R_1_3,
  input  R_1_4,
  input  R_1_5,
  input  R_1_6,
  input  R_1_7,
  input  R_1_8,
  input  R_1_9,
  input  R_1_10,
  input  R_1_11,
  input  R_1_12,
  input  R_1_13,
  input  R_1_14,
  input  R_1_15,
  input  R_2_0,
  input  R_2_1,
  input  R_2_2,
  input  R_2_3,
  input  R_2_4,
  input  R_2_5,
  input  R_2_6,
  input  R_2_7,
  input  R_2_8,
  input  R_2_9,
  input  R_2_10,
  input  R_2_11,
  input  R_2_12,
  input  R_2_13,
  input  R_2_14,
  input  R_2_15,
  input  R_3_0,
  input  R_3_1,
  input  R_3_2,
  input  R_3_3,
  input  R_3_4,
  input  R_3_5,
  input  R_3_6,
  input  R_3_7,
  input  R_3_8,
  input  R_3_9,
  input  R_3_10,
  input  R_3_11,
  input  R_3_12,
  input  R_3_13,
  input  R_3_14,
  input  R_3_15,
  input  R_4_0,
  input  R_4_1,
  input  R_4_2,
  input  R_4_3,
  input  R_4_4,
  input  R_4_5,
  input  R_4_6,
  input  R_4_7,
  input  R_4_8,
  input  R_4_9,
  input  R_4_10,
  input  R_4_11,
  input  R_4_12,
  input  R_4_13,
  input  R_4_14,
  input  R_4_15,
  input  R_5_0,
  input  R_5_1,
  input  R_5_2,
  input  R_5_3,
  input  R_5_4,
  input  R_5_5,
  input  R_5_6,
  input  R_5_7,
  input  R_5_8,
  input  R_5_9,
  input  R_5_10,
  input  R_5_11,
  input  R_5_12,
  input  R_5_13,
  input  R_5_14,
  input  R_5_15,
  input  R_6_0,
  input  R_6_1,
  input  R_6_2,
  input  R_6_3,
  input  R_6_4,
  input  R_6_5,
  input  R_6_6,
  input  R_6_7,
  input  R_6_8,
  input  R_6_9,
  input  R_6_10,
  input  R_6_11,
  input  R_6_12,
  input  R_6_13,
  input  R_6_14,
  input  R_6_15,
  input  R_7_0,
  input  R_7_1,
  input  R_7_2,
  input  R_7_3,
  input  R_7_4,
  input  R_7_5,
  input  R_7_6,
  input  R_7_7,
  input  R_7_8,
  input  R_7_9,
  input  R_7_10,
  input  R_7_11,
  input  R_7_12,
  input  R_7_13,
  input  R_7_14,
  input  R_7_15,
  input  R_8_0,
  input  R_8_1,
  input  R_8_2,
  input  R_8_3,
  input  R_8_4,
  input  R_8_5,
  input  R_8_6,
  input  R_8_7,
  input  R_8_8,
  input  R_8_9,
  input  R_8_10,
  input  R_8_11,
  input  R_8_12,
  input  R_8_13,
  input  R_8_14,
  input  R_8_15,
  input  clk,
  input  rst,
  output R_1_out_0,
  output R_1_out_1,
  output R_1_out_2,
  output R_1_out_3,
  output R_1_out_4,
  output R_1_out_5,
  output R_1_out_6,
  output R_1_out_7,
  output R_1_out_8,
  output R_1_out_9,
  output R_1_out_10,
  output R_1_out_11,
  output R_1_out_12,
  output R_1_out_13,
  output R_1_out_14,
  output R_1_out_15,
  output R_2_out_0,
  output R_2_out_1,
  output R_2_out_2,
  output R_2_out_3,
  output R_2_out_4,
  output R_2_out_5,
  output R_2_out_6,
  output R_2_out_7,
  output R_2_out_8,
  output R_2_out_9,
  output R_2_out_10,
  output R_2_out_11,
  output R_2_out_12,
  output R_2_out_13,
  output R_2_out_14,
  output R_2_out_15,
  output R_3_out_0,
  output R_3_out_1,
  output R_3_out_2,
  output R_3_out_3,
  output R_3_out_4,
  output R_3_out_5,
  output R_3_out_6,
  output R_3_out_7,
  output R_3_out_8,
  output R_3_out_9,
  output R_3_out_10,
  output R_3_out_11,
  output R_3_out_12,
  output R_3_out_13,
  output R_3_out_14,
  output R_3_out_15,
  output R_4_out_0,
  output R_4_out_1,
  output R_4_out_2,
  output R_4_out_3,
  output R_4_out_4,
  output R_4_out_5,
  output R_4_out_6,
  output R_4_out_7,
  output R_4_out_8,
  output R_4_out_9,
  output R_4_out_10,
  output R_4_out_11,
  output R_4_out_12,
  output R_4_out_13,
  output R_4_out_14,
  output R_4_out_15,
  output R_5_out_0,
  output R_5_out_1,
  output R_5_out_2,
  output R_5_out_3,
  output R_5_out_4,
  output R_5_out_5,
  output R_5_out_6,
  output R_5_out_7,
  output R_5_out_8,
  output R_5_out_9,
  output R_5_out_10,
  output R_5_out_11,
  output R_5_out_12,
  output R_5_out_13,
  output R_5_out_14,
  output R_5_out_15,
  output R_6_out_0,
  output R_6_out_1,
  output R_6_out_2,
  output R_6_out_3,
  output R_6_out_4,
  output R_6_out_5,
  output R_6_out_6,
  output R_6_out_7,
  output R_6_out_8,
  output R_6_out_9,
  output R_6_out_10,
  output R_6_out_11,
  output R_6_out_12,
  output R_6_out_13,
  output R_6_out_14,
  output R_6_out_15,
  output R_7_out_0,
  output R_7_out_1,
  output R_7_out_2,
  output R_7_out_3,
  output R_7_out_4,
  output R_7_out_5,
  output R_7_out_6,
  output R_7_out_7,
  output R_7_out_8,
  output R_7_out_9,
  output R_7_out_10,
  output R_7_out_11,
  output R_7_out_12,
  output R_7_out_13,
  output R_7_out_14,
  output R_7_out_15,
  output R_8_out_0,
  output R_8_out_1,
  output R_8_out_2,
  output R_8_out_3,
  output R_8_out_4,
  output R_8_out_5,
  output R_8_out_6,
  output R_8_out_7,
  output R_8_out_8,
  output R_8_out_9,
  output R_8_out_10,
  output R_8_out_11,
  output R_8_out_12,
  output R_8_out_13,
  output R_8_out_14,
  output R_8_out_15
);

  _16bit_register _16bit_register_1 (
    .D_0(R_1_0), .D_1(R_1_1), .D_2(R_1_2), .D_3(R_1_3), .D_4(R_1_4), .D_5(R_1_5), .D_6(R_1_6), .D_7(R_1_7),
    .D_8(R_1_8), .D_9(R_1_9), .D_10(R_1_10), .D_11(R_1_11), .D_12(R_1_12), .D_13(R_1_13), .D_14(R_1_14),
    .D_15(R_1_15), .Reset(rst), .Clock(clk), .Q_0(R_1_out_0), .Q_1(R_1_out_1), .Q_2(R_1_out_2),
    .Q_3(R_1_out_3), .Q_4(R_1_out_4), .Q_5(R_1_out_5), .Q_6(R_1_out_6), .Q_7(R_1_out_7), .Q_8(R_1_out_8),
    .Q_9(R_1_out_9), .Q_10(R_1_out_10), .Q_11(R_1_out_11), .Q_12(R_1_out_12), .Q_13(R_1_out_13),
    .Q_14(R_1_out_14), .Q_15(R_1_out_15));
  _16bit_register _16bit_register_2 (
    .D_0(R_2_0), .D_1(R_2_1), .D_2(R_2_2), .D_3(R_2_3), .D_4(R_2_4), .D_5(R_2_5), .D_6(R_2_6), .D_7(R_2_7),
    .D_8(R_2_8), .D_9(R_2_9), .D_10(R_2_10), .D_11(R_2_11), .D_12(R_2_12), .D_13(R_2_13), .D_14(R_2_14),
    .D_15(R_2_15), .Reset(rst), .Clock(clk), .Q_0(R_2_out_0), .Q_1(R_2_out_1), .Q_2(R_2_out_2),
    .Q_3(R_2_out_3), .Q_4(R_2_out_4), .Q_5(R_2_out_5), .Q_6(R_2_out_6), .Q_7(R_2_out_7), .Q_8(R_2_out_8),
    .Q_9(R_2_out_9), .Q_10(R_2_out_10), .Q_11(R_2_out_11), .Q_12(R_2_out_12), .Q_13(R_2_out_13),
    .Q_14(R_2_out_14), .Q_15(R_2_out_15));
  _16bit_register _16bit_register_3 (
    .D_0(R_3_0), .D_1(R_3_1), .D_2(R_3_2), .D_3(R_3_3), .D_4(R_3_4), .D_5(R_3_5), .D_6(R_3_6), .D_7(R_3_7),
    .D_8(R_3_8), .D_9(R_3_9), .D_10(R_3_10), .D_11(R_3_11), .D_12(R_3_12), .D_13(R_3_13), .D_14(R_3_14),
    .D_15(R_3_15), .Reset(rst), .Clock(clk), .Q_0(R_3_out_0), .Q_1(R_3_out_1), .Q_2(R_3_out_2),
    .Q_3(R_3_out_3), .Q_4(R_3_out_4), .Q_5(R_3_out_5), .Q_6(R_3_out_6), .Q_7(R_3_out_7), .Q_8(R_3_out_8),
    .Q_9(R_3_out_9), .Q_10(R_3_out_10), .Q_11(R_3_out_11), .Q_12(R_3_out_12), .Q_13(R_3_out_13),
    .Q_14(R_3_out_14), .Q_15(R_3_out_15));
  _16bit_register _16bit_register_4 (
    .D_0(R_4_0), .D_1(R_4_1), .D_2(R_4_2), .D_3(R_4_3), .D_4(R_4_4), .D_5(R_4_5), .D_6(R_4_6), .D_7(R_4_7),
    .D_8(R_4_8), .D_9(R_4_9), .D_10(R_4_10), .D_11(R_4_11), .D_12(R_4_12), .D_13(R_4_13), .D_14(R_4_14),
    .D_15(R_4_15), .Reset(rst), .Clock(clk), .Q_0(R_4_out_0), .Q_1(R_4_out_1), .Q_2(R_4_out_2),
    .Q_3(R_4_out_3), .Q_4(R_4_out_4), .Q_5(R_4_out_5), .Q_6(R_4_out_6), .Q_7(R_4_out_7), .Q_8(R_4_out_8),
    .Q_9(R_4_out_9), .Q_10(R_4_out_10), .Q_11(R_4_out_11), .Q_12(R_4_out_12), .Q_13(R_4_out_13),
    .Q_14(R_4_out_14), .Q_15(R_4_out_15));
  _16bit_register _16bit_register_5 (
    .D_0(R_5_0), .D_1(R_5_1), .D_2(R_5_2), .D_3(R_5_3), .D_4(R_5_4), .D_5(R_5_5), .D_6(R_5_6), .D_7(R_5_7),
    .D_8(R_5_8), .D_9(R_5_9), .D_10(R_5_10), .D_11(R_5_11), .D_12(R_5_12), .D_13(R_5_13), .D_14(R_5_14),
    .D_15(R_5_15), .Reset(rst), .Clock(clk), .Q_0(R_5_out_0), .Q_1(R_5_out_1), .Q_2(R_5_out_2),
    .Q_3(R_5_out_3), .Q_4(R_5_out_4), .Q_5(R_5_out_5), .Q_6(R_5_out_6), .Q_7(R_5_out_7), .Q_8(R_5_out_8),
    .Q_9(R_5_out_9), .Q_10(R_5_out_10), .Q_11(R_5_out_11), .Q_12(R_5_out_12), .Q_13(R_5_out_13),
    .Q_14(R_5_out_14), .Q_15(R_5_out_15));
  _16bit_register _16bit_register_6 (
    .D_0(R_6_0), .D_1(R_6_1), .D_2(R_6_2), .D_3(R_6_3), .D_4(R_6_4), .D_5(R_6_5), .D_6(R_6_6), .D_7(R_6_7),
    .D_8(R_6_8), .D_9(R_6_9), .D_10(R_6_10), .D_11(R_6_11), .D_12(R_6_12), .D_13(R_6_13), .D_14(R_6_14),
    .D_15(R_6_15), .Reset(rst), .Clock(clk), .Q_0(R_6_out_0), .Q_1(R_6_out_1), .Q_2(R_6_out_2),
    .Q_3(R_6_out_3), .Q_4(R_6_out_4), .Q_5(R_6_out_5), .Q_6(R_6_out_6), .Q_7(R_6_out_7), .Q_8(R_6_out_8),
    .Q_9(R_6_out_9), .Q_10(R_6_out_10), .Q_11(R_6_out_11), .Q_12(R_6_out_12), .Q_13(R_6_out_13),
    .Q_14(R_6_out_14), .Q_15(R_6_out_15));
  _16bit_register _16bit_register_7 (
    .D_0(R_7_0), .D_1(R_7_1), .D_2(R_7_2), .D_3(R_7_3), .D_4(R_7_4), .D_5(R_7_5), .D_6(R_7_6), .D_7(R_7_7),
    .D_8(R_7_8), .D_9(R_7_9), .D_10(R_7_10), .D_11(R_7_11), .D_12(R_7_12), .D_13(R_7_13), .D_14(R_7_14),
    .D_15(R_7_15), .Reset(rst), .Clock(clk), .Q_0(R_7_out_0), .Q_1(R_7_out_1), .Q_2(R_7_out_2),
    .Q_3(R_7_out_3), .Q_4(R_7_out_4), .Q_5(R_7_out_5), .Q_6(R_7_out_6), .Q_7(R_7_out_7), .Q_8(R_7_out_8),
    .Q_9(R_7_out_9), .Q_10(R_7_out_10), .Q_11(R_7_out_11), .Q_12(R_7_out_12), .Q_13(R_7_out_13),
    .Q_14(R_7_out_14), .Q_15(R_7_out_15));
  _16bit_register _16bit_register_8 (
    .D_0(R_8_0), .D_1(R_8_1), .D_2(R_8_2), .D_3(R_8_3), .D_4(R_8_4), .D_5(R_8_5), .D_6(R_8_6), .D_7(R_8_7),
    .D_8(R_8_8), .D_9(R_8_9), .D_10(R_8_10), .D_11(R_8_11), .D_12(R_8_12), .D_13(R_8_13), .D_14(R_8_14),
    .D_15(R_8_15), .Reset(rst), .Clock(clk), .Q_0(R_8_out_0), .Q_1(R_8_out_1), .Q_2(R_8_out_2),
    .Q_3(R_8_out_3), .Q_4(R_8_out_4), .Q_5(R_8_out_5), .Q_6(R_8_out_6), .Q_7(R_8_out_7), .Q_8(R_8_out_8),
    .Q_9(R_8_out_9), .Q_10(R_8_out_10), .Q_11(R_8_out_11), .Q_12(R_8_out_12), .Q_13(R_8_out_13),
    .Q_14(R_8_out_14), .Q_15(R_8_out_15));
endmodule
