// Digital circuit index_counter.dig as structural Verilog
module index_counter (
  input  Reset,
  input  Increment,
  output index_0,
  output index_1
);

  wire multiplexer_1_out, multiplexer_2_out, xor_1_out, xor_2_out, xor_3_out;

  xor xor_1 (xor_1_out, index_0, 1'b1);
  xor xor_2 (xor_2_out, index_1, index_0);
  xor xor_3 (xor_3_out, Reset, Increment);
  Multiplexer multiplexer_1 (.sel(Reset), .in_0(xor_1_out), .in_1(1'b0), .out(multiplexer_1_out));
  Multiplexer multiplexer_2 (.sel(Reset), .in_0(xor_2_out), .in_1(1'b0), .out(multiplexer_2_out));
  D_FF d_ff_1 (.D(multiplexer_1_out), .C(xor_3_out), .Q(index_0));  // open: nQ
  D_FF d_ff_2 (.D(multiplexer_2_out), .C(xor_3_out), .Q(index_1));  // open: nQ
endmodule
