// Digital circuit index_incrementer.dig as structural Verilog
module index_incrementer (
  input  C_6,
  input  C_7,
  input  C_8,
  output increment_0,
  output increment_1
);

  or or_1 (increment_0, C_6, C_8);
  or or_2 (increment_1, C_7, C_8);
endmodule
