// Digital circuit not_16_bit.dig as structural Verilog
module not_16_bit (
  input  A_0,
  input  A_1,
  input  A_2,
  input  A_3,
  input  A_4,
  input  A_5,
  input  A_6,
  input  A_7,
  input  A_8,
  input  A_9,
  input  A_10,
  input  A_11,
  input  A_12,
  input  A_13,
  input  A_14,
  input  A_15,
  output Not_0,
  output Not_1,
  output Not_2,
  output Not_3,
  output Not_4,
  output Not_5,
  output Not_6,
  output Not_7,
  output Not_8,
  output Not_9,
  output Not_10,
  output Not_11,
  output Not_12,
  output Not_13,
  output Not_14,
  output Not_15
);

  not u_not_1 (Not_0, A_0);
  not u_not_2 (Not_1, A_1);
  not u_not_3 (Not_2, A_2);
  not u_not_4 (Not_3, A_3);
  not u_not_5 (Not_4, A_4);
  not u_not_6 (Not_5, A_5);
  not u_not_7 (Not_6, A_6);
  not u_not_8 (Not_7, A_7);
  not u_not_9 (Not_8, A_8);
  not u_not_10 (Not_9, A_9);
  not u_not_11 (Not_10, A_10);
  not u_not_12 (Not_11, A_11);
  not u_not_13 (Not_12, A_12);
  not u_not_14 (Not_13, A_13);
  not u_not_15 (Not_14, A_14);
  not not_16 (Not_15, A_15);
endmodule
