// Digital circuit xor_16_bit.dig as structural Verilog
module xor_16_bit (
  input  A_0,
  input  A_1,
  input  A_2,
  input  A_3,
  input  A_4,
  input  A_5,
  input  A_6,
  input  A_7,
  input  A_8,
  input  A_9,
  input  A_10,
  input  A_11,
  input  A_12,
  input  A_13,
  input  A_14,
  input  A_15,
  input  B_0,
  input  B_1,
  input  B_2,
  input  B_3,
  input  B_4,
  input  B_5,
  input  B_6,
  input  B_7,
  input  B_8,
  input  B_9,
  input  B_10,
  input  B_11,
  input  B_12,
  input  B_13,
  input  B_14,
  input  B_15,
  output Or_0,
  output Or_1,
  output Or_2,
  output Or_3,
  output Or_4,
  output Or_5,
  output Or_6,
  output Or_7,
  output Or_8,
  output Or_9,
  output Or_10,
  output Or_11,
  output Or_12,
  output Or_13,
  output Or_14,
  output Or_15
);

  xor xor_1 (Or_0, A_0, B_0);
  xor xor_2 (Or_1, A_1, B_1);
  xor xor_3 (Or_2, A_2, B_2);
  xor xor_4 (Or_3, A_3, B_3);
  xor xor_5 (Or_4, A_4, B_4);
  xor xor_6 (Or_5, A_5, B_5);
  xor xor_7 (Or_6, A_6, B_6);
  xor xor_8 (Or_7, A_7, B_7);
  xor xor_9 (Or_8, A_8, B_8);
  xor xor_10 (Or_9, A_9, B_9);
  xor xor_11 (Or_10, A_10, B_10);
  xor xor_12 (Or_11, A_11, B_11);
  xor xor_13 (Or_12, A_12, B_12);
  xor xor_14 (Or_13, A_13, B_13);
  xor xor_15 (Or_14, A_14, B_14);
  xor xor_16 (Or_15, A_15, B_15);
endmodule
